// Logisim project cpu24.circ as structural Verilog: 25 circuits, main circuit ◇单周期MIPS
module \单周期MIPS  (
);

  wire AluSrcB, BEQ, BNE, branch_1_branch, CLK, Go, HLEN, J, Jal, jr, LUI, MEM_SIGN_EXT, MemToReg, MemWrite,
       MFLO, or_1_out, or_2_out, pcvalid, RegDst, RegWrite, RST, SHAMT_SRC, SignedExt, syscall, tunnel;
  wire [1:0] B_BRANCH, MODE;
  wire [3:0] AluOp;
  wire [4:0] multiplexer_1_out, multiplexer_2_out, multiplexer_3_out, multiplexer_4_out, multiplexer_5_out,
       multiplexer_8_out;
  wire [5:0] func, OP;
  wire [15:0] \总周期数 , \无条件分支数 , \条件分支成功数 ;
  wire [25:6] Imm26;
  wire [31:0] a0, bit_extender_1_out, bit_extender_2_out, HI, Imm__2, imm_ext, LedData, LO_Out, LO_R,
       multiplexer_7_out, multiplexer_9_out, multiplexer_10_out, multiplexer_11_out, multiplexer_12_out, PC,
       PC_4, PC_out, shifter_1_out, v0, \数据存储器_1_dataout ;

  Button \u_总复位  (.out(RST));
  Button \u_继续运行  (.out(Go));
  Clock clock_1 (.out(CLK));
  Register #(.width(32)) u_PC (.D(PC_out), .en(pcvalid), .Q(PC), .clk(CLK), .clr(RST));
  Hex_Digit_Display hex_digit_display_1 (.value(LedData[31:28]));  // open: dp
  Branch branch_1 (
    .rt(Imm26[20:16]), .Bne(BNE), .B(B_BRANCH), .R(LO_R[0]), .Beq(BEQ), .in_3(tunnel),
    .Branch(branch_1_branch));
  Adder #(.width(32)) adder_1 (.a(PC), .b(32'h4), .out(PC_4));  // open: cin, cout
  Counter #(.width(16), .max('hffff)) counter_1 (
    .count(pcvalid), .Q(\总周期数 ), .clk(CLK), .clr(RST));  // open: load, D, carry
  Hex_Digit_Display hex_digit_display_2 (.value(LedData[27:24]));  // open: dp
  Hex_Digit_Display hex_digit_display_3 (.value(LedData[23:20]));  // open: dp
  \PC转移逻辑  \pc转移逻辑_1  (
    .rs(a0), .PC(PC), .imm_ext(imm_ext), .imm26({Imm26, func}), .JR(jr), .J(J), .Branch(branch_1_branch),
    .PC_Out(PC_out));
  Counter #(.width(16), .max('hffff)) counter_2 (
    .count(branch_1_branch), .Q(\条件分支成功数 ), .clk(CLK), .clr(RST));  // open: load, D, carry
  Hex_Digit_Display hex_digit_display_4 (.value(LedData[15:12]));  // open: dp
  Hex_Digit_Display hex_digit_display_5 (.value(LedData[19:16]));  // open: dp
  ROM #(.addrWidth(10), .dataWidth(32)) rom_1 (.addr(PC[11:2]), .data({OP, Imm26, func}));  // open: sel
  Hex_Digit_Display hex_digit_display_6 (.value(LedData[7:4]));  // open: dp
  Hex_Digit_Display hex_digit_display_7 (.value(LedData[11:8]));  // open: dp
  Hex_Digit_Display hex_digit_display_8 (.value(LedData[3:0]));  // open: dp
  Multiplexer #(.width(5), .enable("false")) multiplexer_1 (
    .in0(Imm26[25:21]), .in1(5'b00100), .out(multiplexer_1_out), .sel(syscall));
  Multiplexer #(.width(5), .enable("false")) multiplexer_2 (
    .in0(Imm26[20:16]), .in1(Imm26[15:11]), .out(multiplexer_2_out), .sel(RegDst));
  Multiplexer #(.width(5), .enable("false")) multiplexer_3 (
    .in0(Imm26[20:16]), .in1(5'b00010), .out(multiplexer_3_out), .sel(syscall));
  Multiplexer #(.width(5), .enable("false")) multiplexer_4 (
    .in0(multiplexer_2_out), .in1({5{1'b1}}), .out(multiplexer_4_out), .sel(Jal));
  assign bit_extender_1_out = {{16{1'b0}}, {Imm26[15:6], func}};  // Bit_Extender bit_extender_1
  assign bit_extender_2_out = {{16{Imm26[15]}}, {Imm26[15:6], func}};  // Bit_Extender bit_extender_2
  // Probe on \总周期数 
  // Probe on \无条件分支数 
  // Probe on \条件分支成功数 
  \硬布线控制器  \u_硬布线控制器_1  (
    .Func(func), .OP(OP), .ALU_OP(AluOp), .MemToReg(MemToReg), .MemWrite(MemWrite), .ALU_SRC(AluSrcB),
    .RegWrite(RegWrite), .SysCALL(syscall), .SignedExt(SignedExt), .RegDst(RegDst), .JR(jr), .JMP(J),
    .Beq(BEQ), .JAL(Jal), .Bne(BNE), .SHAMT_SRC(SHAMT_SRC), .LUI(LUI), .HLEN(HLEN), .MFLO(MFLO),
    .MEM_SIGN_EXT(MEM_SIGN_EXT), .B_BRANCH(B_BRANCH), .MODE(MODE));
  or or_1 (or_1_out, B_BRANCH[1], B_BRANCH[0]);
  Multiplexer #(.width(5), .enable("false")) multiplexer_5 (
    .in0(multiplexer_3_out), .in1({5{1'b0}}), .out(multiplexer_5_out), .sel(or_1_out));
  Multiplexer #(.width(32), .enable("false")) multiplexer_6 (
    .in0(bit_extender_1_out), .in1(bit_extender_2_out), .out(imm_ext), .sel(SignedExt));
  Shifter #(.width(32)) shifter_1 (.in(bit_extender_1_out), .\dist (5'b10000), .out(shifter_1_out));
  MIPS_Regifile mips_regifile_1 (
    .Din(multiplexer_12_out), .Clk(CLK), .R1(a0), .R2(v0), .WE(RegWrite), .W_num(multiplexer_4_out),
    .R1_num(multiplexer_1_out), .R2_num(multiplexer_5_out));
  Counter #(.width(16), .max('hffff)) counter_3 (
    .count(or_2_out), .Q(\无条件分支数 ), .clk(CLK), .clr(RST));  // open: load, D, carry
  or or_2 (or_2_out, jr, J);
  Multiplexer #(.width(32), .enable("false")) multiplexer_7 (
    .in0(v0), .in1(imm_ext), .out(multiplexer_7_out), .sel(AluSrcB));
  Multiplexer #(.width(5), .enable("false")) multiplexer_8 (
    .in0(Imm26[10:6]), .in1(a0[4:0]), .out(multiplexer_8_out), .sel(SHAMT_SRC));
  Shifter #(.width(32)) shifter_2 (.in(imm_ext), .\dist (5'b00010), .out(Imm__2));
  MIPS_ALU mips_alu_1 (
    .X(a0), .Y(multiplexer_7_out), .AluOP(AluOp), .Equal(tunnel), .Result(LO_R), .Result_2(HI),
    .shamt(multiplexer_8_out));
  \数据存储器  \u_数据存储器_1  (
    .\字节地址 (LO_R[11:0]), .Din(v0), .DataOut(\数据存储器_1_dataout ), .CLK(CLK), .WE(MemWrite), .Mode(MODE),
    .clr(RST), .in_3(MEM_SIGN_EXT));
  Multiplexer #(.width(32), .enable("false")) multiplexer_9 (
    .in0(LO_R), .in1(\数据存储器_1_dataout ), .out(multiplexer_9_out), .sel(MemToReg));
  Multiplexer #(.width(32), .enable("false")) multiplexer_10 (
    .in0(multiplexer_9_out), .in1(PC_4), .out(multiplexer_10_out), .sel(Jal));
  Multiplexer #(.width(32), .enable("false")) multiplexer_11 (
    .in0(multiplexer_10_out), .in1(shifter_1_out), .out(multiplexer_11_out), .sel(LUI));
  Multiplexer #(.width(32), .enable("false")) multiplexer_12 (
    .in0(multiplexer_11_out), .in1(LO_Out), .out(multiplexer_12_out), .sel(MFLO));
  Syscall syscall_1 (
    .CLK(CLK), .RST(RST), .syscall(syscall), .go(Go), .a0(a0), .v0(v0), .LedData(LedData), .PcValid(pcvalid));
  Register #(.width(32)) register_1 (.D(LO_R), .en(HLEN), .Q(LO_Out), .clk(CLK), .clr(RST));
  Register #(.width(32)) register_2 (.D(HI), .en(HLEN), .clk(CLK), .clr(RST));  // open: Q
  // AND_Gate and_1 is placed but not wired

  // Other names for the same wires on the sheet: Imm26[5:0] = func; rt[4:0] = Imm26[20:16]; rs[31:0] = a0

  // Notes on the sheet:
  //   数码管输出应该用寄存器锁存，否则显示数据只能一闪而过
  //   可以通过项目增加Logisim库的方式将前几次实验完成的电路作为子电路引入到本电路中使用
  //   指令存储器
  //   指令字
  //   contents of rom_1 (hex, n*v repeats v):
  //   20110001 8000c05 20110001 20120002 20130003 8000c09 20110001 20120002 20130003 8000c0d 20110001
  //   20120002 20130003 8000c11 20110001 20120002 20130003 c000df0 20100001 20110001 118fc0 112020
  //   20020022 c 118882 12200001 8000c15 112020 20020022 c 20110001 118880 112020 20020022 c 12200001
  //   8000c1f 20110001 118fc0 112020 20020022 c 1188c3 112020 20020022 c 118903 112020 20020022 c 118903
  //   112020 20020022 c 118903 112020 20020022 c 118903 112020 20020022 c 118903 112020 20020022 c 118903
  //   112020 20020022 c 118903 112020 20020022 c 20100001 109fc0 139fc3 8021 2012000c 24160003 26100001
  //   3210000f 20080008 20090001 139900 2709825 132020 20020022 c 1094022 1500fff9 22100001 2018000f
  //   2188024 108700 20080008 20090001 139902 2709825 132021 20020022 c 1094022 1500fff9 108702 2c9b022
  //   12c00001 8000c50 4020 1084027 84400 3508ffff 82021 20020022 c 2010ffff 20110000 ae300000 22100001
  //   22310004 ae300000 22100001 22310004 ae300000 22100001 22310004 ae300000 22100001 22310004 ae300000
  //   22100001 22310004 ae300000 22100001 22310004 ae300000 22100001 22310004 ae300000 22100001 22310004
  //   ae300000 22100001 22310004 ae300000 22100001 22310004 ae300000 22100001 22310004 ae300000 22100001
  //   22310004 ae300000 22100001 22310004 ae300000 22100001 22310004 ae300000 22100001 22310004 ae300000
  //   22100001 22310004 22100001 8020 2011003c 8e130000 8e340000 274402a 11000002 ae330000 ae140000
  //   2231fffc 1611fff8 102020 20020022 c 22100004 2011003c 1611fff2 20020032 c 20080001 20090003 20110876
  //   118d00 112020 20020022 c 200b0008 1118806 1318806 112020 20020022 c 216bffff 1560fff9 20020032 c
  //   20080001 20090003 20110876 118d00 112020 20020022 c 200b0008 1118807 1318807 112020 20020022 c
  //   216bffff 1560fff9 20020032 c 20080001 20110010 112020 20020022 c 200b0020 2288823 112020 20020022 c
  //   216bffff 1560fffa 20020032 c 2008ffff 20117777 112020 20020022 c 200b0010 2288826 112020 20020022 c
  //   216bffff 1560fffa 20020032 c 2008ffff 20117777 112020 20020022 c 200b0010 3a31ffff 112020 20020022 c
  //   216bffff 1560fffa 20020032 c 200b0008 3c11fedc 3631ffff 112020 20020022 c 3c11ba98 112020 c 3c117654
  //   112020 c 3c113210 112020 c 216bffff 1560fff0 20020032 c 2008ffff 20090000 20111997 112020 20020022 c
  //   2288820 2e291949 1120fffa 20020032 c 20080002 20111111 112020 20020022 c 200b0020 2280019 8812
  //   112020 20020022 c 216bffff 1560fff9 20020032 c 20080002 20111111 118c00 112020 20020022 c 200b001c
  //   228001b 8812 112020 20020022 c 216bffff 1560fff9 20020032 c 20090000 200b0010 34118483 20120404
  //   118c00 129400 36318281 22520404 ad310000 2328820 21290004 216bffff 1560fffb 200b0020 20090000
  //   81310000 112020 20020022 c 21290001 216bffff 1560fff9 20020032 c 20090000 200b0010 34118483 20120404
  //   118c00 129400 36318281 22520404 ad310000 2328820 21290004 216bffff 1560fffb 200b0020 20090000
  //   91310000 112020 20020022 c 21290001 216bffff 1560fff9 20020032 c 20090000 200b0010 34118483 20120404
  //   118c00 129400 36318281 22520404 ad310000 2328820 21290004 216bffff 1560fffb 200b0020 20090000
  //   85310000 112020 20020022 c 21290002 216bffff 1560fff9 20020032 c 20090000 200b0010 34118483 20120404
  //   118c00 129400 36318281 22520404 ad310000 2328820 21290004 216bffff 1560fffb 200b0020 20090000
  //   95310000 112020 20020022 c 21290002 216bffff 1560fff9 20020032 c 20090000 200b0020 20110000 20120001
  //   a1310000 112020 20020022 c 2328820 21290001 216bffff 1560fff8 200b0008 20090000 8d310000 112020
  //   20020022 c 21290004 216bffff 1560fff9 20020032 c 20090000 200b0020 20110001 20120001 a5310000 112020
  //   20020022 c 2328820 21290002 216bffff 1560fff8 200b0010 20090000 8d310000 112020 20020022 c 21290004
  //   216bffff 1560fff9 20020032 c 2011fff1 112020 20020022 c 22310001 1a20fffb 20020032 c 2011000f 112020
  //   20020022 c 2231ffff 1e20fffb 20020032 c 2011fff1 112020 20020022 c 22310001 620fffb 20020032 c
  //   2011000f 112020 20020022 c 2231ffff 621fffb 20020032 c c 20100000 22100001 102020 20020022 c
  //   22100002 102020 20020022 c 22100003 102020 20020022 c 22100004 102020 20020022 c 22100005 102020
  //   20020022 c 22100006 102020 20020022 c 22100007 102020 20020022 c 22100008 102020 2002002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
  //   数码管输出
  //   OP
  //   Func
  //   rs
  //   rt
  //   rd
  //   imm
  //   总复位信号应将除ROM以外所有存储组件全部清零
  //   Beq
  //   JMP
  //   JR
  //   Bne
  //   OP
  //   JAL
  //   Func
  //   Syscall
  //   MemToReg
  //   MemWrite
  //   AluOP
  //   AluSrcB
  //   RegWrite
  //   RegDst
endmodule

// 单周期硬布线控制器
module \硬布线控制器  (
  input  [5:0] OP,
  input  [5:0] Func,
  output [3:0] ALU_OP,
  output MemToReg,
  output MemWrite,
  output ALU_SRC,
  output RegWrite,
  output SysCALL,
  output SignedExt,
  output RegDst,
  output Beq,
  output Bne,
  output JR,
  output JMP,
  output JAL,
  output SHAMT_SRC,
  output LUI,
  output HLEN,
  output MFLO,
  output [1:0] MODE,
  output MEM_SIGN_EXT,
  output [1:0] B_BRANCH
);

  \运算控制器  \u_运算控制器_1  (
    .OP0(OP[0]), .OP1(OP[1]), .OP2(OP[2]), .OP3(OP[3]), .OP4(OP[4]), .OP5(OP[5]), .F0(Func[0]), .F1(Func[1]),
    .F2(Func[2]), .F3(Func[3]), .F4(Func[4]), .F5(Func[5]), .S0(ALU_OP[0]), .S1(ALU_OP[1]), .S2(ALU_OP[2]),
    .S3(ALU_OP[3]));
  \控制信号生成  \u_控制信号生成_1  (
    .OP0(OP[0]), .OP1(OP[1]), .OP2(OP[2]), .OP3(OP[3]), .OP4(OP[4]), .OP5(OP[5]), .F0(Func[0]), .F1(Func[1]),
    .F2(Func[2]), .F3(Func[3]), .F4(Func[4]), .F5(Func[5]), .MemToReg(MemToReg), .MemWrite(MemWrite),
    .ALU_SRC(ALU_SRC), .RegWrite(RegWrite), .SysCALL(SysCALL), .SignedExt(SignedExt), .RegDst(RegDst),
    .BEQ(Beq), .BNE(Bne), .JR(JR), .JMP(JMP), .JAL(JAL));
  \控制信号扩展  \u_控制信号扩展_1  (
    .OP0(OP[0]), .OP1(OP[1]), .OP2(OP[2]), .OP3(OP[3]), .OP4(OP[4]), .OP5(OP[5]), .F0(Func[0]), .F1(Func[1]),
    .F2(Func[2]), .F3(Func[3]), .F4(Func[4]), .F5(Func[5]), .SHAMT_SRC(SHAMT_SRC), .LUI(LUI), .HLEN(HLEN),
    .MFLO(MFLO), .MODE1(MODE[1]), .MODE0(MODE[0]), .MEM_SIGN_EXT(MEM_SIGN_EXT), .B_BRANCH1(B_BRANCH[1]),
    .B_BRANCH0(B_BRANCH[0]));

  // Other names for the same wires on the sheet: OP_CODE[5:0] = OP

  // Notes on the sheet:
  //   运算器控制器，根据指令生成运算器功能选择信号
  //   控制信号生成，产生数据通路需要的其他控制信号
endmodule

// 运算器控制器
module \运算控制器  (
  input  OP0,
  input  OP1,
  input  OP2,
  input  OP3,
  input  OP4,
  input  OP5,
  input  F0,
  input  F1,
  input  F2,
  input  F3,
  input  F4,
  input  F5,
  output S0,
  output S1,
  output S2,
  output S3
);

  wire and_1_out, and_2_out, and_3_out, and_4_out, and_5_out, and_6_out, and_7_out, and_8_out, and_9_out,
       and_10_out, and_11_out, and_12_out, and_13_out, and_14_out, and_15_out, and_16_out, and_17_out,
       and_18_out, and_19_out, and_20_out, and_21_out, and_22_out, and_23_out, and_24_out, and_25_out,
       and_26_out, and_27_out, and_28_out, and_29_out, and_30_out, and_31_out, and_32_out, and_33_out,
       and_34_out, and_35_out, and_36_out, and_37_out, and_38_out, and_39_out, and_40_out, and_41_out,
       and_42_out, and_43_out, and_44_out, and_45_out, and_46_out, and_47_out, and_48_out, and_49_out,
       and_50_out, and_51_out, and_52_out, and_53_out, and_54_out, and_55_out, and_56_out, and_57_out,
       and_58_out, and_59_out, and_60_out, and_61_out, and_62_out, and_63_out, and_64_out, and_65_out,
       and_66_out, and_67_out, and_68_out, and_69_out, and_70_out, and_71_out, and_72_out, not_1_out,
       not_2_out, not_3_out, not_4_out, not_5_out, not_6_out, not_7_out, not_8_out, not_9_out, not_10_out,
       not_11_out, not_12_out, not_13_out, not_14_out, not_15_out, not_16_out, not_17_out, not_18_out,
       not_19_out, not_20_out, not_21_out, not_22_out, not_23_out, not_24_out, not_25_out, not_26_out,
       not_27_out, not_28_out, not_29_out, not_30_out, not_31_out, not_32_out, not_33_out, not_34_out,
       not_35_out, not_36_out, not_37_out, not_38_out, not_39_out, not_40_out, not_41_out, not_42_out,
       not_43_out, not_44_out, not_45_out, not_46_out, not_47_out, not_48_out, not_49_out, not_50_out,
       not_51_out, not_52_out, not_53_out, not_54_out, not_55_out, not_56_out, not_57_out, not_58_out,
       not_59_out, not_60_out, not_61_out, not_62_out, not_63_out, not_64_out, not_65_out, not_66_out,
       not_67_out, not_68_out, not_69_out, not_70_out, not_71_out, not_72_out, not_73_out, not_74_out,
       not_75_out, not_76_out, not_77_out, not_78_out, not_79_out, not_80_out, not_81_out, not_82_out,
       not_83_out, not_84_out, not_85_out, not_86_out, not_87_out, not_88_out, not_89_out, not_90_out,
       not_91_out, not_92_out, not_93_out, not_94_out, not_95_out, not_96_out, not_97_out, not_98_out,
       not_99_out, not_100_out, not_101_out, not_102_out, not_103_out, not_104_out, not_105_out, not_106_out,
       not_107_out, not_108_out, not_109_out, not_110_out, not_111_out, not_112_out, not_113_out,
       not_114_out, not_115_out, not_116_out, not_117_out, not_118_out, not_119_out, not_120_out,
       not_121_out, not_122_out, not_123_out, not_124_out, not_125_out, not_126_out, not_127_out,
       not_128_out, not_129_out, not_130_out, not_131_out, not_132_out, not_133_out, not_134_out,
       not_135_out, not_136_out, not_137_out, not_138_out, not_139_out, not_140_out, not_141_out,
       not_142_out, not_143_out, not_144_out, not_145_out, not_146_out, not_147_out, not_148_out,
       not_149_out, not_150_out, not_151_out, not_152_out, not_153_out, not_154_out, not_155_out,
       not_156_out, not_157_out, not_158_out, not_159_out, not_160_out, not_161_out, not_162_out,
       not_163_out, not_164_out, not_165_out, not_166_out, not_167_out, not_168_out, not_169_out,
       not_170_out, not_171_out, not_172_out, not_173_out, not_174_out, not_175_out, not_176_out,
       not_177_out, not_178_out, not_179_out, not_180_out, not_181_out, not_182_out, not_183_out,
       not_184_out, not_185_out, not_186_out, not_187_out, not_188_out, not_189_out, not_190_out,
       not_191_out, not_192_out, not_193_out, not_194_out, not_195_out, not_196_out, not_197_out,
       not_198_out, not_199_out, not_200_out, not_201_out, not_202_out, not_203_out, not_204_out,
       not_205_out, not_206_out, not_207_out, not_208_out, not_209_out, not_210_out, not_211_out,
       not_212_out, not_213_out, not_214_out, not_215_out, not_216_out, not_217_out, not_218_out,
       not_219_out, not_220_out, not_221_out, not_222_out, not_223_out, not_224_out, not_225_out,
       not_226_out, not_227_out, not_228_out, not_229_out, not_230_out, not_231_out, not_232_out,
       not_233_out, not_234_out, not_235_out, not_236_out, not_237_out, not_238_out, not_239_out,
       not_240_out, not_241_out, not_242_out, not_243_out, not_244_out, not_245_out, not_246_out,
       not_247_out, not_248_out, not_249_out, not_250_out, not_251_out, not_252_out, not_253_out,
       not_254_out, not_255_out, not_256_out, not_257_out, not_258_out, not_259_out, not_260_out,
       not_261_out, not_262_out, not_263_out, not_264_out, not_265_out, not_266_out, not_267_out,
       not_268_out, not_269_out, not_270_out, not_271_out, not_272_out, not_273_out, not_274_out,
       not_275_out, not_276_out, not_277_out, not_278_out, not_279_out, not_280_out, not_281_out,
       not_282_out, not_283_out, not_284_out, not_285_out, not_286_out, not_287_out, not_288_out,
       not_289_out, not_290_out, not_291_out, not_292_out, not_293_out, not_294_out, not_295_out,
       not_296_out, not_297_out, not_298_out, not_299_out, not_300_out, not_301_out, not_302_out,
       not_303_out, not_304_out, not_305_out, not_306_out, not_307_out, not_308_out, not_309_out,
       not_310_out, not_311_out, not_312_out, not_313_out, not_314_out, not_315_out, not_316_out,
       not_317_out, not_318_out, not_319_out, not_320_out, not_321_out, not_322_out, not_323_out,
       not_324_out, not_325_out, not_326_out, not_327_out, not_328_out, not_329_out, not_330_out,
       not_331_out, not_332_out, not_333_out, not_334_out, not_335_out, not_336_out, not_337_out,
       not_338_out, not_339_out, not_340_out, not_341_out, not_342_out, not_343_out, not_344_out,
       not_345_out, not_346_out, not_347_out, not_348_out, not_349_out, not_350_out, not_351_out,
       not_352_out, not_353_out, not_354_out, not_355_out, not_356_out, not_357_out, not_358_out,
       not_359_out, not_360_out, not_361_out, not_362_out, not_363_out, not_364_out, not_365_out,
       not_366_out, not_367_out, not_368_out, not_369_out, not_370_out, not_371_out, not_372_out,
       not_373_out, not_374_out, not_375_out, not_376_out, not_377_out, not_378_out, not_379_out,
       not_380_out, not_381_out, not_382_out, not_383_out, not_384_out, not_385_out, not_386_out,
       not_387_out, not_388_out, not_389_out, not_390_out, not_391_out, not_392_out, not_393_out,
       not_394_out, not_395_out, not_396_out, not_397_out, not_398_out, not_399_out, not_400_out,
       not_401_out, not_402_out, not_403_out, not_404_out, not_405_out, not_406_out, not_407_out,
       not_408_out, not_409_out, not_410_out, not_411_out, not_412_out, not_413_out, not_414_out,
       not_415_out, not_416_out, not_417_out, not_418_out, not_419_out, not_420_out, not_421_out,
       not_422_out, not_423_out, not_424_out, not_425_out, not_426_out, not_427_out, not_428_out, not_429_out;

  not not_1 (not_1_out, OP5);
  not not_2 (not_2_out, OP4);
  not not_3 (not_3_out, OP3);
  not not_4 (not_4_out, OP2);
  not not_5 (not_5_out, OP1);
  not not_6 (not_6_out, OP0);
  not not_7 (not_7_out, F5);
  not not_8 (not_8_out, F4);
  not not_9 (not_9_out, F3);
  not not_10 (not_10_out, F2);
  not not_11 (not_11_out, OP5);
  not not_12 (not_12_out, OP4);
  not not_13 (not_13_out, OP3);
  not not_14 (not_14_out, OP2);
  not not_15 (not_15_out, OP1);
  not not_16 (not_16_out, OP0);
  not not_17 (not_17_out, F4);
  not not_18 (not_18_out, F3);
  not not_19 (not_19_out, F2);
  not not_20 (not_20_out, F1);
  not not_21 (not_21_out, F0);
  not not_22 (not_22_out, OP5);
  not not_23 (not_23_out, OP4);
  not not_24 (not_24_out, OP3);
  not not_25 (not_25_out, OP2);
  not not_26 (not_26_out, OP1);
  not not_27 (not_27_out, OP0);
  not not_28 (not_28_out, F4);
  not not_29 (not_29_out, F3);
  not not_30 (not_30_out, F2);
  not not_31 (not_31_out, F1);
  not not_32 (not_32_out, OP5);
  not not_33 (not_33_out, OP4);
  not not_34 (not_34_out, OP3);
  not not_35 (not_35_out, OP2);
  not not_36 (not_36_out, OP1);
  not not_37 (not_37_out, OP0);
  not not_38 (not_38_out, F4);
  not not_39 (not_39_out, F3);
  not not_40 (not_40_out, F1);
  not not_41 (not_41_out, F0);
  not not_42 (not_42_out, OP5);
  not not_43 (not_43_out, OP4);
  not not_44 (not_44_out, OP3);
  not not_45 (not_45_out, OP2);
  not not_46 (not_46_out, OP1);
  not not_47 (not_47_out, OP0);
  not not_48 (not_48_out, F4);
  not not_49 (not_49_out, F2);
  not not_50 (not_50_out, F0);
  not not_51 (not_51_out, OP5);
  not not_52 (not_52_out, OP4);
  not not_53 (not_53_out, OP2);
  not not_54 (not_54_out, OP1);
  not not_55 (not_55_out, OP0);
  not not_56 (not_56_out, OP5);
  not not_57 (not_57_out, OP4);
  not not_58 (not_58_out, OP1);
  not not_59 (not_59_out, OP0);
  not not_60 (not_60_out, OP5);
  not not_61 (not_61_out, OP4);
  not not_62 (not_62_out, OP2);
  not not_63 (not_63_out, OP1);
  not not_64 (not_64_out, OP5);
  not not_65 (not_65_out, OP4);
  not not_66 (not_66_out, OP2);
  not not_67 (not_67_out, OP0);
  not not_68 (not_68_out, OP4);
  not not_69 (not_69_out, OP3);
  not not_70 (not_70_out, OP2);
  not not_71 (not_71_out, OP4);
  not not_72 (not_72_out, OP2);
  not not_73 (not_73_out, OP5);
  not not_74 (not_74_out, OP4);
  not not_75 (not_75_out, OP3);
  not not_76 (not_76_out, OP2);
  not not_77 (not_77_out, OP1);
  not not_78 (not_78_out, OP0);
  not not_79 (not_79_out, F5);
  not not_80 (not_80_out, F4);
  not not_81 (not_81_out, F3);
  not not_82 (not_82_out, OP5);
  not not_83 (not_83_out, OP4);
  not not_84 (not_84_out, OP3);
  not not_85 (not_85_out, OP2);
  not not_86 (not_86_out, OP1);
  not not_87 (not_87_out, OP0);
  not not_88 (not_88_out, F4);
  not not_89 (not_89_out, F3);
  not not_90 (not_90_out, F0);
  not not_91 (not_91_out, OP5);
  not not_92 (not_92_out, OP4);
  not not_93 (not_93_out, OP0);
  not not_94 (not_94_out, OP5);
  not not_95 (not_95_out, OP4);
  not not_96 (not_96_out, OP2);
  not not_97 (not_97_out, OP5);
  not not_98 (not_98_out, OP4);
  not not_99 (not_99_out, OP3);
  not not_100 (not_100_out, OP2);
  not not_101 (not_101_out, OP1);
  not not_102 (not_102_out, OP0);
  not not_103 (not_103_out, F5);
  not not_104 (not_104_out, F2);
  not not_105 (not_105_out, F1);
  not not_106 (not_106_out, OP4);
  not not_107 (not_107_out, OP3);
  not not_108 (not_108_out, OP2);
  not not_109 (not_109_out, OP1);
  not not_110 (not_110_out, OP0);
  not not_111 (not_111_out, OP4);
  not not_112 (not_112_out, OP3);
  not not_113 (not_113_out, OP1);
  not not_114 (not_114_out, OP0);
  not not_115 (not_115_out, OP4);
  not not_116 (not_116_out, OP3);
  not not_117 (not_117_out, OP2);
  not not_118 (not_118_out, OP1);
  not not_119 (not_119_out, OP4);
  not not_120 (not_120_out, OP3);
  not not_121 (not_121_out, OP1);
  not not_122 (not_122_out, OP4);
  not not_123 (not_123_out, OP2);
  not not_124 (not_124_out, OP1);
  not not_125 (not_125_out, OP0);
  not not_126 (not_126_out, OP4);
  not not_127 (not_127_out, OP2);
  not not_128 (not_128_out, OP1);
  not not_129 (not_129_out, OP5);
  not not_130 (not_130_out, OP4);
  not not_131 (not_131_out, OP3);
  not not_132 (not_132_out, OP0);
  not not_133 (not_133_out, OP5);
  not not_134 (not_134_out, OP4);
  not not_135 (not_135_out, OP3);
  not not_136 (not_136_out, OP5);
  not not_137 (not_137_out, OP4);
  not not_138 (not_138_out, OP3);
  not not_139 (not_139_out, OP2);
  not not_140 (not_140_out, OP1);
  not not_141 (not_141_out, OP5);
  not not_142 (not_142_out, OP4);
  not not_143 (not_143_out, OP3);
  not not_144 (not_144_out, OP2);
  not not_145 (not_145_out, OP1);
  not not_146 (not_146_out, OP5);
  not not_147 (not_147_out, OP4);
  not not_148 (not_148_out, OP3);
  not not_149 (not_149_out, OP2);
  not not_150 (not_150_out, OP1);
  not not_151 (not_151_out, OP0);
  not not_152 (not_152_out, F5);
  not not_153 (not_153_out, F4);
  not not_154 (not_154_out, F3);
  not not_155 (not_155_out, F2);
  not not_156 (not_156_out, F0);
  not not_157 (not_157_out, OP5);
  not not_158 (not_158_out, OP4);
  not not_159 (not_159_out, OP3);
  not not_160 (not_160_out, OP2);
  not not_161 (not_161_out, OP1);
  not not_162 (not_162_out, OP0);
  not not_163 (not_163_out, F4);
  not not_164 (not_164_out, F3);
  not not_165 (not_165_out, F2);
  not not_166 (not_166_out, F0);
  not not_167 (not_167_out, OP5);
  not not_168 (not_168_out, OP4);
  not not_169 (not_169_out, OP3);
  not not_170 (not_170_out, OP2);
  not not_171 (not_171_out, OP1);
  not not_172 (not_172_out, OP0);
  not not_173 (not_173_out, F4);
  not not_174 (not_174_out, F3);
  not not_175 (not_175_out, F1);
  not not_176 (not_176_out, F0);
  not not_177 (not_177_out, OP5);
  not not_178 (not_178_out, OP4);
  not not_179 (not_179_out, OP3);
  not not_180 (not_180_out, OP2);
  not not_181 (not_181_out, OP1);
  not not_182 (not_182_out, OP0);
  not not_183 (not_183_out, F4);
  not not_184 (not_184_out, F3);
  not not_185 (not_185_out, OP5);
  not not_186 (not_186_out, OP4);
  not not_187 (not_187_out, OP3);
  not not_188 (not_188_out, OP2);
  not not_189 (not_189_out, OP1);
  not not_190 (not_190_out, OP0);
  not not_191 (not_191_out, F4);
  not not_192 (not_192_out, F2);
  not not_193 (not_193_out, F0);
  not not_194 (not_194_out, OP5);
  not not_195 (not_195_out, OP4);
  not not_196 (not_196_out, OP1);
  not not_197 (not_197_out, OP0);
  not not_198 (not_198_out, OP5);
  not not_199 (not_199_out, OP4);
  not not_200 (not_200_out, OP2);
  not not_201 (not_201_out, OP0);
  not not_202 (not_202_out, OP5);
  not not_203 (not_203_out, OP4);
  not not_204 (not_204_out, OP3);
  not not_205 (not_205_out, OP2);
  not not_206 (not_206_out, OP1);
  not not_207 (not_207_out, OP0);
  not not_208 (not_208_out, F5);
  not not_209 (not_209_out, F4);
  not not_210 (not_210_out, F3);
  not not_211 (not_211_out, F0);
  not not_212 (not_212_out, OP5);
  not not_213 (not_213_out, OP4);
  not not_214 (not_214_out, OP3);
  not not_215 (not_215_out, OP2);
  not not_216 (not_216_out, OP1);
  not not_217 (not_217_out, OP0);
  not not_218 (not_218_out, F4);
  not not_219 (not_219_out, F3);
  not not_220 (not_220_out, F2);
  not not_221 (not_221_out, OP5);
  not not_222 (not_222_out, OP4);
  not not_223 (not_223_out, OP2);
  not not_224 (not_224_out, OP5);
  not not_225 (not_225_out, OP4);
  not not_226 (not_226_out, OP3);
  not not_227 (not_227_out, OP2);
  not not_228 (not_228_out, OP1);
  not not_229 (not_229_out, OP0);
  not not_230 (not_230_out, F5);
  not not_231 (not_231_out, F2);
  not not_232 (not_232_out, F1);
  not not_233 (not_233_out, OP5);
  not not_234 (not_234_out, OP4);
  not not_235 (not_235_out, OP3);
  not not_236 (not_236_out, OP0);
  not not_237 (not_237_out, OP5);
  not not_238 (not_238_out, OP4);
  not not_239 (not_239_out, OP3);
  not not_240 (not_240_out, OP5);
  not not_241 (not_241_out, OP4);
  not not_242 (not_242_out, OP3);
  not not_243 (not_243_out, OP2);
  not not_244 (not_244_out, OP1);
  not not_245 (not_245_out, OP5);
  not not_246 (not_246_out, OP4);
  not not_247 (not_247_out, OP3);
  not not_248 (not_248_out, OP2);
  not not_249 (not_249_out, OP1);
  not not_250 (not_250_out, OP5);
  not not_251 (not_251_out, OP4);
  not not_252 (not_252_out, OP3);
  not not_253 (not_253_out, OP2);
  not not_254 (not_254_out, OP1);
  not not_255 (not_255_out, OP0);
  not not_256 (not_256_out, F4);
  not not_257 (not_257_out, F3);
  not not_258 (not_258_out, F2);
  not not_259 (not_259_out, F1);
  not not_260 (not_260_out, F0);
  not not_261 (not_261_out, OP5);
  not not_262 (not_262_out, OP4);
  not not_263 (not_263_out, OP3);
  not not_264 (not_264_out, OP2);
  not not_265 (not_265_out, OP1);
  not not_266 (not_266_out, OP0);
  not not_267 (not_267_out, F4);
  not not_268 (not_268_out, F3);
  not not_269 (not_269_out, F2);
  not not_270 (not_270_out, F1);
  not not_271 (not_271_out, OP5);
  not not_272 (not_272_out, OP4);
  not not_273 (not_273_out, OP3);
  not not_274 (not_274_out, OP2);
  not not_275 (not_275_out, OP1);
  not not_276 (not_276_out, OP0);
  not not_277 (not_277_out, F4);
  not not_278 (not_278_out, F3);
  not not_279 (not_279_out, F2);
  not not_280 (not_280_out, F0);
  not not_281 (not_281_out, OP5);
  not not_282 (not_282_out, OP4);
  not not_283 (not_283_out, OP3);
  not not_284 (not_284_out, OP2);
  not not_285 (not_285_out, OP1);
  not not_286 (not_286_out, OP0);
  not not_287 (not_287_out, F4);
  not not_288 (not_288_out, F3);
  not not_289 (not_289_out, F1);
  not not_290 (not_290_out, F0);
  not not_291 (not_291_out, OP5);
  not not_292 (not_292_out, OP4);
  not not_293 (not_293_out, OP3);
  not not_294 (not_294_out, OP2);
  not not_295 (not_295_out, OP1);
  not not_296 (not_296_out, OP0);
  not not_297 (not_297_out, F4);
  not not_298 (not_298_out, F2);
  not not_299 (not_299_out, OP5);
  not not_300 (not_300_out, OP4);
  not not_301 (not_301_out, OP2);
  not not_302 (not_302_out, OP1);
  not not_303 (not_303_out, OP0);
  not not_304 (not_304_out, OP5);
  not not_305 (not_305_out, OP4);
  not not_306 (not_306_out, OP1);
  not not_307 (not_307_out, OP0);
  not not_308 (not_308_out, OP5);
  not not_309 (not_309_out, OP4);
  not not_310 (not_310_out, OP2);
  not not_311 (not_311_out, OP1);
  not not_312 (not_312_out, OP4);
  not not_313 (not_313_out, OP3);
  not not_314 (not_314_out, OP2);
  not not_315 (not_315_out, OP4);
  not not_316 (not_316_out, OP2);
  not not_317 (not_317_out, OP5);
  not not_318 (not_318_out, OP4);
  not not_319 (not_319_out, OP3);
  not not_320 (not_320_out, OP2);
  not not_321 (not_321_out, OP1);
  not not_322 (not_322_out, OP0);
  not not_323 (not_323_out, F4);
  not not_324 (not_324_out, F3);
  not not_325 (not_325_out, F2);
  not not_326 (not_326_out, OP5);
  not not_327 (not_327_out, OP4);
  not not_328 (not_328_out, OP3);
  not not_329 (not_329_out, OP2);
  not not_330 (not_330_out, OP1);
  not not_331 (not_331_out, OP0);
  not not_332 (not_332_out, F5);
  not not_333 (not_333_out, F2);
  not not_334 (not_334_out, OP4);
  not not_335 (not_335_out, OP3);
  not not_336 (not_336_out, OP2);
  not not_337 (not_337_out, OP1);
  not not_338 (not_338_out, OP0);
  not not_339 (not_339_out, OP4);
  not not_340 (not_340_out, OP3);
  not not_341 (not_341_out, OP1);
  not not_342 (not_342_out, OP0);
  not not_343 (not_343_out, OP4);
  not not_344 (not_344_out, OP3);
  not not_345 (not_345_out, OP2);
  not not_346 (not_346_out, OP1);
  not not_347 (not_347_out, OP4);
  not not_348 (not_348_out, OP3);
  not not_349 (not_349_out, OP1);
  not not_350 (not_350_out, OP4);
  not not_351 (not_351_out, OP2);
  not not_352 (not_352_out, OP1);
  not not_353 (not_353_out, OP0);
  not not_354 (not_354_out, OP4);
  not not_355 (not_355_out, OP2);
  not not_356 (not_356_out, OP1);
  not not_357 (not_357_out, OP5);
  not not_358 (not_358_out, OP4);
  not not_359 (not_359_out, OP3);
  not not_360 (not_360_out, OP2);
  not not_361 (not_361_out, OP1);
  not not_362 (not_362_out, OP0);
  not not_363 (not_363_out, F4);
  not not_364 (not_364_out, F3);
  not not_365 (not_365_out, F1);
  not not_366 (not_366_out, OP5);
  not not_367 (not_367_out, OP4);
  not not_368 (not_368_out, OP3);
  not not_369 (not_369_out, OP2);
  not not_370 (not_370_out, OP1);
  not not_371 (not_371_out, OP0);
  not not_372 (not_372_out, F4);
  not not_373 (not_373_out, F3);
  not not_374 (not_374_out, OP5);
  not not_375 (not_375_out, OP4);
  not not_376 (not_376_out, OP3);
  not not_377 (not_377_out, OP2);
  not not_378 (not_378_out, OP1);
  not not_379 (not_379_out, OP0);
  not not_380 (not_380_out, F4);
  not not_381 (not_381_out, F2);
  not not_382 (not_382_out, F0);
  not not_383 (not_383_out, OP5);
  not not_384 (not_384_out, OP4);
  not not_385 (not_385_out, OP3);
  not not_386 (not_386_out, OP2);
  not not_387 (not_387_out, OP1);
  not not_388 (not_388_out, OP0);
  not not_389 (not_389_out, F4);
  not not_390 (not_390_out, F2);
  not not_391 (not_391_out, OP5);
  not not_392 (not_392_out, OP4);
  not not_393 (not_393_out, OP2);
  not not_394 (not_394_out, OP0);
  not not_395 (not_395_out, OP5);
  not not_396 (not_396_out, OP4);
  not not_397 (not_397_out, OP1);
  not not_398 (not_398_out, OP5);
  not not_399 (not_399_out, OP4);
  not not_400 (not_400_out, OP3);
  not not_401 (not_401_out, OP2);
  not not_402 (not_402_out, OP1);
  not not_403 (not_403_out, OP0);
  not not_404 (not_404_out, F4);
  not not_405 (not_405_out, F3);
  not not_406 (not_406_out, F0);
  not not_407 (not_407_out, OP5);
  not not_408 (not_408_out, OP4);
  not not_409 (not_409_out, OP0);
  not not_410 (not_410_out, OP5);
  not not_411 (not_411_out, OP4);
  not not_412 (not_412_out, OP2);
  not not_413 (not_413_out, OP5);
  not not_414 (not_414_out, OP4);
  not not_415 (not_415_out, OP3);
  not not_416 (not_416_out, OP0);
  not not_417 (not_417_out, OP5);
  not not_418 (not_418_out, OP4);
  not not_419 (not_419_out, OP3);
  not not_420 (not_420_out, OP5);
  not not_421 (not_421_out, OP4);
  not not_422 (not_422_out, OP3);
  not not_423 (not_423_out, OP2);
  not not_424 (not_424_out, OP1);
  not not_425 (not_425_out, OP5);
  not not_426 (not_426_out, OP4);
  not not_427 (not_427_out, OP3);
  not not_428 (not_428_out, OP2);
  not not_429 (not_429_out, OP1);
  and and_1 (and_1_out, not_1_out, not_2_out, not_3_out, not_4_out, not_5_out, not_6_out, not_7_out, not_8_out, not_9_out, not_10_out, F1, F0);
  and and_2 (and_2_out, not_11_out, not_12_out, not_13_out, not_14_out, not_15_out, not_16_out, F5, not_17_out, not_18_out, not_19_out, not_20_out, not_21_out);
  and and_3 (and_3_out, not_22_out, not_23_out, not_24_out, not_25_out, not_26_out, not_27_out, F5, not_28_out, not_29_out, not_30_out, not_31_out, F0);
  and and_4 (and_4_out, not_32_out, not_33_out, not_34_out, not_35_out, not_36_out, not_37_out, F5, not_38_out, not_39_out, F2, not_40_out, not_41_out);
  and and_5 (and_5_out, not_42_out, not_43_out, not_44_out, not_45_out, not_46_out, not_47_out, F5, not_48_out, F3, not_49_out, F1, not_50_out);
  and and_6 (and_6_out, not_51_out, not_52_out, OP3, not_53_out, not_54_out, not_55_out);
  and and_7 (and_7_out, not_56_out, not_57_out, OP3, OP2, not_58_out, not_59_out);
  and and_8 (and_8_out, not_60_out, not_61_out, OP3, not_62_out, not_63_out, OP0);
  and and_9 (and_9_out, not_64_out, not_65_out, OP3, not_66_out, OP1, not_67_out);
  and and_10 (and_10_out, OP5, not_68_out, not_69_out, not_70_out, OP1, OP0);
  and and_11 (and_11_out, OP5, not_71_out, OP3, not_72_out, OP1, OP0);
  and and_12 (and_12_out, not_73_out, not_74_out, not_75_out, not_76_out, not_77_out, not_78_out, not_79_out, not_80_out, not_81_out, F2, F1, F0);
  and and_13 (and_13_out, not_82_out, not_83_out, not_84_out, not_85_out, not_86_out, not_87_out, F5, not_88_out, not_89_out, F2, F1, not_90_out);
  and and_14 (and_14_out, not_91_out, not_92_out, OP3, OP2, OP1, not_93_out);
  and and_15 (and_15_out, not_94_out, not_95_out, OP3, not_96_out, OP1, OP0);
  and and_16 (and_16_out, not_97_out, not_98_out, not_99_out, not_100_out, not_101_out, not_102_out, not_103_out, F4, F3, not_104_out, not_105_out, F0);
  and and_17 (and_17_out, OP5, not_106_out, not_107_out, not_108_out, not_109_out, not_110_out);
  and and_18 (and_18_out, OP5, not_111_out, not_112_out, OP2, not_113_out, not_114_out);
  and and_19 (and_19_out, OP5, not_115_out, not_116_out, not_117_out, not_118_out, OP0);
  and and_20 (and_20_out, OP5, not_119_out, not_120_out, OP2, not_121_out, OP0);
  and and_21 (and_21_out, OP5, not_122_out, OP3, not_123_out, not_124_out, not_125_out);
  and and_22 (and_22_out, OP5, not_126_out, OP3, not_127_out, not_128_out, OP0);
  and and_23 (and_23_out, not_129_out, not_130_out, not_131_out, OP2, OP1, not_132_out);
  and and_24 (and_24_out, not_133_out, not_134_out, not_135_out, OP2, OP1, OP0);
  and and_25 (and_25_out, not_136_out, not_137_out, not_138_out, not_139_out, not_140_out, OP0);
  and and_26 (and_26_out, not_141_out, not_142_out, not_143_out, not_144_out, not_145_out, OP0);
  and and_27 (and_27_out, not_146_out, not_147_out, not_148_out, not_149_out, not_150_out, not_151_out, not_152_out, not_153_out, not_154_out, not_155_out, F1, not_156_out);
  and and_28 (and_28_out, not_157_out, not_158_out, not_159_out, not_160_out, not_161_out, not_162_out, F5, not_163_out, not_164_out, not_165_out, F1, not_166_out);
  and and_29 (and_29_out, not_167_out, not_168_out, not_169_out, not_170_out, not_171_out, not_172_out, F5, not_173_out, not_174_out, F2, not_175_out, not_176_out);
  and and_30 (and_30_out, not_177_out, not_178_out, not_179_out, not_180_out, not_181_out, not_182_out, F5, not_183_out, not_184_out, F2, F1, F0);
  and and_31 (and_31_out, not_185_out, not_186_out, not_187_out, not_188_out, not_189_out, not_190_out, F5, not_191_out, F3, not_192_out, F1, not_193_out);
  and and_32 (and_32_out, not_194_out, not_195_out, OP3, OP2, not_196_out, not_197_out);
  and and_33 (and_33_out, not_198_out, not_199_out, OP3, not_200_out, OP1, not_201_out);
  and and_34 (and_34_out, not_202_out, not_203_out, not_204_out, not_205_out, not_206_out, not_207_out, not_208_out, not_209_out, not_210_out, F2, F1, not_211_out);
  and and_35 (and_35_out, not_212_out, not_213_out, not_214_out, not_215_out, not_216_out, not_217_out, F5, not_218_out, not_219_out, not_220_out, F1, F0);
  and and_36 (and_36_out, not_221_out, not_222_out, OP3, not_223_out, OP1, OP0);
  and and_37 (and_37_out, not_224_out, not_225_out, not_226_out, not_227_out, not_228_out, not_229_out, not_230_out, F4, F3, not_231_out, not_232_out, F0);
  and and_38 (and_38_out, not_233_out, not_234_out, not_235_out, OP2, OP1, not_236_out);
  and and_39 (and_39_out, not_237_out, not_238_out, not_239_out, OP2, OP1, OP0);
  and and_40 (and_40_out, not_240_out, not_241_out, not_242_out, not_243_out, not_244_out, OP0);
  and and_41 (and_41_out, not_245_out, not_246_out, not_247_out, not_248_out, not_249_out, OP0);
  and and_42 (and_42_out, not_250_out, not_251_out, not_252_out, not_253_out, not_254_out, not_255_out, F5, not_256_out, not_257_out, not_258_out, not_259_out, not_260_out);
  and and_43 (and_43_out, not_261_out, not_262_out, not_263_out, not_264_out, not_265_out, not_266_out, F5, not_267_out, not_268_out, not_269_out, not_270_out, F0);
  and and_44 (and_44_out, not_271_out, not_272_out, not_273_out, not_274_out, not_275_out, not_276_out, F5, not_277_out, not_278_out, not_279_out, F1, not_280_out);
  and and_45 (and_45_out, not_281_out, not_282_out, not_283_out, not_284_out, not_285_out, not_286_out, F5, not_287_out, not_288_out, F2, not_289_out, not_290_out);
  and and_46 (and_46_out, not_291_out, not_292_out, not_293_out, not_294_out, not_295_out, not_296_out, F5, not_297_out, F3, not_298_out, F1, F0);
  and and_47 (and_47_out, not_299_out, not_300_out, OP3, not_301_out, not_302_out, not_303_out);
  and and_48 (and_48_out, not_304_out, not_305_out, OP3, OP2, not_306_out, not_307_out);
  and and_49 (and_49_out, not_308_out, not_309_out, OP3, not_310_out, not_311_out, OP0);
  and and_50 (and_50_out, OP5, not_312_out, not_313_out, not_314_out, OP1, OP0);
  and and_51 (and_51_out, OP5, not_315_out, OP3, not_316_out, OP1, OP0);
  and and_52 (and_52_out, not_317_out, not_318_out, not_319_out, not_320_out, not_321_out, not_322_out, F5, not_323_out, not_324_out, not_325_out, F1, F0);
  and and_53 (and_53_out, not_326_out, not_327_out, not_328_out, not_329_out, not_330_out, not_331_out, not_332_out, F4, F3, not_333_out, F1, F0);
  and and_54 (and_54_out, OP5, not_334_out, not_335_out, not_336_out, not_337_out, not_338_out);
  and and_55 (and_55_out, OP5, not_339_out, not_340_out, OP2, not_341_out, not_342_out);
  and and_56 (and_56_out, OP5, not_343_out, not_344_out, not_345_out, not_346_out, OP0);
  and and_57 (and_57_out, OP5, not_347_out, not_348_out, OP2, not_349_out, OP0);
  and and_58 (and_58_out, OP5, not_350_out, OP3, not_351_out, not_352_out, not_353_out);
  and and_59 (and_59_out, OP5, not_354_out, OP3, not_355_out, not_356_out, OP0);
  and and_60 (and_60_out, not_357_out, not_358_out, not_359_out, not_360_out, not_361_out, not_362_out, F5, not_363_out, not_364_out, F2, not_365_out, F0);
  and and_61 (and_61_out, not_366_out, not_367_out, not_368_out, not_369_out, not_370_out, not_371_out, F5, not_372_out, not_373_out, F2, F1, F0);
  and and_62 (and_62_out, not_374_out, not_375_out, not_376_out, not_377_out, not_378_out, not_379_out, F5, not_380_out, F3, not_381_out, F1, not_382_out);
  and and_63 (and_63_out, not_383_out, not_384_out, not_385_out, not_386_out, not_387_out, not_388_out, F5, not_389_out, F3, not_390_out, F1, F0);
  and and_64 (and_64_out, not_391_out, not_392_out, OP3, not_393_out, OP1, not_394_out);
  and and_65 (and_65_out, not_395_out, not_396_out, OP3, OP2, not_397_out, OP0);
  and and_66 (and_66_out, not_398_out, not_399_out, not_400_out, not_401_out, not_402_out, not_403_out, F5, not_404_out, not_405_out, F2, F1, not_406_out);
  and and_67 (and_67_out, not_407_out, not_408_out, OP3, OP2, OP1, not_409_out);
  and and_68 (and_68_out, not_410_out, not_411_out, OP3, not_412_out, OP1, OP0);
  and and_69 (and_69_out, not_413_out, not_414_out, not_415_out, OP2, OP1, not_416_out);
  and and_70 (and_70_out, not_417_out, not_418_out, not_419_out, OP2, OP1, OP0);
  and and_71 (and_71_out, not_420_out, not_421_out, not_422_out, not_423_out, not_424_out, OP0);
  and and_72 (and_72_out, not_425_out, not_426_out, not_427_out, not_428_out, not_429_out, OP0);
  or or_1 (S0, and_1_out, and_2_out, and_3_out, and_4_out, and_5_out, and_6_out, and_7_out, and_8_out, and_9_out, and_10_out, and_11_out, and_12_out, and_13_out, and_14_out, and_15_out, and_16_out, and_17_out, and_18_out, and_19_out, and_20_out, and_21_out, and_22_out, and_23_out, and_24_out, and_25_out, and_26_out);
  or or_2 (S1, and_27_out, and_28_out, and_29_out, and_30_out, and_31_out, and_32_out, and_33_out, and_34_out, and_35_out, and_36_out, and_37_out, and_38_out, and_39_out, and_40_out, and_41_out);
  or or_3 (S2, and_42_out, and_43_out, and_44_out, and_45_out, and_46_out, and_47_out, and_48_out, and_49_out, and_50_out, and_51_out, and_52_out, and_53_out, and_54_out, and_55_out, and_56_out, and_57_out, and_58_out, and_59_out);
  or or_4 (S3, and_60_out, and_61_out, and_62_out, and_63_out, and_64_out, and_65_out, and_66_out, and_67_out, and_68_out, and_69_out, and_70_out, and_71_out, and_72_out);
endmodule

// 控制信号生成
module \控制信号生成  (
  input  OP0,
  input  OP1,
  input  OP2,
  input  OP3,
  input  OP4,
  input  OP5,
  input  F0,
  input  F1,
  input  F2,
  input  F3,
  input  F4,
  input  F5,
  output MemToReg,
  output MemWrite,
  output ALU_SRC,
  output RegWrite,
  output SysCALL,
  output SignedExt,
  output RegDst,
  output BEQ,
  output BNE,
  output JR,
  output JMP,
  output JAL
);

  wire and_1_out, and_2_out, and_3_out, and_4_out, and_5_out, and_6_out, and_7_out, and_8_out, and_9_out,
       and_10_out, and_11_out, and_12_out, and_13_out, and_14_out, and_15_out, and_16_out, and_17_out,
       and_18_out, and_19_out, and_20_out, and_21_out, and_22_out, and_23_out, and_24_out, and_25_out,
       and_26_out, and_27_out, and_28_out, and_29_out, and_30_out, and_31_out, and_32_out, and_33_out,
       and_34_out, and_35_out, and_36_out, and_37_out, and_38_out, and_39_out, and_40_out, and_41_out,
       and_42_out, and_43_out, and_44_out, and_45_out, and_46_out, and_47_out, and_48_out, and_49_out,
       and_50_out, and_51_out, and_52_out, and_53_out, and_54_out, and_56_out, and_57_out, and_58_out,
       and_59_out, and_60_out, and_61_out, and_62_out, and_63_out, and_64_out, and_65_out, and_66_out,
       and_67_out, and_68_out, and_69_out, and_70_out, and_71_out, and_72_out, and_73_out, and_74_out,
       and_75_out, and_76_out, and_77_out, and_78_out, and_79_out, and_80_out, and_81_out, and_82_out,
       and_83_out, and_84_out, and_85_out, and_86_out, and_87_out, and_88_out, and_89_out, and_90_out,
       and_94_out, and_95_out, and_96_out, not_1_out, not_2_out, not_3_out, not_4_out, not_5_out, not_6_out,
       not_7_out, not_8_out, not_9_out, not_10_out, not_11_out, not_12_out, not_13_out, not_14_out,
       not_15_out, not_16_out, not_17_out, not_18_out, not_19_out, not_20_out, not_21_out, not_22_out,
       not_23_out, not_24_out, not_25_out, not_26_out, not_27_out, not_28_out, not_29_out, not_30_out,
       not_31_out, not_32_out, not_33_out, not_34_out, not_35_out, not_36_out, not_37_out, not_38_out,
       not_39_out, not_40_out, not_41_out, not_42_out, not_43_out, not_44_out, not_45_out, not_46_out,
       not_47_out, not_48_out, not_49_out, not_50_out, not_51_out, not_52_out, not_53_out, not_54_out,
       not_55_out, not_56_out, not_57_out, not_58_out, not_59_out, not_60_out, not_61_out, not_62_out,
       not_63_out, not_64_out, not_65_out, not_66_out, not_67_out, not_68_out, not_69_out, not_70_out,
       not_71_out, not_72_out, not_73_out, not_74_out, not_75_out, not_76_out, not_77_out, not_78_out,
       not_79_out, not_80_out, not_81_out, not_82_out, not_83_out, not_84_out, not_85_out, not_86_out,
       not_87_out, not_88_out, not_89_out, not_90_out, not_91_out, not_92_out, not_93_out, not_94_out,
       not_95_out, not_96_out, not_97_out, not_98_out, not_99_out, not_100_out, not_101_out, not_102_out,
       not_103_out, not_104_out, not_105_out, not_106_out, not_107_out, not_108_out, not_109_out,
       not_110_out, not_111_out, not_112_out, not_113_out, not_114_out, not_115_out, not_116_out,
       not_117_out, not_118_out, not_119_out, not_120_out, not_121_out, not_122_out, not_123_out,
       not_124_out, not_125_out, not_126_out, not_127_out, not_128_out, not_129_out, not_130_out,
       not_131_out, not_132_out, not_133_out, not_134_out, not_135_out, not_136_out, not_137_out,
       not_138_out, not_139_out, not_140_out, not_141_out, not_142_out, not_143_out, not_144_out,
       not_145_out, not_146_out, not_147_out, not_148_out, not_149_out, not_150_out, not_151_out,
       not_152_out, not_153_out, not_154_out, not_155_out, not_156_out, not_157_out, not_158_out,
       not_159_out, not_160_out, not_161_out, not_162_out, not_163_out, not_164_out, not_165_out,
       not_166_out, not_167_out, not_168_out, not_169_out, not_170_out, not_171_out, not_172_out,
       not_173_out, not_174_out, not_175_out, not_176_out, not_177_out, not_178_out, not_179_out,
       not_180_out, not_181_out, not_182_out, not_183_out, not_184_out, not_185_out, not_186_out,
       not_187_out, not_188_out, not_189_out, not_190_out, not_191_out, not_192_out, not_193_out,
       not_194_out, not_195_out, not_196_out, not_197_out, not_198_out, not_199_out, not_200_out,
       not_201_out, not_202_out, not_203_out, not_204_out, not_205_out, not_206_out, not_207_out,
       not_208_out, not_209_out, not_210_out, not_211_out, not_212_out, not_213_out, not_214_out,
       not_215_out, not_216_out, not_217_out, not_218_out, not_219_out, not_220_out, not_221_out,
       not_222_out, not_223_out, not_224_out, not_225_out, not_226_out, not_227_out, not_228_out,
       not_229_out, not_230_out, not_231_out, not_232_out, not_233_out, not_234_out, not_235_out,
       not_236_out, not_237_out, not_238_out, not_239_out, not_240_out, not_241_out, not_242_out,
       not_243_out, not_244_out, not_245_out, not_246_out, not_247_out, not_248_out, not_249_out,
       not_250_out, not_251_out, not_252_out, not_253_out, not_254_out, not_255_out, not_256_out,
       not_257_out, not_258_out, not_259_out, not_260_out, not_261_out, not_262_out, not_263_out,
       not_264_out, not_265_out, not_266_out, not_267_out, not_268_out, not_269_out, not_270_out,
       not_271_out, not_272_out, not_273_out, not_274_out, not_275_out, not_276_out, not_277_out,
       not_278_out, not_279_out, not_280_out, not_281_out, not_282_out, not_283_out, not_284_out,
       not_285_out, not_286_out, not_287_out, not_288_out, not_289_out, not_290_out, not_291_out,
       not_292_out, not_293_out, not_294_out, not_295_out, not_296_out, not_297_out, not_298_out,
       not_299_out, not_300_out, not_301_out, not_302_out, not_303_out, not_304_out, not_305_out,
       not_306_out, not_307_out, not_308_out, not_309_out, not_310_out, not_311_out, not_312_out,
       not_313_out, not_314_out, not_315_out, not_316_out, not_317_out, not_318_out, not_319_out,
       not_320_out, not_321_out, not_322_out, not_323_out, not_324_out, not_325_out, not_326_out,
       not_327_out, not_328_out, not_329_out, not_330_out, not_331_out, not_332_out, not_333_out,
       not_334_out, not_335_out, not_336_out, not_337_out, not_338_out, not_339_out, not_340_out,
       not_341_out, not_342_out, not_343_out, not_344_out, not_345_out, not_346_out, not_347_out,
       not_348_out, not_349_out, not_350_out, not_351_out, not_352_out, not_353_out, not_354_out,
       not_355_out, not_356_out, not_357_out, not_358_out, not_359_out, not_360_out, not_361_out,
       not_362_out, not_363_out, not_364_out, not_365_out, not_366_out, not_367_out, not_368_out,
       not_369_out, not_370_out, not_371_out, not_372_out, not_373_out, not_374_out, not_375_out,
       not_376_out, not_377_out, not_378_out, not_379_out, not_380_out, not_381_out, not_382_out,
       not_383_out, not_384_out, not_385_out, not_386_out, not_387_out, not_388_out, not_389_out,
       not_390_out, not_391_out, not_392_out, not_393_out, not_394_out, not_395_out, not_396_out,
       not_397_out, not_398_out, not_399_out, not_400_out, not_401_out, not_402_out, not_403_out,
       not_404_out, not_405_out, not_406_out, not_407_out, not_408_out, not_409_out, not_410_out,
       not_411_out, not_412_out, not_413_out, not_414_out, not_415_out, not_416_out, not_417_out,
       not_418_out, not_419_out, not_420_out, not_421_out, not_422_out, not_423_out, not_424_out,
       not_425_out, not_426_out, not_427_out, not_428_out, not_429_out, not_430_out, not_431_out,
       not_432_out, not_433_out, not_434_out, not_435_out, not_436_out, not_437_out, not_438_out,
       not_439_out, not_440_out, not_441_out, not_442_out, not_443_out, not_444_out, not_445_out,
       not_446_out, not_447_out, not_448_out, not_449_out, not_450_out, not_451_out, not_452_out,
       not_453_out, not_454_out, not_455_out, not_456_out, not_457_out, not_458_out, not_459_out,
       not_460_out, not_461_out, not_462_out, not_463_out, not_464_out, not_465_out, not_466_out,
       not_467_out, not_468_out, not_469_out, not_470_out, not_471_out, not_472_out, not_473_out,
       not_474_out, not_475_out, not_476_out, not_477_out, not_478_out, not_479_out, not_480_out,
       not_481_out, not_482_out, not_483_out, not_484_out, not_485_out, not_486_out, not_487_out,
       not_488_out, not_489_out, not_490_out, not_491_out, not_492_out, not_493_out, not_494_out,
       not_495_out, not_496_out, not_497_out, not_498_out, not_499_out, not_500_out, not_501_out,
       not_502_out, not_503_out, not_504_out, not_505_out, not_506_out, not_507_out, not_508_out,
       not_509_out, not_510_out, not_511_out, not_512_out, not_513_out, not_514_out, not_515_out,
       not_516_out, not_517_out, not_518_out, not_519_out, not_520_out, not_521_out, not_522_out,
       not_523_out, not_524_out, not_525_out, not_526_out, not_527_out, not_528_out, not_529_out,
       not_530_out, not_531_out, not_532_out, not_533_out, not_534_out, not_535_out, not_536_out,
       not_537_out, not_538_out, not_539_out, not_540_out, not_541_out, not_542_out, not_543_out,
       not_544_out, not_545_out, not_546_out, not_547_out, not_548_out, not_549_out, not_550_out,
       not_551_out, not_552_out, not_553_out, not_554_out, not_555_out, not_556_out, not_557_out,
       not_558_out, not_559_out, not_560_out, not_561_out, not_562_out, not_563_out, not_564_out,
       not_565_out, not_566_out, not_567_out, not_568_out, not_569_out, not_570_out, not_571_out,
       not_572_out, not_573_out, not_574_out, not_575_out, not_576_out, not_577_out, not_578_out,
       not_579_out, not_580_out, not_581_out, not_582_out, not_583_out, not_584_out, not_585_out,
       not_586_out, not_587_out, not_588_out, not_589_out;

  not not_1 (not_1_out, OP4);
  not not_2 (not_2_out, OP3);
  not not_3 (not_3_out, OP2);
  not not_4 (not_4_out, OP4);
  not not_5 (not_5_out, OP3);
  not not_6 (not_6_out, OP2);
  not not_7 (not_7_out, OP1);
  not not_8 (not_8_out, OP0);
  not not_9 (not_9_out, OP4);
  not not_10 (not_10_out, OP3);
  not not_11 (not_11_out, OP1);
  not not_12 (not_12_out, OP0);
  not not_13 (not_13_out, OP4);
  not not_14 (not_14_out, OP3);
  not not_15 (not_15_out, OP2);
  not not_16 (not_16_out, OP1);
  not not_17 (not_17_out, OP4);
  not not_18 (not_18_out, OP3);
  not not_19 (not_19_out, OP1);
  not not_20 (not_20_out, OP4);
  not not_21 (not_21_out, OP2);
  not not_22 (not_22_out, OP4);
  not not_23 (not_23_out, OP2);
  not not_24 (not_24_out, OP1);
  not not_25 (not_25_out, OP0);
  not not_26 (not_26_out, OP4);
  not not_27 (not_27_out, OP2);
  not not_28 (not_28_out, OP1);
  not not_29 (not_29_out, OP5);
  not not_30 (not_30_out, OP4);
  not not_31 (not_31_out, OP2);
  not not_32 (not_32_out, OP1);
  not not_33 (not_33_out, OP0);
  not not_34 (not_34_out, OP5);
  not not_35 (not_35_out, OP4);
  not not_36 (not_36_out, OP1);
  not not_37 (not_37_out, OP0);
  not not_38 (not_38_out, OP5);
  not not_39 (not_39_out, OP4);
  not not_40 (not_40_out, OP2);
  not not_41 (not_41_out, OP1);
  not not_42 (not_42_out, OP5);
  not not_43 (not_43_out, OP4);
  not not_44 (not_44_out, OP2);
  not not_45 (not_45_out, OP0);
  not not_46 (not_46_out, OP5);
  not not_47 (not_47_out, OP4);
  not not_48 (not_48_out, OP1);
  not not_49 (not_49_out, OP4);
  not not_50 (not_50_out, OP3);
  not not_51 (not_51_out, OP2);
  not not_52 (not_52_out, OP4);
  not not_53 (not_53_out, OP2);
  not not_54 (not_54_out, OP5);
  not not_55 (not_55_out, OP4);
  not not_56 (not_56_out, OP0);
  not not_57 (not_57_out, OP5);
  not not_58 (not_58_out, OP4);
  not not_59 (not_59_out, OP2);
  not not_60 (not_60_out, OP4);
  not not_61 (not_61_out, OP3);
  not not_62 (not_62_out, OP2);
  not not_63 (not_63_out, OP1);
  not not_64 (not_64_out, OP0);
  not not_65 (not_65_out, OP4);
  not not_66 (not_66_out, OP3);
  not not_67 (not_67_out, OP1);
  not not_68 (not_68_out, OP0);
  not not_69 (not_69_out, OP4);
  not not_70 (not_70_out, OP3);
  not not_71 (not_71_out, OP2);
  not not_72 (not_72_out, OP1);
  not not_73 (not_73_out, OP4);
  not not_74 (not_74_out, OP3);
  not not_75 (not_75_out, OP1);
  not not_76 (not_76_out, OP4);
  not not_77 (not_77_out, OP2);
  not not_78 (not_78_out, OP1);
  not not_79 (not_79_out, OP0);
  not not_80 (not_80_out, OP4);
  not not_81 (not_81_out, OP2);
  not not_82 (not_82_out, OP1);
  not not_83 (not_83_out, OP5);
  not not_84 (not_84_out, OP4);
  not not_85 (not_85_out, OP3);
  not not_86 (not_86_out, OP2);
  not not_87 (not_87_out, OP1);
  not not_88 (not_88_out, OP0);
  not not_89 (not_89_out, F5);
  not not_90 (not_90_out, F4);
  not not_91 (not_91_out, F3);
  not not_92 (not_92_out, F2);
  not not_93 (not_93_out, F1);
  not not_94 (not_94_out, F0);
  not not_95 (not_95_out, OP5);
  not not_96 (not_96_out, OP4);
  not not_97 (not_97_out, OP3);
  not not_98 (not_98_out, OP2);
  not not_99 (not_99_out, OP1);
  not not_100 (not_100_out, OP0);
  not not_101 (not_101_out, F5);
  not not_102 (not_102_out, F4);
  not not_103 (not_103_out, F3);
  not not_104 (not_104_out, F2);
  not not_105 (not_105_out, OP5);
  not not_106 (not_106_out, OP4);
  not not_107 (not_107_out, OP3);
  not not_108 (not_108_out, OP2);
  not not_109 (not_109_out, OP1);
  not not_110 (not_110_out, OP0);
  not not_111 (not_111_out, F5);
  not not_112 (not_112_out, F4);
  not not_113 (not_113_out, F3);
  not not_114 (not_114_out, F2);
  not not_115 (not_115_out, F0);
  not not_116 (not_116_out, OP5);
  not not_117 (not_117_out, OP4);
  not not_118 (not_118_out, OP3);
  not not_119 (not_119_out, OP2);
  not not_120 (not_120_out, OP1);
  not not_121 (not_121_out, OP0);
  not not_122 (not_122_out, F4);
  not not_123 (not_123_out, F3);
  not not_124 (not_124_out, F2);
  not not_125 (not_125_out, F1);
  not not_126 (not_126_out, F0);
  not not_127 (not_127_out, OP5);
  not not_128 (not_128_out, OP4);
  not not_129 (not_129_out, OP3);
  not not_130 (not_130_out, OP2);
  not not_131 (not_131_out, OP1);
  not not_132 (not_132_out, OP0);
  not not_133 (not_133_out, F4);
  not not_134 (not_134_out, F3);
  not not_135 (not_135_out, F2);
  not not_136 (not_136_out, F1);
  not not_137 (not_137_out, OP5);
  not not_138 (not_138_out, OP4);
  not not_139 (not_139_out, OP3);
  not not_140 (not_140_out, OP2);
  not not_141 (not_141_out, OP1);
  not not_142 (not_142_out, OP0);
  not not_143 (not_143_out, F4);
  not not_144 (not_144_out, F3);
  not not_145 (not_145_out, F2);
  not not_146 (not_146_out, F0);
  not not_147 (not_147_out, OP5);
  not not_148 (not_148_out, OP4);
  not not_149 (not_149_out, OP3);
  not not_150 (not_150_out, OP2);
  not not_151 (not_151_out, OP1);
  not not_152 (not_152_out, OP0);
  not not_153 (not_153_out, F4);
  not not_154 (not_154_out, F3);
  not not_155 (not_155_out, F1);
  not not_156 (not_156_out, F0);
  not not_157 (not_157_out, OP5);
  not not_158 (not_158_out, OP4);
  not not_159 (not_159_out, OP3);
  not not_160 (not_160_out, OP2);
  not not_161 (not_161_out, OP1);
  not not_162 (not_162_out, OP0);
  not not_163 (not_163_out, F4);
  not not_164 (not_164_out, F3);
  not not_165 (not_165_out, F1);
  not not_166 (not_166_out, OP5);
  not not_167 (not_167_out, OP4);
  not not_168 (not_168_out, OP3);
  not not_169 (not_169_out, OP2);
  not not_170 (not_170_out, OP1);
  not not_171 (not_171_out, OP0);
  not not_172 (not_172_out, F4);
  not not_173 (not_173_out, F3);
  not not_174 (not_174_out, OP5);
  not not_175 (not_175_out, OP4);
  not not_176 (not_176_out, OP3);
  not not_177 (not_177_out, OP2);
  not not_178 (not_178_out, OP1);
  not not_179 (not_179_out, OP0);
  not not_180 (not_180_out, F4);
  not not_181 (not_181_out, F2);
  not not_182 (not_182_out, F0);
  not not_183 (not_183_out, OP5);
  not not_184 (not_184_out, OP4);
  not not_185 (not_185_out, OP3);
  not not_186 (not_186_out, OP2);
  not not_187 (not_187_out, OP1);
  not not_188 (not_188_out, OP0);
  not not_189 (not_189_out, F4);
  not not_190 (not_190_out, F2);
  not not_191 (not_191_out, OP5);
  not not_192 (not_192_out, OP4);
  not not_193 (not_193_out, OP3);
  not not_194 (not_194_out, OP2);
  not not_195 (not_195_out, OP5);
  not not_196 (not_196_out, OP4);
  not not_197 (not_197_out, OP2);
  not not_198 (not_198_out, OP1);
  not not_199 (not_199_out, OP0);
  not not_200 (not_200_out, OP5);
  not not_201 (not_201_out, OP4);
  not not_202 (not_202_out, OP1);
  not not_203 (not_203_out, OP0);
  not not_204 (not_204_out, OP5);
  not not_205 (not_205_out, OP4);
  not not_206 (not_206_out, OP2);
  not not_207 (not_207_out, OP1);
  not not_208 (not_208_out, OP5);
  not not_209 (not_209_out, OP4);
  not not_210 (not_210_out, OP2);
  not not_211 (not_211_out, OP0);
  not not_212 (not_212_out, OP5);
  not not_213 (not_213_out, OP4);
  not not_214 (not_214_out, OP1);
  not not_215 (not_215_out, OP4);
  not not_216 (not_216_out, OP3);
  not not_217 (not_217_out, OP2);
  not not_218 (not_218_out, OP5);
  not not_219 (not_219_out, OP4);
  not not_220 (not_220_out, OP3);
  not not_221 (not_221_out, OP2);
  not not_222 (not_222_out, OP1);
  not not_223 (not_223_out, OP0);
  not not_224 (not_224_out, F5);
  not not_225 (not_225_out, F4);
  not not_226 (not_226_out, F3);
  not not_227 (not_227_out, F1);
  not not_228 (not_228_out, F0);
  not not_229 (not_229_out, OP5);
  not not_230 (not_230_out, OP4);
  not not_231 (not_231_out, OP3);
  not not_232 (not_232_out, OP2);
  not not_233 (not_233_out, OP1);
  not not_234 (not_234_out, OP0);
  not not_235 (not_235_out, F5);
  not not_236 (not_236_out, F4);
  not not_237 (not_237_out, F3);
  not not_238 (not_238_out, F0);
  not not_239 (not_239_out, OP5);
  not not_240 (not_240_out, OP4);
  not not_241 (not_241_out, OP3);
  not not_242 (not_242_out, OP2);
  not not_243 (not_243_out, OP1);
  not not_244 (not_244_out, OP0);
  not not_245 (not_245_out, F5);
  not not_246 (not_246_out, F4);
  not not_247 (not_247_out, F3);
  not not_248 (not_248_out, OP5);
  not not_249 (not_249_out, OP4);
  not not_250 (not_250_out, OP3);
  not not_251 (not_251_out, OP2);
  not not_252 (not_252_out, OP1);
  not not_253 (not_253_out, OP0);
  not not_254 (not_254_out, F4);
  not not_255 (not_255_out, F3);
  not not_256 (not_256_out, F2);
  not not_257 (not_257_out, OP5);
  not not_258 (not_258_out, OP4);
  not not_259 (not_259_out, OP3);
  not not_260 (not_260_out, OP2);
  not not_261 (not_261_out, OP1);
  not not_262 (not_262_out, OP0);
  not not_263 (not_263_out, F4);
  not not_264 (not_264_out, F3);
  not not_265 (not_265_out, F0);
  not not_266 (not_266_out, OP5);
  not not_267 (not_267_out, OP4);
  not not_268 (not_268_out, OP0);
  not not_269 (not_269_out, OP5);
  not not_270 (not_270_out, OP4);
  not not_271 (not_271_out, OP5);
  not not_272 (not_272_out, OP4);
  not not_273 (not_273_out, OP2);
  not not_274 (not_274_out, OP5);
  not not_275 (not_275_out, OP4);
  not not_276 (not_276_out, OP3);
  not not_277 (not_277_out, OP2);
  not not_278 (not_278_out, OP1);
  not not_279 (not_279_out, OP0);
  not not_280 (not_280_out, F5);
  not not_281 (not_281_out, F3);
  not not_282 (not_282_out, F2);
  not not_283 (not_283_out, F0);
  not not_284 (not_284_out, OP4);
  not not_285 (not_285_out, OP3);
  not not_286 (not_286_out, OP2);
  not not_287 (not_287_out, OP1);
  not not_288 (not_288_out, OP0);
  not not_289 (not_289_out, OP4);
  not not_290 (not_290_out, OP3);
  not not_291 (not_291_out, OP1);
  not not_292 (not_292_out, OP0);
  not not_293 (not_293_out, OP4);
  not not_294 (not_294_out, OP3);
  not not_295 (not_295_out, OP2);
  not not_296 (not_296_out, OP1);
  not not_297 (not_297_out, OP4);
  not not_298 (not_298_out, OP3);
  not not_299 (not_299_out, OP1);
  not not_300 (not_300_out, OP5);
  not not_301 (not_301_out, OP4);
  not not_302 (not_302_out, OP3);
  not not_303 (not_303_out, OP2);
  not not_304 (not_304_out, OP1);
  not not_305 (not_305_out, OP0);
  not not_306 (not_306_out, F5);
  not not_307 (not_307_out, F4);
  not not_308 (not_308_out, F1);
  not not_309 (not_309_out, F0);
  not not_310 (not_310_out, OP5);
  not not_311 (not_311_out, OP4);
  not not_312 (not_312_out, OP3);
  not not_313 (not_313_out, OP1);
  not not_314 (not_314_out, OP0);
  not not_315 (not_315_out, OP5);
  not not_316 (not_316_out, OP4);
  not not_317 (not_317_out, OP3);
  not not_318 (not_318_out, OP1);
  not not_319 (not_319_out, OP5);
  not not_320 (not_320_out, OP4);
  not not_321 (not_321_out, OP2);
  not not_322 (not_322_out, OP1);
  not not_323 (not_323_out, OP0);
  not not_324 (not_324_out, OP5);
  not not_325 (not_325_out, OP4);
  not not_326 (not_326_out, OP2);
  not not_327 (not_327_out, OP1);
  not not_328 (not_328_out, OP5);
  not not_329 (not_329_out, OP4);
  not not_330 (not_330_out, OP2);
  not not_331 (not_331_out, OP0);
  not not_332 (not_332_out, OP4);
  not not_333 (not_333_out, OP3);
  not not_334 (not_334_out, OP2);
  not not_335 (not_335_out, OP4);
  not not_336 (not_336_out, OP2);
  not not_337 (not_337_out, OP5);
  not not_338 (not_338_out, OP4);
  not not_339 (not_339_out, OP2);
  not not_340 (not_340_out, OP4);
  not not_341 (not_341_out, OP3);
  not not_342 (not_342_out, OP2);
  not not_343 (not_343_out, OP1);
  not not_344 (not_344_out, OP0);
  not not_345 (not_345_out, OP4);
  not not_346 (not_346_out, OP3);
  not not_347 (not_347_out, OP1);
  not not_348 (not_348_out, OP0);
  not not_349 (not_349_out, OP4);
  not not_350 (not_350_out, OP3);
  not not_351 (not_351_out, OP2);
  not not_352 (not_352_out, OP1);
  not not_353 (not_353_out, OP4);
  not not_354 (not_354_out, OP3);
  not not_355 (not_355_out, OP1);
  not not_356 (not_356_out, OP4);
  not not_357 (not_357_out, OP2);
  not not_358 (not_358_out, OP1);
  not not_359 (not_359_out, OP0);
  not not_360 (not_360_out, OP4);
  not not_361 (not_361_out, OP2);
  not not_362 (not_362_out, OP1);
  not not_363 (not_363_out, OP5);
  not not_364 (not_364_out, OP4);
  not not_365 (not_365_out, OP3);
  not not_366 (not_366_out, OP0);
  not not_367 (not_367_out, OP5);
  not not_368 (not_368_out, OP4);
  not not_369 (not_369_out, OP3);
  not not_370 (not_370_out, OP5);
  not not_371 (not_371_out, OP4);
  not not_372 (not_372_out, OP3);
  not not_373 (not_373_out, OP2);
  not not_374 (not_374_out, OP1);
  not not_375 (not_375_out, OP5);
  not not_376 (not_376_out, OP4);
  not not_377 (not_377_out, OP3);
  not not_378 (not_378_out, OP2);
  not not_379 (not_379_out, OP1);
  not not_380 (not_380_out, OP5);
  not not_381 (not_381_out, OP4);
  not not_382 (not_382_out, OP3);
  not not_383 (not_383_out, OP2);
  not not_384 (not_384_out, OP1);
  not not_385 (not_385_out, OP0);
  not not_386 (not_386_out, F5);
  not not_387 (not_387_out, F4);
  not not_388 (not_388_out, F3);
  not not_389 (not_389_out, F2);
  not not_390 (not_390_out, F1);
  not not_391 (not_391_out, F0);
  not not_392 (not_392_out, OP5);
  not not_393 (not_393_out, OP4);
  not not_394 (not_394_out, OP3);
  not not_395 (not_395_out, OP2);
  not not_396 (not_396_out, OP1);
  not not_397 (not_397_out, OP0);
  not not_398 (not_398_out, F5);
  not not_399 (not_399_out, F4);
  not not_400 (not_400_out, F3);
  not not_401 (not_401_out, F2);
  not not_402 (not_402_out, OP5);
  not not_403 (not_403_out, OP4);
  not not_404 (not_404_out, OP3);
  not not_405 (not_405_out, OP2);
  not not_406 (not_406_out, OP1);
  not not_407 (not_407_out, OP0);
  not not_408 (not_408_out, F5);
  not not_409 (not_409_out, F4);
  not not_410 (not_410_out, F3);
  not not_411 (not_411_out, F2);
  not not_412 (not_412_out, F0);
  not not_413 (not_413_out, OP5);
  not not_414 (not_414_out, OP4);
  not not_415 (not_415_out, OP3);
  not not_416 (not_416_out, OP2);
  not not_417 (not_417_out, OP1);
  not not_418 (not_418_out, OP0);
  not not_419 (not_419_out, F4);
  not not_420 (not_420_out, F3);
  not not_421 (not_421_out, F2);
  not not_422 (not_422_out, F1);
  not not_423 (not_423_out, F0);
  not not_424 (not_424_out, OP5);
  not not_425 (not_425_out, OP4);
  not not_426 (not_426_out, OP3);
  not not_427 (not_427_out, OP2);
  not not_428 (not_428_out, OP1);
  not not_429 (not_429_out, OP0);
  not not_430 (not_430_out, F4);
  not not_431 (not_431_out, F3);
  not not_432 (not_432_out, F2);
  not not_433 (not_433_out, F1);
  not not_434 (not_434_out, OP5);
  not not_435 (not_435_out, OP4);
  not not_436 (not_436_out, OP3);
  not not_437 (not_437_out, OP2);
  not not_438 (not_438_out, OP1);
  not not_439 (not_439_out, OP0);
  not not_440 (not_440_out, F4);
  not not_441 (not_441_out, F3);
  not not_442 (not_442_out, F2);
  not not_443 (not_443_out, F0);
  not not_444 (not_444_out, OP5);
  not not_445 (not_445_out, OP4);
  not not_446 (not_446_out, OP3);
  not not_447 (not_447_out, OP2);
  not not_448 (not_448_out, OP1);
  not not_449 (not_449_out, OP0);
  not not_450 (not_450_out, F4);
  not not_451 (not_451_out, F3);
  not not_452 (not_452_out, F1);
  not not_453 (not_453_out, F0);
  not not_454 (not_454_out, OP5);
  not not_455 (not_455_out, OP4);
  not not_456 (not_456_out, OP3);
  not not_457 (not_457_out, OP2);
  not not_458 (not_458_out, OP1);
  not not_459 (not_459_out, OP0);
  not not_460 (not_460_out, F4);
  not not_461 (not_461_out, F3);
  not not_462 (not_462_out, F1);
  not not_463 (not_463_out, OP5);
  not not_464 (not_464_out, OP4);
  not not_465 (not_465_out, OP3);
  not not_466 (not_466_out, OP2);
  not not_467 (not_467_out, OP1);
  not not_468 (not_468_out, OP0);
  not not_469 (not_469_out, F4);
  not not_470 (not_470_out, F3);
  not not_471 (not_471_out, OP5);
  not not_472 (not_472_out, OP4);
  not not_473 (not_473_out, OP3);
  not not_474 (not_474_out, OP2);
  not not_475 (not_475_out, OP1);
  not not_476 (not_476_out, OP0);
  not not_477 (not_477_out, F4);
  not not_478 (not_478_out, F2);
  not not_479 (not_479_out, F0);
  not not_480 (not_480_out, OP5);
  not not_481 (not_481_out, OP4);
  not not_482 (not_482_out, OP3);
  not not_483 (not_483_out, OP2);
  not not_484 (not_484_out, OP1);
  not not_485 (not_485_out, OP0);
  not not_486 (not_486_out, F4);
  not not_487 (not_487_out, F2);
  not not_488 (not_488_out, OP5);
  not not_489 (not_489_out, OP4);
  not not_490 (not_490_out, OP3);
  not not_491 (not_491_out, OP2);
  not not_492 (not_492_out, OP1);
  not not_493 (not_493_out, OP0);
  not not_494 (not_494_out, F5);
  not not_495 (not_495_out, F4);
  not not_496 (not_496_out, F3);
  not not_497 (not_497_out, F1);
  not not_498 (not_498_out, F0);
  not not_499 (not_499_out, OP5);
  not not_500 (not_500_out, OP4);
  not not_501 (not_501_out, OP3);
  not not_502 (not_502_out, OP2);
  not not_503 (not_503_out, OP1);
  not not_504 (not_504_out, OP0);
  not not_505 (not_505_out, F5);
  not not_506 (not_506_out, F4);
  not not_507 (not_507_out, F3);
  not not_508 (not_508_out, F0);
  not not_509 (not_509_out, OP5);
  not not_510 (not_510_out, OP4);
  not not_511 (not_511_out, OP3);
  not not_512 (not_512_out, OP2);
  not not_513 (not_513_out, OP1);
  not not_514 (not_514_out, OP0);
  not not_515 (not_515_out, F5);
  not not_516 (not_516_out, F4);
  not not_517 (not_517_out, F3);
  not not_518 (not_518_out, OP5);
  not not_519 (not_519_out, OP4);
  not not_520 (not_520_out, OP3);
  not not_521 (not_521_out, OP2);
  not not_522 (not_522_out, OP1);
  not not_523 (not_523_out, OP0);
  not not_524 (not_524_out, F4);
  not not_525 (not_525_out, F3);
  not not_526 (not_526_out, F2);
  not not_527 (not_527_out, OP5);
  not not_528 (not_528_out, OP4);
  not not_529 (not_529_out, OP3);
  not not_530 (not_530_out, OP2);
  not not_531 (not_531_out, OP1);
  not not_532 (not_532_out, OP0);
  not not_533 (not_533_out, F4);
  not not_534 (not_534_out, F3);
  not not_535 (not_535_out, F0);
  not not_536 (not_536_out, OP5);
  not not_537 (not_537_out, OP4);
  not not_538 (not_538_out, OP3);
  not not_539 (not_539_out, OP2);
  not not_540 (not_540_out, OP1);
  not not_541 (not_541_out, OP0);
  not not_542 (not_542_out, F5);
  not not_543 (not_543_out, F3);
  not not_544 (not_544_out, F2);
  not not_545 (not_545_out, F0);
  not not_546 (not_546_out, OP5);
  not not_547 (not_547_out, OP4);
  not not_548 (not_548_out, OP3);
  not not_549 (not_549_out, OP1);
  not not_550 (not_550_out, OP0);
  not not_551 (not_551_out, OP5);
  not not_552 (not_552_out, OP4);
  not not_553 (not_553_out, OP3);
  not not_554 (not_554_out, OP1);
  not not_555 (not_555_out, OP5);
  not not_556 (not_556_out, OP4);
  not not_557 (not_557_out, OP3);
  not not_558 (not_558_out, OP2);
  not not_559 (not_559_out, OP1);
  not not_560 (not_560_out, OP0);
  not not_561 (not_561_out, F5);
  not not_562 (not_562_out, F4);
  not not_563 (not_563_out, F2);
  not not_564 (not_564_out, F1);
  not not_565 (not_565_out, F0);
  not not_566 (not_566_out, OP5);
  not not_567 (not_567_out, OP4);
  not not_568 (not_568_out, OP3);
  not not_569 (not_569_out, OP2);
  not not_570 (not_570_out, OP1);
  not not_571 (not_571_out, OP0);
  not not_572 (not_572_out, F5);
  not not_573 (not_573_out, F4);
  not not_574 (not_574_out, F2);
  not not_575 (not_575_out, F1);
  not not_576 (not_576_out, F0);
  not not_577 (not_577_out, OP5);
  not not_578 (not_578_out, OP4);
  not not_579 (not_579_out, OP3);
  not not_580 (not_580_out, OP2);
  not not_581 (not_581_out, OP0);
  not not_582 (not_582_out, OP5);
  not not_583 (not_583_out, OP4);
  not not_584 (not_584_out, OP3);
  not not_585 (not_585_out, OP2);
  not not_586 (not_586_out, OP5);
  not not_587 (not_587_out, OP4);
  not not_588 (not_588_out, OP3);
  not not_589 (not_589_out, OP2);
  and and_1 (and_1_out, OP5, not_1_out, not_2_out, not_3_out, OP1, OP0);
  and and_2 (and_2_out, OP5, not_4_out, not_5_out, not_6_out, not_7_out, not_8_out);
  and and_3 (and_3_out, OP5, not_9_out, not_10_out, OP2, not_11_out, not_12_out);
  and and_4 (and_4_out, OP5, not_13_out, not_14_out, not_15_out, not_16_out, OP0);
  and and_5 (and_5_out, OP5, not_17_out, not_18_out, OP2, not_19_out, OP0);
  and and_6 (and_6_out, OP5, not_20_out, OP3, not_21_out, OP1, OP0);
  and and_7 (and_7_out, OP5, not_22_out, OP3, not_23_out, not_24_out, not_25_out);
  and and_8 (and_8_out, OP5, not_26_out, OP3, not_27_out, not_28_out, OP0);
  and and_9 (and_9_out, not_29_out, not_30_out, OP3, not_31_out, not_32_out, not_33_out);
  and and_10 (and_10_out, not_34_out, not_35_out, OP3, OP2, not_36_out, not_37_out);
  and and_11 (and_11_out, not_38_out, not_39_out, OP3, not_40_out, not_41_out, OP0);
  and and_12 (and_12_out, not_42_out, not_43_out, OP3, not_44_out, OP1, not_45_out);
  and and_13 (and_13_out, not_46_out, not_47_out, OP3, OP2, not_48_out, OP0);
  and and_14 (and_14_out, OP5, not_49_out, not_50_out, not_51_out, OP1, OP0);
  and and_15 (and_15_out, OP5, not_52_out, OP3, not_53_out, OP1, OP0);
  and and_16 (and_16_out, not_54_out, not_55_out, OP3, OP2, OP1, not_56_out);
  and and_17 (and_17_out, not_57_out, not_58_out, OP3, not_59_out, OP1, OP0);
  and and_18 (and_18_out, OP5, not_60_out, not_61_out, not_62_out, not_63_out, not_64_out);
  and and_19 (and_19_out, OP5, not_65_out, not_66_out, OP2, not_67_out, not_68_out);
  and and_20 (and_20_out, OP5, not_69_out, not_70_out, not_71_out, not_72_out, OP0);
  and and_21 (and_21_out, OP5, not_73_out, not_74_out, OP2, not_75_out, OP0);
  and and_22 (and_22_out, OP5, not_76_out, OP3, not_77_out, not_78_out, not_79_out);
  and and_23 (and_23_out, OP5, not_80_out, OP3, not_81_out, not_82_out, OP0);
  and and_24 (and_24_out, not_83_out, not_84_out, not_85_out, not_86_out, not_87_out, not_88_out, not_89_out, not_90_out, not_91_out, not_92_out, not_93_out, not_94_out);
  and and_25 (and_25_out, not_95_out, not_96_out, not_97_out, not_98_out, not_99_out, not_100_out, not_101_out, not_102_out, not_103_out, not_104_out, F1, F0);
  and and_26 (and_26_out, not_105_out, not_106_out, not_107_out, not_108_out, not_109_out, not_110_out, not_111_out, not_112_out, not_113_out, not_114_out, F1, not_115_out);
  and and_27 (and_27_out, not_116_out, not_117_out, not_118_out, not_119_out, not_120_out, not_121_out, F5, not_122_out, not_123_out, not_124_out, not_125_out, not_126_out);
  and and_28 (and_28_out, not_127_out, not_128_out, not_129_out, not_130_out, not_131_out, not_132_out, F5, not_133_out, not_134_out, not_135_out, not_136_out, F0);
  and and_29 (and_29_out, not_137_out, not_138_out, not_139_out, not_140_out, not_141_out, not_142_out, F5, not_143_out, not_144_out, not_145_out, F1, not_146_out);
  and and_30 (and_30_out, not_147_out, not_148_out, not_149_out, not_150_out, not_151_out, not_152_out, F5, not_153_out, not_154_out, F2, not_155_out, not_156_out);
  and and_31 (and_31_out, not_157_out, not_158_out, not_159_out, not_160_out, not_161_out, not_162_out, F5, not_163_out, not_164_out, F2, not_165_out, F0);
  and and_32 (and_32_out, not_166_out, not_167_out, not_168_out, not_169_out, not_170_out, not_171_out, F5, not_172_out, not_173_out, F2, F1, F0);
  and and_33 (and_33_out, not_174_out, not_175_out, not_176_out, not_177_out, not_178_out, not_179_out, F5, not_180_out, F3, not_181_out, F1, not_182_out);
  and and_34 (and_34_out, not_183_out, not_184_out, not_185_out, not_186_out, not_187_out, not_188_out, F5, not_189_out, F3, not_190_out, F1, F0);
  and and_35 (and_35_out, not_191_out, not_192_out, not_193_out, not_194_out, OP1, OP0);
  and and_36 (and_36_out, not_195_out, not_196_out, OP3, not_197_out, not_198_out, not_199_out);
  and and_37 (and_37_out, not_200_out, not_201_out, OP3, OP2, not_202_out, not_203_out);
  and and_38 (and_38_out, not_204_out, not_205_out, OP3, not_206_out, not_207_out, OP0);
  and and_39 (and_39_out, not_208_out, not_209_out, OP3, not_210_out, OP1, not_211_out);
  and and_40 (and_40_out, not_212_out, not_213_out, OP3, OP2, not_214_out, OP0);
  and and_41 (and_41_out, OP5, not_215_out, not_216_out, not_217_out, OP1, OP0);
  and and_42 (and_42_out, not_218_out, not_219_out, not_220_out, not_221_out, not_222_out, not_223_out, not_224_out, not_225_out, not_226_out, F2, not_227_out, not_228_out);
  and and_43 (and_43_out, not_229_out, not_230_out, not_231_out, not_232_out, not_233_out, not_234_out, not_235_out, not_236_out, not_237_out, F2, F1, not_238_out);
  and and_44 (and_44_out, not_239_out, not_240_out, not_241_out, not_242_out, not_243_out, not_244_out, not_245_out, not_246_out, not_247_out, F2, F1, F0);
  and and_45 (and_45_out, not_248_out, not_249_out, not_250_out, not_251_out, not_252_out, not_253_out, F5, not_254_out, not_255_out, not_256_out, F1, F0);
  and and_46 (and_46_out, not_257_out, not_258_out, not_259_out, not_260_out, not_261_out, not_262_out, F5, not_263_out, not_264_out, F2, F1, not_265_out);
  and and_47 (and_47_out, not_266_out, not_267_out, OP3, OP2, OP1, not_268_out);
  and and_48 (and_48_out, not_269_out, not_270_out, OP3, OP2, OP1, OP0);
  and and_49 (and_49_out, not_271_out, not_272_out, OP3, not_273_out, OP1, OP0);
  and and_50 (and_50_out, not_274_out, not_275_out, not_276_out, not_277_out, not_278_out, not_279_out, not_280_out, F4, not_281_out, not_282_out, F1, not_283_out);
  and and_51 (and_51_out, OP5, not_284_out, not_285_out, not_286_out, not_287_out, not_288_out);
  and and_52 (and_52_out, OP5, not_289_out, not_290_out, OP2, not_291_out, not_292_out);
  and and_53 (and_53_out, OP5, not_293_out, not_294_out, not_295_out, not_296_out, OP0);
  and and_54 (and_54_out, OP5, not_297_out, not_298_out, OP2, not_299_out, OP0);
  and and_55 (SysCALL, not_300_out, not_301_out, not_302_out, not_303_out, not_304_out, not_305_out, not_306_out, not_307_out, F3, F2, not_308_out, not_309_out);
  and and_56 (and_56_out, not_310_out, not_311_out, not_312_out, OP2, not_313_out, not_314_out);
  and and_57 (and_57_out, not_315_out, not_316_out, not_317_out, OP2, not_318_out, OP0);
  and and_58 (and_58_out, not_319_out, not_320_out, OP3, not_321_out, not_322_out, not_323_out);
  and and_59 (and_59_out, not_324_out, not_325_out, OP3, not_326_out, not_327_out, OP0);
  and and_60 (and_60_out, not_328_out, not_329_out, OP3, not_330_out, OP1, not_331_out);
  and and_61 (and_61_out, OP5, not_332_out, not_333_out, not_334_out, OP1, OP0);
  and and_62 (and_62_out, OP5, not_335_out, OP3, not_336_out, OP1, OP0);
  and and_63 (and_63_out, not_337_out, not_338_out, OP3, not_339_out, OP1, OP0);
  and and_64 (and_64_out, OP5, not_340_out, not_341_out, not_342_out, not_343_out, not_344_out);
  and and_65 (and_65_out, OP5, not_345_out, not_346_out, OP2, not_347_out, not_348_out);
  and and_66 (and_66_out, OP5, not_349_out, not_350_out, not_351_out, not_352_out, OP0);
  and and_67 (and_67_out, OP5, not_353_out, not_354_out, OP2, not_355_out, OP0);
  and and_68 (and_68_out, OP5, not_356_out, OP3, not_357_out, not_358_out, not_359_out);
  and and_69 (and_69_out, OP5, not_360_out, OP3, not_361_out, not_362_out, OP0);
  and and_70 (and_70_out, not_363_out, not_364_out, not_365_out, OP2, OP1, not_366_out);
  and and_71 (and_71_out, not_367_out, not_368_out, not_369_out, OP2, OP1, OP0);
  and and_72 (and_72_out, not_370_out, not_371_out, not_372_out, not_373_out, not_374_out, OP0);
  and and_73 (and_73_out, not_375_out, not_376_out, not_377_out, not_378_out, not_379_out, OP0);
  and and_74 (and_74_out, not_380_out, not_381_out, not_382_out, not_383_out, not_384_out, not_385_out, not_386_out, not_387_out, not_388_out, not_389_out, not_390_out, not_391_out);
  and and_75 (and_75_out, not_392_out, not_393_out, not_394_out, not_395_out, not_396_out, not_397_out, not_398_out, not_399_out, not_400_out, not_401_out, F1, F0);
  and and_76 (and_76_out, not_402_out, not_403_out, not_404_out, not_405_out, not_406_out, not_407_out, not_408_out, not_409_out, not_410_out, not_411_out, F1, not_412_out);
  and and_77 (and_77_out, not_413_out, not_414_out, not_415_out, not_416_out, not_417_out, not_418_out, F5, not_419_out, not_420_out, not_421_out, not_422_out, not_423_out);
  and and_78 (and_78_out, not_424_out, not_425_out, not_426_out, not_427_out, not_428_out, not_429_out, F5, not_430_out, not_431_out, not_432_out, not_433_out, F0);
  and and_79 (and_79_out, not_434_out, not_435_out, not_436_out, not_437_out, not_438_out, not_439_out, F5, not_440_out, not_441_out, not_442_out, F1, not_443_out);
  and and_80 (and_80_out, not_444_out, not_445_out, not_446_out, not_447_out, not_448_out, not_449_out, F5, not_450_out, not_451_out, F2, not_452_out, not_453_out);
  and and_81 (and_81_out, not_454_out, not_455_out, not_456_out, not_457_out, not_458_out, not_459_out, F5, not_460_out, not_461_out, F2, not_462_out, F0);
  and and_82 (and_82_out, not_463_out, not_464_out, not_465_out, not_466_out, not_467_out, not_468_out, F5, not_469_out, not_470_out, F2, F1, F0);
  and and_83 (and_83_out, not_471_out, not_472_out, not_473_out, not_474_out, not_475_out, not_476_out, F5, not_477_out, F3, not_478_out, F1, not_479_out);
  and and_84 (and_84_out, not_480_out, not_481_out, not_482_out, not_483_out, not_484_out, not_485_out, F5, not_486_out, F3, not_487_out, F1, F0);
  and and_85 (and_85_out, not_488_out, not_489_out, not_490_out, not_491_out, not_492_out, not_493_out, not_494_out, not_495_out, not_496_out, F2, not_497_out, not_498_out);
  and and_86 (and_86_out, not_499_out, not_500_out, not_501_out, not_502_out, not_503_out, not_504_out, not_505_out, not_506_out, not_507_out, F2, F1, not_508_out);
  and and_87 (and_87_out, not_509_out, not_510_out, not_511_out, not_512_out, not_513_out, not_514_out, not_515_out, not_516_out, not_517_out, F2, F1, F0);
  and and_88 (and_88_out, not_518_out, not_519_out, not_520_out, not_521_out, not_522_out, not_523_out, F5, not_524_out, not_525_out, not_526_out, F1, F0);
  and and_89 (and_89_out, not_527_out, not_528_out, not_529_out, not_530_out, not_531_out, not_532_out, F5, not_533_out, not_534_out, F2, F1, not_535_out);
  and and_90 (and_90_out, not_536_out, not_537_out, not_538_out, not_539_out, not_540_out, not_541_out, not_542_out, F4, not_543_out, not_544_out, F1, not_545_out);
  and and_91 (BEQ, not_546_out, not_547_out, not_548_out, OP2, not_549_out, not_550_out);
  and and_92 (BNE, not_551_out, not_552_out, not_553_out, OP2, not_554_out, OP0);
  and and_93 (JR, not_555_out, not_556_out, not_557_out, not_558_out, not_559_out, not_560_out, not_561_out, not_562_out, F3, not_563_out, not_564_out, not_565_out);
  and and_94 (and_94_out, not_566_out, not_567_out, not_568_out, not_569_out, not_570_out, not_571_out, not_572_out, not_573_out, F3, not_574_out, not_575_out, not_576_out);
  and and_95 (and_95_out, not_577_out, not_578_out, not_579_out, not_580_out, OP1, not_581_out);
  and and_96 (and_96_out, not_582_out, not_583_out, not_584_out, not_585_out, OP1, OP0);
  and and_97 (JAL, not_586_out, not_587_out, not_588_out, not_589_out, OP1, OP0);
  or or_1 (MemToReg, and_1_out, and_2_out, and_3_out, and_4_out, and_5_out);
  or or_2 (MemWrite, and_6_out, and_7_out, and_8_out);
  or or_3 (ALU_SRC, and_9_out, and_10_out, and_11_out, and_12_out, and_13_out, and_14_out, and_15_out, and_16_out, and_17_out, and_18_out, and_19_out, and_20_out, and_21_out, and_22_out, and_23_out);
  or or_4 (JMP, and_94_out, and_95_out, and_96_out);
  or or_5 (SignedExt, and_56_out, and_57_out, and_58_out, and_59_out, and_60_out, and_61_out, and_62_out, and_63_out, and_64_out, and_65_out, and_66_out, and_67_out, and_68_out, and_69_out, and_70_out, and_71_out, and_72_out, and_73_out);
  or or_6 (RegDst, and_74_out, and_75_out, and_76_out, and_77_out, and_78_out, and_79_out, and_80_out, and_81_out, and_82_out, and_83_out, and_84_out, and_85_out, and_86_out, and_87_out, and_88_out, and_89_out, and_90_out);
  or or_7 (RegWrite, and_24_out, and_25_out, and_26_out, and_27_out, and_28_out, and_29_out, and_30_out, and_31_out, and_32_out, and_33_out, and_34_out, and_35_out, and_36_out, and_37_out, and_38_out, and_39_out, and_40_out, and_41_out, and_42_out, and_43_out, and_44_out, and_45_out, and_46_out, and_47_out, and_48_out, and_49_out, and_50_out, and_51_out, and_52_out, and_53_out, and_54_out);
endmodule

module \控制信号扩展  (
  input  OP0,
  input  OP1,
  input  OP2,
  input  OP3,
  input  OP4,
  input  OP5,
  input  F0,
  input  F1,
  input  F2,
  input  F3,
  input  F4,
  input  F5,
  output SHAMT_SRC,
  output LUI,
  output HLEN,
  output MFLO,
  output MODE1,
  output MODE0,
  output MEM_SIGN_EXT,
  output B_BRANCH1,
  output B_BRANCH0
);

  wire and_1_out, and_2_out, and_3_out, and_5_out, and_6_out, and_8_out, and_9_out, and_10_out, and_11_out,
       and_12_out, and_13_out, and_14_out, and_15_out, and_16_out, and_17_out, and_18_out, and_19_out,
       and_20_out, and_21_out, not_1_out, not_2_out, not_3_out, not_4_out, not_5_out, not_6_out, not_7_out,
       not_8_out, not_9_out, not_10_out, not_11_out, not_12_out, not_13_out, not_14_out, not_15_out,
       not_16_out, not_17_out, not_18_out, not_19_out, not_20_out, not_21_out, not_22_out, not_23_out,
       not_24_out, not_25_out, not_26_out, not_27_out, not_28_out, not_29_out, not_30_out, not_31_out,
       not_32_out, not_33_out, not_34_out, not_35_out, not_36_out, not_37_out, not_38_out, not_39_out,
       not_40_out, not_41_out, not_42_out, not_43_out, not_44_out, not_45_out, not_46_out, not_47_out,
       not_48_out, not_49_out, not_50_out, not_51_out, not_52_out, not_53_out, not_54_out, not_55_out,
       not_56_out, not_57_out, not_58_out, not_59_out, not_60_out, not_61_out, not_62_out, not_63_out,
       not_64_out, not_65_out, not_66_out, not_67_out, not_68_out, not_69_out, not_70_out, not_71_out,
       not_72_out, not_73_out, not_74_out, not_75_out, not_76_out, not_77_out, not_78_out, not_79_out,
       not_80_out, not_81_out, not_82_out, not_83_out, not_84_out, not_85_out, not_86_out, not_87_out,
       not_88_out, not_89_out, not_90_out, not_91_out, not_92_out, not_93_out, not_94_out, not_95_out,
       not_96_out, not_97_out, not_98_out, not_99_out, not_100_out, not_101_out, not_102_out, not_103_out,
       not_104_out, not_105_out, not_106_out, not_107_out, not_108_out, not_109_out, not_110_out,
       not_111_out, not_112_out, not_113_out, not_114_out, not_115_out, not_116_out, not_117_out, not_118_out;

  not not_1 (not_1_out, OP5);
  not not_2 (not_2_out, OP4);
  not not_3 (not_3_out, OP3);
  not not_4 (not_4_out, OP2);
  not not_5 (not_5_out, OP1);
  not not_6 (not_6_out, OP0);
  not not_7 (not_7_out, F5);
  not not_8 (not_8_out, F4);
  not not_9 (not_9_out, F3);
  not not_10 (not_10_out, F1);
  not not_11 (not_11_out, F0);
  not not_12 (not_12_out, OP5);
  not not_13 (not_13_out, OP4);
  not not_14 (not_14_out, OP3);
  not not_15 (not_15_out, OP2);
  not not_16 (not_16_out, OP1);
  not not_17 (not_17_out, OP0);
  not not_18 (not_18_out, F5);
  not not_19 (not_19_out, F4);
  not not_20 (not_20_out, F3);
  not not_21 (not_21_out, F0);
  not not_22 (not_22_out, OP5);
  not not_23 (not_23_out, OP4);
  not not_24 (not_24_out, OP3);
  not not_25 (not_25_out, OP2);
  not not_26 (not_26_out, OP1);
  not not_27 (not_27_out, OP0);
  not not_28 (not_28_out, F5);
  not not_29 (not_29_out, F4);
  not not_30 (not_30_out, F3);
  not not_31 (not_31_out, OP5);
  not not_32 (not_32_out, OP4);
  not not_33 (not_33_out, OP5);
  not not_34 (not_34_out, OP4);
  not not_35 (not_35_out, OP3);
  not not_36 (not_36_out, OP2);
  not not_37 (not_37_out, OP1);
  not not_38 (not_38_out, OP0);
  not not_39 (not_39_out, F5);
  not not_40 (not_40_out, F2);
  not not_41 (not_41_out, F1);
  not not_42 (not_42_out, OP5);
  not not_43 (not_43_out, OP4);
  not not_44 (not_44_out, OP3);
  not not_45 (not_45_out, OP2);
  not not_46 (not_46_out, OP1);
  not not_47 (not_47_out, OP0);
  not not_48 (not_48_out, F5);
  not not_49 (not_49_out, F2);
  not not_50 (not_50_out, OP5);
  not not_51 (not_51_out, OP4);
  not not_52 (not_52_out, OP3);
  not not_53 (not_53_out, OP2);
  not not_54 (not_54_out, OP1);
  not not_55 (not_55_out, OP0);
  not not_56 (not_56_out, F5);
  not not_57 (not_57_out, F3);
  not not_58 (not_58_out, F2);
  not not_59 (not_59_out, F0);
  not not_60 (not_60_out, OP4);
  not not_61 (not_61_out, OP3);
  not not_62 (not_62_out, OP2);
  not not_63 (not_63_out, OP1);
  not not_64 (not_64_out, OP4);
  not not_65 (not_65_out, OP3);
  not not_66 (not_66_out, OP1);
  not not_67 (not_67_out, OP4);
  not not_68 (not_68_out, OP2);
  not not_69 (not_69_out, OP1);
  not not_70 (not_70_out, OP4);
  not not_71 (not_71_out, OP3);
  not not_72 (not_72_out, OP2);
  not not_73 (not_73_out, OP1);
  not not_74 (not_74_out, OP0);
  not not_75 (not_75_out, OP4);
  not not_76 (not_76_out, OP3);
  not not_77 (not_77_out, OP1);
  not not_78 (not_78_out, OP0);
  not not_79 (not_79_out, OP4);
  not not_80 (not_80_out, OP2);
  not not_81 (not_81_out, OP1);
  not not_82 (not_82_out, OP0);
  not not_83 (not_83_out, OP4);
  not not_84 (not_84_out, OP3);
  not not_85 (not_85_out, OP2);
  not not_86 (not_86_out, OP1);
  not not_87 (not_87_out, OP0);
  not not_88 (not_88_out, OP4);
  not not_89 (not_89_out, OP3);
  not not_90 (not_90_out, OP2);
  not not_91 (not_91_out, OP1);
  not not_92 (not_92_out, OP5);
  not not_93 (not_93_out, OP4);
  not not_94 (not_94_out, OP3);
  not not_95 (not_95_out, OP5);
  not not_96 (not_96_out, OP4);
  not not_97 (not_97_out, OP3);
  not not_98 (not_98_out, OP2);
  not not_99 (not_99_out, OP1);
  not not_100 (not_100_out, OP5);
  not not_101 (not_101_out, OP4);
  not not_102 (not_102_out, OP3);
  not not_103 (not_103_out, OP2);
  not not_104 (not_104_out, OP1);
  not not_105 (not_105_out, OP5);
  not not_106 (not_106_out, OP4);
  not not_107 (not_107_out, OP3);
  not not_108 (not_108_out, OP2);
  not not_109 (not_109_out, OP1);
  not not_110 (not_110_out, OP5);
  not not_111 (not_111_out, OP4);
  not not_112 (not_112_out, OP3);
  not not_113 (not_113_out, OP2);
  not not_114 (not_114_out, OP1);
  not not_115 (not_115_out, OP5);
  not not_116 (not_116_out, OP4);
  not not_117 (not_117_out, OP3);
  not not_118 (not_118_out, OP0);
  and and_1 (and_1_out, not_1_out, not_2_out, not_3_out, not_4_out, not_5_out, not_6_out, not_7_out, not_8_out, not_9_out, F2, not_10_out, not_11_out);
  and and_2 (and_2_out, not_12_out, not_13_out, not_14_out, not_15_out, not_16_out, not_17_out, not_18_out, not_19_out, not_20_out, F2, F1, not_21_out);
  and and_3 (and_3_out, not_22_out, not_23_out, not_24_out, not_25_out, not_26_out, not_27_out, not_28_out, not_29_out, not_30_out, F2, F1, F0);
  and and_4 (LUI, not_31_out, not_32_out, OP3, OP2, OP1, OP0);
  and and_5 (and_5_out, not_33_out, not_34_out, not_35_out, not_36_out, not_37_out, not_38_out, not_39_out, F4, F3, not_40_out, not_41_out, F0);
  and and_6 (and_6_out, not_42_out, not_43_out, not_44_out, not_45_out, not_46_out, not_47_out, not_48_out, F4, F3, not_49_out, F1, F0);
  and and_7 (MFLO, not_50_out, not_51_out, not_52_out, not_53_out, not_54_out, not_55_out, not_56_out, F4, not_57_out, not_58_out, F1, not_59_out);
  and and_8 (and_8_out, OP5, not_60_out, not_61_out, not_62_out, not_63_out, OP0);
  and and_9 (and_9_out, OP5, not_64_out, not_65_out, OP2, not_66_out, OP0);
  and and_10 (and_10_out, OP5, not_67_out, OP3, not_68_out, not_69_out, OP0);
  and and_11 (and_11_out, OP5, not_70_out, not_71_out, not_72_out, not_73_out, not_74_out);
  and and_12 (and_12_out, OP5, not_75_out, not_76_out, OP2, not_77_out, not_78_out);
  and and_13 (and_13_out, OP5, not_79_out, OP3, not_80_out, not_81_out, not_82_out);
  and and_14 (and_14_out, OP5, not_83_out, not_84_out, not_85_out, not_86_out, not_87_out);
  and and_15 (and_15_out, OP5, not_88_out, not_89_out, not_90_out, not_91_out, OP0);
  and and_16 (and_16_out, not_92_out, not_93_out, not_94_out, OP2, OP1, OP0);
  and and_17 (and_17_out, not_95_out, not_96_out, not_97_out, not_98_out, not_99_out, OP0);
  and and_18 (and_18_out, not_100_out, not_101_out, not_102_out, not_103_out, not_104_out, OP0);
  and and_19 (and_19_out, not_105_out, not_106_out, not_107_out, not_108_out, not_109_out, OP0);
  and and_20 (and_20_out, not_110_out, not_111_out, not_112_out, not_113_out, not_114_out, OP0);
  and and_21 (and_21_out, not_115_out, not_116_out, not_117_out, OP2, OP1, not_118_out);
  or or_1 (SHAMT_SRC, and_1_out, and_2_out, and_3_out);
  or or_2 (HLEN, and_5_out, and_6_out);
  or or_3 (MODE1, and_8_out, and_9_out, and_10_out);
  or or_4 (MODE0, and_11_out, and_12_out, and_13_out);
  or or_5 (MEM_SIGN_EXT, and_14_out, and_15_out);
  or or_6 (B_BRANCH1, and_16_out, and_17_out, and_18_out);
  or or_7 (B_BRANCH0, and_19_out, and_20_out, and_21_out);
endmodule

// ALU
module MIPS_ALU (
  input  [4:0] shamt,
  input  [31:0] X,
  input  [31:0] Y,
  input  [3:0] AluOP,
  output Equal,
  output [31:0] Result,
  output [31:0] Result_2
);

  wire [0:0] comparator_1_lt, comparator_2_lt;
  wire [31:0] adder_1_out, AND_out, divider_1_out, divider_1_rem, multiplier_1_cout, multiplier_1_out,
       NOR_out, OR_out, shifter_1_out, shifter_2_out, shifter_3_out, subtractor_1_out, XOR_out;

  assign AND_out = X & Y;  // AND_Gate AND, 32 bits wide
  assign OR_out = X | Y;  // OR_Gate OR, 32 bits wide
  Shifter #(.width(32)) shifter_1 (.in(Y), .\dist (shamt), .out(shifter_1_out));
  Shifter #(.width(32), .shift("ar")) shifter_2 (.in(Y), .\dist (shamt), .out(shifter_2_out));
  Shifter #(.width(32), .shift("lr")) shifter_3 (.in(Y), .\dist (shamt), .out(shifter_3_out));
  Multiplier #(.width(32)) multiplier_1 (.a(X), .b(Y), .out(multiplier_1_out), .cout(multiplier_1_cout));  // open: cin
  Divider #(.width(32)) divider_1 (.a(X), .b(Y), .out(divider_1_out), .rem(divider_1_rem));  // open: upper
  Adder #(.width(32)) adder_1 (.a(X), .b(Y), .out(adder_1_out));  // open: cin, cout
  Subtractor #(.width(32)) subtractor_1 (.a(X), .b(Y), .out(subtractor_1_out));  // open: bin, bout
  assign XOR_out = X ^ Y;  // XOR_Gate XOR, 32 bits wide
  assign NOR_out = ~(X | Y);  // NOR_Gate NOR, 32 bits wide
  Comparator #(.width(32)) comparator_1 (.a(X), .b(Y), .eq(Equal), .lt(comparator_1_lt[0]));  // open: gt
  Comparator #(.width(32), .mode("unsigned")) comparator_2 (.a(X), .b(Y), .lt(comparator_2_lt[0]));  // open: gt, eq
  Multiplexer #(.select(4), .width(32), .enable("false")) multiplexer_1 (
    .in0(shifter_1_out), .in1(shifter_2_out), .in2(shifter_3_out), .in3(multiplier_1_out),
    .in4(divider_1_out), .in5(adder_1_out), .in6(subtractor_1_out), .in7(AND_out), .in8(OR_out),
    .in9(XOR_out), .in10(NOR_out), .in11({{31{1'b0}}, comparator_1_lt[0]}),
    .in12({{31{1'b0}}, comparator_2_lt[0]}), .in13({32{1'b0}}), .in14({32{1'b0}}), .in15({32{1'b0}}),
    .out(Result), .sel(AluOP));
  Multiplexer #(.select(4), .width(32), .enable("false")) multiplexer_2 (
    .in0({32{1'b0}}), .in1({32{1'b0}}), .in2({32{1'b0}}), .in3(multiplier_1_cout), .in4(divider_1_rem),
    .in5({32{1'b0}}), .in6({32{1'b0}}), .in7({32{1'b0}}), .in8({32{1'b0}}), .in9({32{1'b0}}),
    .in10({32{1'b0}}), .in11({32{1'b0}}), .in12({32{1'b0}}), .in13({32{1'b0}}), .in14({32{1'b0}}),
    .in15({32{1'b0}}), .out(Result_2), .sel(AluOP));

  // Other names for the same wires on the sheet: Result2[31:0] = Result_2; S[3:0] = AluOP

  // Notes on the sheet:
  //   不要改变此引脚区域内容，也不要改变ALU封装形式
  //   输入引脚
  //   输出引脚
endmodule

module MIPS_Regifile (
  input  [31:0] Din,
  input  Clk,
  input  WE,
  input  [4:0] R1_num,
  input  [4:0] W_num,
  input  [4:0] R2_num,
  output [31:0] R1,
  output [31:0] R2
);

  // RegisterFile registerfile_1: pin names not known; wires that end beside it: Din, Clk, WE, W_num, R1_num, R2_num, R1, R2
endmodule
module \理想流水线  (
);

  wire AluSrcB, AluSrcB_ex, BEQ, BNE, CLK, Go, HLEN, HLEN_ex, IR1, IR2, IR3, J, Jal, Jal_ex, Jal_mem, Jal_wb,
       jr, LUI, LUI_ex, LUI_mem, LUI_wb, MEM_SIGN_EXT, MEM_SIGN_EXT_ex, MEM_SIGN_EXT_mem, MemToReg,
       MemToReg_ex, MemToReg_mem, MemToReg_wb, MemWrite, MemWrite_ex, MemWrite_mem, MFLO, MFLO_ex, MFLO_mem,
       MFLO_wb, or_1_out, or_2_out, pcvalid, RegDst, RegWrite, RegWrite_ex, RegWrite_mem, RegWrite_wb, RST,
       SHAMT_SRC, SHAMT_SRC_ex, SignedExt, syscall, syscall_ex, syscall_mem, syscall_wb, tunnel, W1, W2, W3,
       \流水线跳转语句分支判断_1_发生跳转 ;
  wire [1:0] B_BRANCH, MODE, MODE_ex, MODE_mem;
  wire [3:0] AluOp, AluOp_ex;
  wire [4:0] multiplexer_2_out, multiplexer_3_out, multiplexer_4_out, multiplexer_6_out, multiplexer_11_out,
       W__ex, W__mem, W__wb, W_num;
  wire [5:0] func;
  wire [11:0] EX_PC, ID_PC, IF_PC, MEM_PC, WB_PC;
  wire [15:0] \LoadUse次数 , \总周期数 , \插入气泡数 , \无条件分支数 , \条件分支成功数 ;
  wire [25:6] Imm26;
  wire [31:0] adder_2_out, bit_extender_1_out, bit_extender_2_out, HI, imm_ext, imm_ext_ex, imm_ext_mem,
       imm_ext_sft, imm_ext_sft_ex, imm_ext_sft_mem, imm_ext_sft_wb, IR_ex, IR_mem, IR_wb, LedData, LO_Out,
       LO_Out_mem, LO_Out_wb, LO_R, LO_R_mem, LO_R_wb, Mem_out, Mem_out_wb, multiplexer_1_out,
       multiplexer_8_out, multiplexer_9_out, multiplexer_10_out, multiplexer_12_out, multiplexer_13_out,
       multiplexer_14_out, PC_4, PC_ex, PC_if, PC_mem, PC_out, PC_q, PC_wb, R1_a0, R1_a0_ex, R1_a0_mem,
       R1_a0_wb, R2_v0, R2_v0_ex, R2_v0_mem, R2_v0_wb, RegDin, rom_1_data;
  wire [31:26] IR;

  Button \u_总复位  (.out(RST));
  Button _1 (.out(IR1));
  Button _2 (.out(IR2));
  Button _3 (.out(IR3));
  Button \u_继续运行  (.out(Go));
  LED led_1 (.in(W1));
  LED led_2 (.in(W2));
  LED led_3 (.in(W3));
  Multiplexer #(.width(32), .enable("false")) multiplexer_1 (
    .in0(PC_4), .in1(PC_out), .out(multiplexer_1_out), .sel(\流水线跳转语句分支判断_1_发生跳转 ));
  Register #(.width(32)) PC (.D(multiplexer_1_out), .en(pcvalid), .Q(PC_q), .clk(CLK), .clr(RST));
  Hex_Digit_Display hex_digit_display_1 (.value(LedData[31:28]));  // open: dp
  Adder #(.width(32)) adder_1 (.a(PC_q), .b(32'h4), .out(PC_4));  // open: cin, cout
  Counter #(.width(16), .max('hffff)) counter_1 (
    .count(pcvalid), .Q(\总周期数 ), .clk(CLK), .clr(RST));  // open: load, D, carry
  Hex_Digit_Display hex_digit_display_2 (.value(LedData[23:20]));  // open: dp
  Hex_Digit_Display hex_digit_display_3 (.value(LedData[27:24]));  // open: dp
  Hex_Digit_Display hex_digit_display_4 (.value(LedData[19:16]));  // open: dp
  Hex_Digit_Display hex_digit_display_5 (.value(LedData[15:12]));  // open: dp
  ROM #(.addrWidth(10), .dataWidth(32)) rom_1 (.addr(PC_q[11:2]), .data(rom_1_data));  // open: sel
  Hex_Digit_Display hex_digit_display_6 (.value(LedData[7:4]));  // open: dp
  Hex_Digit_Display hex_digit_display_7 (.value(LedData[11:8]));  // open: dp
  Clock clock_1 (.out(CLK));
  or or_1 (or_1_out, \流水线跳转语句分支判断_1_发生跳转 , RST);
  Hex_Digit_Display hex_digit_display_8 (.value(LedData[3:0]));  // open: dp
  IF_ID if_id_1 (
    .PC_in(PC_q), .IR_in(rom_1_data), .CLK(CLK), .PC_out(PC_if), .IR_out({IR, Imm26, func}),
    .\同步清零_气泡_高电平有效 (or_1_out), .\使能端_低电平有效_stall_高电平有效 (1'b0));
  \流水线跳转语句分支判断  \u_流水线跳转语句分支判断_1  (
    .PC(PC_if), .\_32位指令 ({IR, Imm26, func}), .\跳转信号 ({B_BRANCH, SignedExt, jr, Jal, J, BNE, BEQ}),
    .rs(R1_a0), .rt(R2_v0), .Next_PC(PC_out), .\发生跳转 (\流水线跳转语句分支判断_1_发生跳转 ));
  // Probe on \总周期数 
  // Probe on \无条件分支数 
  // Probe on \条件分支成功数 
  // Probe on \插入气泡数 
  // Probe on \LoadUse次数 
  Multiplexer #(.width(5), .enable("false")) multiplexer_2 (
    .in0(Imm26[25:21]), .in1(5'b00100), .out(multiplexer_2_out), .sel(syscall));
  Multiplexer #(.width(5), .enable("false")) multiplexer_3 (
    .in0(Imm26[20:16]), .in1(5'b00010), .out(multiplexer_3_out), .sel(syscall));
  Multiplexer #(.width(5), .enable("false")) multiplexer_4 (
    .in0(Imm26[20:16]), .in1(Imm26[15:11]), .out(multiplexer_4_out), .sel(RegDst));
  // Probe on IF_PC
  or or_2 (or_2_out, B_BRANCH[1], B_BRANCH[0]);
  Multiplexer #(.width(5), .enable("false")) multiplexer_5 (
    .in0(multiplexer_4_out), .in1({5{1'b1}}), .out(W_num), .sel(Jal));
  assign bit_extender_1_out = {{16{1'b0}}, {Imm26[15:6], func}};  // Bit_Extender bit_extender_1
  assign bit_extender_2_out = {{16{Imm26[15]}}, {Imm26[15:6], func}};  // Bit_Extender bit_extender_2
  // Probe on ID_PC
  Multiplexer #(.width(5), .enable("false")) multiplexer_6 (
    .in0(multiplexer_3_out), .in1({5{1'b0}}), .out(multiplexer_6_out), .sel(or_2_out));
  Multiplexer #(.width(32), .enable("false")) multiplexer_7 (
    .in0(bit_extender_1_out), .in1(bit_extender_2_out), .out(imm_ext), .sel(SignedExt));
  Shifter #(.width(32)) shifter_1 (.in(bit_extender_1_out), .\dist (5'b10000), .out(imm_ext_sft));
  // Probe on MEM_PC
  // Probe on EX_PC
  // Probe on WB_PC
  MIPS_Regifile mips_regifile_1 (
    .Din(RegDin), .Clk(CLK), .R1(R1_a0), .R2(R2_v0), .WE(RegWrite_wb), .W_num(W__wb),
    .R1_num(multiplexer_2_out), .R2_num(multiplexer_6_out));
  Shifter #(.width(32)) shifter_2 (.in(imm_ext), .\dist (5'b00010));  // open: out
  Multiplexer #(.select(2), .width(32), .enable("false")) multiplexer_8 (
    .in1(LO_R), .in2(LO_R_mem), .in3(LO_R), .out(multiplexer_8_out));  // open: in0, sel
  Multiplexer #(.select(2), .width(32), .enable("false")) multiplexer_9 (
    .in1(LO_R), .in2(LO_R_mem), .in3(LO_R), .out(multiplexer_9_out));  // open: in0, sel
  \硬布线控制器  \u_硬布线控制器_1  (
    .Func(func), .OP(IR), .ALU_OP(AluOp), .MemToReg(MemToReg), .MemWrite(MemWrite), .ALU_SRC(AluSrcB),
    .RegWrite(RegWrite), .SysCALL(syscall), .SignedExt(SignedExt), .RegDst(RegDst), .JR(jr), .JMP(J),
    .Beq(BEQ), .JAL(Jal), .Bne(BNE), .SHAMT_SRC(SHAMT_SRC), .LUI(LUI), .HLEN(HLEN), .MFLO(MFLO),
    .MEM_SIGN_EXT(MEM_SIGN_EXT), .B_BRANCH(B_BRANCH), .MODE(MODE));
  ID_EX id_ex_1 (
    .RegWrite_in(RegWrite), .jal_in(Jal), .lui_in(LUI), .mflo_in(MFLO), .MemToReg_in(MemToReg),
    .syscall_in(syscall), .mem_sign_ext_in(MEM_SIGN_EXT), .MemWrite_in(MemWrite), .MODE_in(MODE),
    .shamt_src_in(SHAMT_SRC), .HLEN_in(HLEN), .AluSrcB_in(AluSrcB), .AluOP_in(AluOp),
    .imm_ext_sft_in(imm_ext_sft), .imm_ext_in(imm_ext), .R2_v0_in(R2_v0), .R1_a0_in(R1_a0), .PC_in(PC_if),
    .IR_in({IR, Imm26, func}), .CLK(CLK), .RegWrite_out(RegWrite_ex), .jal_out(Jal_ex), .lui_out(LUI_ex),
    .mflo_out(MFLO_ex), .MemToReg_out(MemToReg_ex), .syscall_out(syscall_ex),
    .mem_sign_ext_out(MEM_SIGN_EXT_ex), .MemWrite_out(MemWrite_ex), .MODE_out(MODE_ex),
    .shamt_src_out(SHAMT_SRC_ex), .HLEN_out(HLEN_ex), .AluSrcB_out(AluSrcB_ex), .AluOP_out(AluOp_ex),
    .imm_ext_sft_out(imm_ext_sft_ex), .imm_ext_out(imm_ext_ex), .R2_v0_out(R2_v0_ex), .R1_a0_out(R1_a0_ex),
    .PC_out(PC_ex), .IR_out(IR_ex), .\同步清零_气泡_高电平有效 (RST), .w__in(W_num), .w__out(W__ex));  // open: 使能端_低电平有效_stall_高电平有效
  // AND_Gate and_1 is placed but not wired
  Multiplexer #(.width(32), .enable("false")) multiplexer_10 (
    .in0(R2_v0_ex), .in1(imm_ext_ex), .out(multiplexer_10_out), .sel(AluSrcB_ex));
  Multiplexer #(.width(5), .enable("false")) multiplexer_11 (
    .in0(IR_ex[10:6]), .in1(R1_a0_ex[4:0]), .out(multiplexer_11_out), .sel(SHAMT_SRC_ex));
  EX_MEM ex_mem_1 (
    .RegWrite_in(RegWrite_ex), .jal_in(Jal_ex), .lui_in(LUI_ex), .mflo_in(MFLO_ex),
    .MemToReg_in(MemToReg_ex), .syscall_in(syscall_ex), .mem_sign_ext_in(MEM_SIGN_EXT_ex),
    .MemWrite_in(MemWrite_ex), .MODE_in(MODE_ex), .alu_r1_lo_in(LO_R), .lo_out_in(LO_Out),
    .imm_ext_sft_in(imm_ext_sft_ex), .imm_ext_in(imm_ext_ex), .R2_v0_in(R2_v0_ex), .R1_a0_in(R1_a0_ex),
    .PC_in(PC_ex), .IR_in(IR_ex), .CLK(CLK), .RegWrite_out(RegWrite_mem), .jal_out(Jal_mem),
    .lui_out(LUI_mem), .mflo_out(MFLO_mem), .MemToReg_out(MemToReg_mem), .syscall_out(syscall_mem),
    .mem_sign_ext_out(MEM_SIGN_EXT_mem), .MemWrite_out(MemWrite_mem), .MODE_out(MODE_mem),
    .alu_r1_lo_out(LO_R_mem), .lo_out_out(LO_Out_mem), .imm_ext_sft_out(imm_ext_sft_mem),
    .imm_ext_out(imm_ext_mem), .R2_v0_out(R2_v0_mem), .R1_a0_out(R1_a0_mem), .PC_out(PC_mem),
    .IR_out(IR_mem), .\同步清零_气泡_高电平有效 (RST), .w__in(W__ex), .w__out(W__mem));  // open: 使能端_低电平有效_stall_高电平有效
  MIPS_ALU mips_alu_1 (
    .X(R1_a0_ex), .Y(multiplexer_10_out), .AluOP(AluOp_ex), .Equal(tunnel), .Result(LO_R), .Result_2(HI),
    .shamt(multiplexer_11_out));
  Register #(.width(32)) register_1 (.D(LO_R), .en(HLEN_ex), .Q(LO_Out), .clk(CLK), .clr(RST));
  Register #(.width(32)) register_2 (.D(HI), .en(HLEN_ex), .clk(CLK), .clr(RST));  // open: Q
  MEM_WB mem_wb_1 (
    .RegWrite_in(RegWrite_mem), .jal_in(Jal_mem), .lui_in(LUI_mem), .mflo_in(MFLO_mem),
    .MemToReg_in(MemToReg_mem), .syscall_in(syscall_mem), .PC_in(PC_mem), .IR_in(IR_mem), .CLK(CLK),
    .RegWrite_out(RegWrite_wb), .jal_out(Jal_wb), .lui_out(LUI_wb), .mflo_out(MFLO_wb),
    .MemToReg_out(MemToReg_wb), .syscall_out(syscall_wb), .PC_out(PC_wb), .IR_out(IR_wb),
    .\同步清零_气泡_高电平有效 (RST), .R2_v0_in(R2_v0_mem), .R2_v0_out(R2_v0_wb), .R1_a0_in(R1_a0_mem),
    .R1_a0_out(R1_a0_wb), .alu_r1_lo_in(LO_R_mem), .alu_r1_lo_out(LO_R_wb), .lo_out_in(LO_Out_mem),
    .lo_out_out(LO_Out_wb), .imm_ext_sft_in(imm_ext_sft_mem), .imm_ext_sft_out(imm_ext_sft_wb),
    .MemOut_in(Mem_out), .MemOut_out(Mem_out_wb), .w__in(W__mem), .w__out(W__wb));  // open: 使能端_低电平有效_stall_高电平有效
  \数据存储器  \u_数据存储器_1  (
    .\字节地址 (LO_R_mem[11:0]), .Din(R2_v0_mem), .DataOut(Mem_out), .CLK(CLK), .WE(MemWrite_mem),
    .Mode(MODE_mem), .clr(RST), .in_3(MEM_SIGN_EXT_mem));
  Multiplexer #(.width(32), .enable("false")) multiplexer_12 (
    .in0(LO_R_wb), .in1(Mem_out_wb), .out(multiplexer_12_out), .sel(MemToReg_wb));
  Adder #(.width(32)) adder_2 (.a(PC_wb), .b(32'h4), .out(adder_2_out));  // open: cin, cout
  Syscall syscall_1 (
    .CLK(CLK), .RST(RST), .syscall(syscall_wb), .go(Go), .a0(R1_a0_wb), .v0(R2_v0_wb), .LedData(LedData),
    .PcValid(pcvalid));
  Multiplexer #(.width(32), .enable("false")) multiplexer_13 (
    .in0(multiplexer_12_out), .in1(adder_2_out), .out(multiplexer_13_out), .sel(Jal_wb));
  Multiplexer #(.width(32), .enable("false")) multiplexer_14 (
    .in0(multiplexer_13_out), .in1(imm_ext_sft_wb), .out(multiplexer_14_out), .sel(LUI_wb));
  Multiplexer #(.width(32), .enable("false")) multiplexer_15 (
    .in0(multiplexer_14_out), .in1(LO_Out_wb), .out(RegDin), .sel(MFLO_wb));

  // Other names for the same wires on the sheet: Imm26[5:0] = func; IR[25:0] = {Imm26, func}; rt[4:0] = Imm26[20:16];
  //   OP[5:0] = IR; rs[31:0] = R1_a0_ex

  // Notes on the sheet:
  //   中断源
  //   中断等待指示
  //   指令存储器
  //   数码管输出
  //   contents of rom_1 (hex, n*v repeats v):
  //   0 20100000 20110000 20120000 20130000 36100000 36310001 36520002 36730003 ae100000 ae110004 ae120008
  //   ae13000c 2002000a 20110000 20120000 20130000 c
  //   指令字
  //   OP
  //   Func
  //   rs
  //   rt
  //   rd
  //   imm
  //   流水调试日志用
  //   JMP
  //   JR
  //   OP
  //   Func
  //   Beq
  //   Bne
  //   MemToReg
  //   MemWrite
  //   AluOP
  //   AluSrcB
  //   RegWrite
  //   JAL
  //   RegDst
  //   Syscall
endmodule

// 源寄存器使用情况
module \源寄存器使用情况  (
  input  OP0,
  input  OP1,
  input  OP2,
  input  OP3,
  input  OP4,
  input  OP5,
  input  F0,
  input  F1,
  input  F2,
  input  F3,
  input  F4,
  input  F5,
  output R1_Used,
  output R2_Used
);

  wire and_1_out, and_2_out, and_3_out, and_4_out, and_5_out, and_6_out, and_7_out, and_8_out, and_9_out,
       and_10_out, and_11_out, and_12_out, and_13_out, and_14_out, and_15_out, and_16_out, and_17_out,
       and_18_out, and_19_out, and_20_out, and_21_out, and_22_out, and_23_out, and_24_out, and_25_out,
       and_26_out, and_27_out, and_28_out, and_29_out, and_30_out, and_31_out, and_32_out, and_33_out,
       and_34_out, and_35_out, and_36_out, and_37_out, and_38_out, and_39_out, and_40_out, and_41_out,
       and_42_out, and_43_out, and_44_out, and_45_out, and_46_out, and_47_out, and_48_out, and_49_out,
       and_50_out, and_51_out, and_52_out, and_53_out, and_54_out, and_55_out, and_56_out, and_57_out,
       and_58_out, and_59_out, and_60_out, and_61_out, and_62_out, not_1_out, not_2_out, not_3_out,
       not_4_out, not_5_out, not_6_out, not_7_out, not_8_out, not_9_out, not_10_out, not_11_out, not_12_out,
       not_13_out, not_14_out, not_15_out, not_16_out, not_17_out, not_18_out, not_19_out, not_20_out,
       not_21_out, not_22_out, not_23_out, not_24_out, not_25_out, not_26_out, not_27_out, not_28_out,
       not_29_out, not_30_out, not_31_out, not_32_out, not_33_out, not_34_out, not_35_out, not_36_out,
       not_37_out, not_38_out, not_39_out, not_40_out, not_41_out, not_42_out, not_43_out, not_44_out,
       not_45_out, not_46_out, not_47_out, not_48_out, not_49_out, not_50_out, not_51_out, not_52_out,
       not_53_out, not_54_out, not_55_out, not_56_out, not_57_out, not_58_out, not_59_out, not_60_out,
       not_61_out, not_62_out, not_63_out, not_64_out, not_65_out, not_66_out, not_67_out, not_68_out,
       not_69_out, not_70_out, not_71_out, not_72_out, not_73_out, not_74_out, not_75_out, not_76_out,
       not_77_out, not_78_out, not_79_out, not_80_out, not_81_out, not_82_out, not_83_out, not_84_out,
       not_85_out, not_86_out, not_87_out, not_88_out, not_89_out, not_90_out, not_91_out, not_92_out,
       not_93_out, not_94_out, not_95_out, not_96_out, not_97_out, not_98_out, not_99_out, not_100_out,
       not_101_out, not_102_out, not_103_out, not_104_out, not_105_out, not_106_out, not_107_out,
       not_108_out, not_109_out, not_110_out, not_111_out, not_112_out, not_113_out, not_114_out,
       not_115_out, not_116_out, not_117_out, not_118_out, not_119_out, not_120_out, not_121_out,
       not_122_out, not_123_out, not_124_out, not_125_out, not_126_out, not_127_out, not_128_out,
       not_129_out, not_130_out, not_131_out, not_132_out, not_133_out, not_134_out, not_135_out,
       not_136_out, not_137_out, not_138_out, not_139_out, not_140_out, not_141_out, not_142_out,
       not_143_out, not_144_out, not_145_out, not_146_out, not_147_out, not_148_out, not_149_out,
       not_150_out, not_151_out, not_152_out, not_153_out, not_154_out, not_155_out, not_156_out,
       not_157_out, not_158_out, not_159_out, not_160_out, not_161_out, not_162_out, not_163_out,
       not_164_out, not_165_out, not_166_out, not_167_out, not_168_out, not_169_out, not_170_out,
       not_171_out, not_172_out, not_173_out, not_174_out, not_175_out, not_176_out, not_177_out,
       not_178_out, not_179_out, not_180_out, not_181_out, not_182_out, not_183_out, not_184_out,
       not_185_out, not_186_out, not_187_out, not_188_out, not_189_out, not_190_out, not_191_out,
       not_192_out, not_193_out, not_194_out, not_195_out, not_196_out, not_197_out, not_198_out,
       not_199_out, not_200_out, not_201_out, not_202_out, not_203_out, not_204_out, not_205_out,
       not_206_out, not_207_out, not_208_out, not_209_out, not_210_out, not_211_out, not_212_out,
       not_213_out, not_214_out, not_215_out, not_216_out, not_217_out, not_218_out, not_219_out,
       not_220_out, not_221_out, not_222_out, not_223_out, not_224_out, not_225_out, not_226_out,
       not_227_out, not_228_out, not_229_out, not_230_out, not_231_out, not_232_out, not_233_out,
       not_234_out, not_235_out, not_236_out, not_237_out, not_238_out, not_239_out, not_240_out,
       not_241_out, not_242_out, not_243_out, not_244_out, not_245_out, not_246_out, not_247_out,
       not_248_out, not_249_out, not_250_out, not_251_out, not_252_out, not_253_out, not_254_out,
       not_255_out, not_256_out, not_257_out, not_258_out, not_259_out, not_260_out, not_261_out,
       not_262_out, not_263_out, not_264_out, not_265_out, not_266_out, not_267_out, not_268_out,
       not_269_out, not_270_out, not_271_out, not_272_out, not_273_out, not_274_out, not_275_out,
       not_276_out, not_277_out, not_278_out, not_279_out, not_280_out, not_281_out, not_282_out,
       not_283_out, not_284_out, not_285_out, not_286_out, not_287_out, not_288_out, not_289_out,
       not_290_out, not_291_out, not_292_out, not_293_out, not_294_out, not_295_out, not_296_out,
       not_297_out, not_298_out, not_299_out, not_300_out, not_301_out, not_302_out, not_303_out,
       not_304_out, not_305_out, not_306_out, not_307_out, not_308_out, not_309_out, not_310_out,
       not_311_out, not_312_out, not_313_out, not_314_out, not_315_out, not_316_out, not_317_out,
       not_318_out, not_319_out, not_320_out, not_321_out, not_322_out, not_323_out, not_324_out,
       not_325_out, not_326_out, not_327_out, not_328_out, not_329_out, not_330_out, not_331_out,
       not_332_out, not_333_out, not_334_out, not_335_out, not_336_out, not_337_out, not_338_out,
       not_339_out, not_340_out, not_341_out, not_342_out, not_343_out, not_344_out, not_345_out,
       not_346_out, not_347_out, not_348_out, not_349_out, not_350_out, not_351_out, not_352_out,
       not_353_out, not_354_out, not_355_out, not_356_out, not_357_out, not_358_out, not_359_out,
       not_360_out, not_361_out, not_362_out, not_363_out, not_364_out, not_365_out, not_366_out,
       not_367_out, not_368_out, not_369_out, not_370_out, not_371_out, not_372_out, not_373_out,
       not_374_out, not_375_out, not_376_out, not_377_out, not_378_out, not_379_out, not_380_out,
       not_381_out, not_382_out, not_383_out, not_384_out, not_385_out, not_386_out, not_387_out,
       not_388_out, not_389_out, not_390_out, not_391_out, not_392_out, not_393_out, not_394_out,
       not_395_out, not_396_out, not_397_out, not_398_out, not_399_out, not_400_out, not_401_out,
       not_402_out, not_403_out, not_404_out, not_405_out, not_406_out, not_407_out, not_408_out,
       not_409_out, not_410_out, not_411_out, not_412_out, not_413_out, not_414_out, not_415_out,
       not_416_out, not_417_out, not_418_out, not_419_out, not_420_out, not_421_out, not_422_out,
       not_423_out, not_424_out, not_425_out, not_426_out, not_427_out, not_428_out, not_429_out,
       not_430_out, not_431_out, not_432_out, not_433_out, not_434_out, not_435_out, not_436_out,
       not_437_out, not_438_out, not_439_out, not_440_out, not_441_out, not_442_out, or_1_out, or_2_out;

  not not_1 (not_1_out, OP5);
  not not_2 (not_2_out, OP4);
  not not_3 (not_3_out, OP3);
  not not_4 (not_4_out, OP2);
  not not_5 (not_5_out, OP1);
  not not_6 (not_6_out, OP0);
  not not_7 (not_7_out, F4);
  not not_8 (not_8_out, F3);
  not not_9 (not_9_out, F2);
  not not_10 (not_10_out, F1);
  not not_11 (not_11_out, F0);
  not not_12 (not_12_out, OP5);
  not not_13 (not_13_out, OP4);
  not not_14 (not_14_out, OP3);
  not not_15 (not_15_out, OP2);
  not not_16 (not_16_out, OP1);
  not not_17 (not_17_out, OP0);
  not not_18 (not_18_out, F4);
  not not_19 (not_19_out, F3);
  not not_20 (not_20_out, F2);
  not not_21 (not_21_out, F1);
  not not_22 (not_22_out, OP5);
  not not_23 (not_23_out, OP4);
  not not_24 (not_24_out, OP3);
  not not_25 (not_25_out, OP2);
  not not_26 (not_26_out, OP1);
  not not_27 (not_27_out, OP0);
  not not_28 (not_28_out, F4);
  not not_29 (not_29_out, F3);
  not not_30 (not_30_out, F2);
  not not_31 (not_31_out, F0);
  not not_32 (not_32_out, OP5);
  not not_33 (not_33_out, OP4);
  not not_34 (not_34_out, OP3);
  not not_35 (not_35_out, OP2);
  not not_36 (not_36_out, OP1);
  not not_37 (not_37_out, OP0);
  not not_38 (not_38_out, F4);
  not not_39 (not_39_out, F3);
  not not_40 (not_40_out, F1);
  not not_41 (not_41_out, F0);
  not not_42 (not_42_out, OP5);
  not not_43 (not_43_out, OP4);
  not not_44 (not_44_out, OP3);
  not not_45 (not_45_out, OP2);
  not not_46 (not_46_out, OP1);
  not not_47 (not_47_out, OP0);
  not not_48 (not_48_out, F4);
  not not_49 (not_49_out, F3);
  not not_50 (not_50_out, F1);
  not not_51 (not_51_out, OP5);
  not not_52 (not_52_out, OP4);
  not not_53 (not_53_out, OP3);
  not not_54 (not_54_out, OP2);
  not not_55 (not_55_out, OP1);
  not not_56 (not_56_out, OP0);
  not not_57 (not_57_out, F4);
  not not_58 (not_58_out, F3);
  not not_59 (not_59_out, OP5);
  not not_60 (not_60_out, OP4);
  not not_61 (not_61_out, OP3);
  not not_62 (not_62_out, OP2);
  not not_63 (not_63_out, OP1);
  not not_64 (not_64_out, OP0);
  not not_65 (not_65_out, F4);
  not not_66 (not_66_out, F2);
  not not_67 (not_67_out, F0);
  not not_68 (not_68_out, OP5);
  not not_69 (not_69_out, OP4);
  not not_70 (not_70_out, OP3);
  not not_71 (not_71_out, OP2);
  not not_72 (not_72_out, OP1);
  not not_73 (not_73_out, OP0);
  not not_74 (not_74_out, F4);
  not not_75 (not_75_out, F2);
  not not_76 (not_76_out, OP5);
  not not_77 (not_77_out, OP4);
  not not_78 (not_78_out, OP3);
  not not_79 (not_79_out, OP2);
  not not_80 (not_80_out, OP1);
  not not_81 (not_81_out, OP0);
  not not_82 (not_82_out, F5);
  not not_83 (not_83_out, F4);
  not not_84 (not_84_out, F2);
  not not_85 (not_85_out, F1);
  not not_86 (not_86_out, F0);
  not not_87 (not_87_out, OP5);
  not not_88 (not_88_out, OP4);
  not not_89 (not_89_out, OP3);
  not not_90 (not_90_out, OP2);
  not not_91 (not_91_out, OP1);
  not not_92 (not_92_out, OP0);
  not not_93 (not_93_out, F5);
  not not_94 (not_94_out, F4);
  not not_95 (not_95_out, F1);
  not not_96 (not_96_out, F0);
  not not_97 (not_97_out, OP5);
  not not_98 (not_98_out, OP4);
  not not_99 (not_99_out, OP3);
  not not_100 (not_100_out, OP1);
  not not_101 (not_101_out, OP0);
  not not_102 (not_102_out, OP5);
  not not_103 (not_103_out, OP4);
  not not_104 (not_104_out, OP3);
  not not_105 (not_105_out, OP1);
  not not_106 (not_106_out, OP5);
  not not_107 (not_107_out, OP4);
  not not_108 (not_108_out, OP2);
  not not_109 (not_109_out, OP1);
  not not_110 (not_110_out, OP0);
  not not_111 (not_111_out, OP5);
  not not_112 (not_112_out, OP4);
  not not_113 (not_113_out, OP1);
  not not_114 (not_114_out, OP0);
  not not_115 (not_115_out, OP5);
  not not_116 (not_116_out, OP4);
  not not_117 (not_117_out, OP2);
  not not_118 (not_118_out, OP1);
  not not_119 (not_119_out, OP5);
  not not_120 (not_120_out, OP4);
  not not_121 (not_121_out, OP2);
  not not_122 (not_122_out, OP0);
  not not_123 (not_123_out, OP5);
  not not_124 (not_124_out, OP4);
  not not_125 (not_125_out, OP1);
  not not_126 (not_126_out, OP4);
  not not_127 (not_127_out, OP3);
  not not_128 (not_128_out, OP2);
  not not_129 (not_129_out, OP4);
  not not_130 (not_130_out, OP2);
  not not_131 (not_131_out, OP5);
  not not_132 (not_132_out, OP4);
  not not_133 (not_133_out, OP3);
  not not_134 (not_134_out, OP2);
  not not_135 (not_135_out, OP1);
  not not_136 (not_136_out, OP0);
  not not_137 (not_137_out, F5);
  not not_138 (not_138_out, F4);
  not not_139 (not_139_out, F3);
  not not_140 (not_140_out, F1);
  not not_141 (not_141_out, F0);
  not not_142 (not_142_out, OP5);
  not not_143 (not_143_out, OP4);
  not not_144 (not_144_out, OP3);
  not not_145 (not_145_out, OP2);
  not not_146 (not_146_out, OP1);
  not not_147 (not_147_out, OP0);
  not not_148 (not_148_out, F5);
  not not_149 (not_149_out, F4);
  not not_150 (not_150_out, F3);
  not not_151 (not_151_out, F0);
  not not_152 (not_152_out, OP5);
  not not_153 (not_153_out, OP4);
  not not_154 (not_154_out, OP3);
  not not_155 (not_155_out, OP2);
  not not_156 (not_156_out, OP1);
  not not_157 (not_157_out, OP0);
  not not_158 (not_158_out, F5);
  not not_159 (not_159_out, F4);
  not not_160 (not_160_out, F3);
  not not_161 (not_161_out, OP5);
  not not_162 (not_162_out, OP4);
  not not_163 (not_163_out, OP3);
  not not_164 (not_164_out, OP2);
  not not_165 (not_165_out, OP1);
  not not_166 (not_166_out, OP0);
  not not_167 (not_167_out, F4);
  not not_168 (not_168_out, F3);
  not not_169 (not_169_out, F2);
  not not_170 (not_170_out, OP5);
  not not_171 (not_171_out, OP4);
  not not_172 (not_172_out, OP3);
  not not_173 (not_173_out, OP2);
  not not_174 (not_174_out, OP1);
  not not_175 (not_175_out, OP0);
  not not_176 (not_176_out, F4);
  not not_177 (not_177_out, F3);
  not not_178 (not_178_out, F0);
  not not_179 (not_179_out, OP5);
  not not_180 (not_180_out, OP4);
  not not_181 (not_181_out, OP0);
  not not_182 (not_182_out, OP5);
  not not_183 (not_183_out, OP4);
  not not_184 (not_184_out, OP2);
  not not_185 (not_185_out, OP5);
  not not_186 (not_186_out, OP4);
  not not_187 (not_187_out, OP3);
  not not_188 (not_188_out, OP2);
  not not_189 (not_189_out, OP1);
  not not_190 (not_190_out, OP0);
  not not_191 (not_191_out, F5);
  not not_192 (not_192_out, F2);
  not not_193 (not_193_out, F1);
  not not_194 (not_194_out, OP5);
  not not_195 (not_195_out, OP4);
  not not_196 (not_196_out, OP3);
  not not_197 (not_197_out, OP2);
  not not_198 (not_198_out, OP1);
  not not_199 (not_199_out, OP0);
  not not_200 (not_200_out, F5);
  not not_201 (not_201_out, F2);
  not not_202 (not_202_out, OP4);
  not not_203 (not_203_out, OP3);
  not not_204 (not_204_out, OP2);
  not not_205 (not_205_out, OP1);
  not not_206 (not_206_out, OP0);
  not not_207 (not_207_out, OP4);
  not not_208 (not_208_out, OP3);
  not not_209 (not_209_out, OP1);
  not not_210 (not_210_out, OP0);
  not not_211 (not_211_out, OP4);
  not not_212 (not_212_out, OP3);
  not not_213 (not_213_out, OP2);
  not not_214 (not_214_out, OP1);
  not not_215 (not_215_out, OP4);
  not not_216 (not_216_out, OP3);
  not not_217 (not_217_out, OP1);
  not not_218 (not_218_out, OP4);
  not not_219 (not_219_out, OP2);
  not not_220 (not_220_out, OP1);
  not not_221 (not_221_out, OP0);
  not not_222 (not_222_out, OP4);
  not not_223 (not_223_out, OP2);
  not not_224 (not_224_out, OP1);
  not not_225 (not_225_out, OP5);
  not not_226 (not_226_out, OP4);
  not not_227 (not_227_out, OP3);
  not not_228 (not_228_out, OP0);
  not not_229 (not_229_out, OP5);
  not not_230 (not_230_out, OP4);
  not not_231 (not_231_out, OP3);
  not not_232 (not_232_out, OP5);
  not not_233 (not_233_out, OP4);
  not not_234 (not_234_out, OP3);
  not not_235 (not_235_out, OP2);
  not not_236 (not_236_out, OP1);
  not not_237 (not_237_out, OP5);
  not not_238 (not_238_out, OP4);
  not not_239 (not_239_out, OP3);
  not not_240 (not_240_out, OP2);
  not not_241 (not_241_out, OP1);
  not not_242 (not_242_out, OP5);
  not not_243 (not_243_out, OP4);
  not not_244 (not_244_out, OP3);
  not not_245 (not_245_out, OP2);
  not not_246 (not_246_out, OP1);
  not not_247 (not_247_out, OP0);
  not not_248 (not_248_out, F5);
  not not_249 (not_249_out, F4);
  not not_250 (not_250_out, F3);
  not not_251 (not_251_out, F2);
  not not_252 (not_252_out, F1);
  not not_253 (not_253_out, F0);
  not not_254 (not_254_out, OP5);
  not not_255 (not_255_out, OP4);
  not not_256 (not_256_out, OP3);
  not not_257 (not_257_out, OP2);
  not not_258 (not_258_out, OP1);
  not not_259 (not_259_out, OP0);
  not not_260 (not_260_out, F5);
  not not_261 (not_261_out, F4);
  not not_262 (not_262_out, F3);
  not not_263 (not_263_out, F2);
  not not_264 (not_264_out, OP5);
  not not_265 (not_265_out, OP4);
  not not_266 (not_266_out, OP3);
  not not_267 (not_267_out, OP2);
  not not_268 (not_268_out, OP1);
  not not_269 (not_269_out, OP0);
  not not_270 (not_270_out, F5);
  not not_271 (not_271_out, F4);
  not not_272 (not_272_out, F3);
  not not_273 (not_273_out, F2);
  not not_274 (not_274_out, F0);
  not not_275 (not_275_out, OP5);
  not not_276 (not_276_out, OP4);
  not not_277 (not_277_out, OP3);
  not not_278 (not_278_out, OP2);
  not not_279 (not_279_out, OP1);
  not not_280 (not_280_out, OP0);
  not not_281 (not_281_out, F4);
  not not_282 (not_282_out, F3);
  not not_283 (not_283_out, F2);
  not not_284 (not_284_out, F1);
  not not_285 (not_285_out, F0);
  not not_286 (not_286_out, OP5);
  not not_287 (not_287_out, OP4);
  not not_288 (not_288_out, OP3);
  not not_289 (not_289_out, OP2);
  not not_290 (not_290_out, OP1);
  not not_291 (not_291_out, OP0);
  not not_292 (not_292_out, F4);
  not not_293 (not_293_out, F3);
  not not_294 (not_294_out, F2);
  not not_295 (not_295_out, F1);
  not not_296 (not_296_out, OP5);
  not not_297 (not_297_out, OP4);
  not not_298 (not_298_out, OP3);
  not not_299 (not_299_out, OP2);
  not not_300 (not_300_out, OP1);
  not not_301 (not_301_out, OP0);
  not not_302 (not_302_out, F4);
  not not_303 (not_303_out, F3);
  not not_304 (not_304_out, F2);
  not not_305 (not_305_out, F0);
  not not_306 (not_306_out, OP5);
  not not_307 (not_307_out, OP4);
  not not_308 (not_308_out, OP3);
  not not_309 (not_309_out, OP2);
  not not_310 (not_310_out, OP1);
  not not_311 (not_311_out, OP0);
  not not_312 (not_312_out, F4);
  not not_313 (not_313_out, F3);
  not not_314 (not_314_out, F1);
  not not_315 (not_315_out, F0);
  not not_316 (not_316_out, OP5);
  not not_317 (not_317_out, OP4);
  not not_318 (not_318_out, OP3);
  not not_319 (not_319_out, OP2);
  not not_320 (not_320_out, OP1);
  not not_321 (not_321_out, OP0);
  not not_322 (not_322_out, F4);
  not not_323 (not_323_out, F3);
  not not_324 (not_324_out, F1);
  not not_325 (not_325_out, OP5);
  not not_326 (not_326_out, OP4);
  not not_327 (not_327_out, OP3);
  not not_328 (not_328_out, OP2);
  not not_329 (not_329_out, OP1);
  not not_330 (not_330_out, OP0);
  not not_331 (not_331_out, F4);
  not not_332 (not_332_out, F3);
  not not_333 (not_333_out, OP5);
  not not_334 (not_334_out, OP4);
  not not_335 (not_335_out, OP3);
  not not_336 (not_336_out, OP2);
  not not_337 (not_337_out, OP1);
  not not_338 (not_338_out, OP0);
  not not_339 (not_339_out, F4);
  not not_340 (not_340_out, F2);
  not not_341 (not_341_out, F0);
  not not_342 (not_342_out, OP5);
  not not_343 (not_343_out, OP4);
  not not_344 (not_344_out, OP3);
  not not_345 (not_345_out, OP2);
  not not_346 (not_346_out, OP1);
  not not_347 (not_347_out, OP0);
  not not_348 (not_348_out, F4);
  not not_349 (not_349_out, F2);
  not not_350 (not_350_out, OP5);
  not not_351 (not_351_out, OP4);
  not not_352 (not_352_out, OP3);
  not not_353 (not_353_out, OP2);
  not not_354 (not_354_out, OP1);
  not not_355 (not_355_out, OP0);
  not not_356 (not_356_out, F5);
  not not_357 (not_357_out, F4);
  not not_358 (not_358_out, F1);
  not not_359 (not_359_out, F0);
  not not_360 (not_360_out, OP5);
  not not_361 (not_361_out, OP4);
  not not_362 (not_362_out, OP3);
  not not_363 (not_363_out, OP1);
  not not_364 (not_364_out, OP0);
  not not_365 (not_365_out, OP5);
  not not_366 (not_366_out, OP4);
  not not_367 (not_367_out, OP3);
  not not_368 (not_368_out, OP1);
  not not_369 (not_369_out, OP4);
  not not_370 (not_370_out, OP2);
  not not_371 (not_371_out, OP5);
  not not_372 (not_372_out, OP4);
  not not_373 (not_373_out, OP3);
  not not_374 (not_374_out, OP2);
  not not_375 (not_375_out, OP1);
  not not_376 (not_376_out, OP0);
  not not_377 (not_377_out, F5);
  not not_378 (not_378_out, F4);
  not not_379 (not_379_out, F3);
  not not_380 (not_380_out, F1);
  not not_381 (not_381_out, F0);
  not not_382 (not_382_out, OP5);
  not not_383 (not_383_out, OP4);
  not not_384 (not_384_out, OP3);
  not not_385 (not_385_out, OP2);
  not not_386 (not_386_out, OP1);
  not not_387 (not_387_out, OP0);
  not not_388 (not_388_out, F5);
  not not_389 (not_389_out, F4);
  not not_390 (not_390_out, F3);
  not not_391 (not_391_out, F0);
  not not_392 (not_392_out, OP5);
  not not_393 (not_393_out, OP4);
  not not_394 (not_394_out, OP3);
  not not_395 (not_395_out, OP2);
  not not_396 (not_396_out, OP1);
  not not_397 (not_397_out, OP0);
  not not_398 (not_398_out, F5);
  not not_399 (not_399_out, F4);
  not not_400 (not_400_out, F3);
  not not_401 (not_401_out, OP5);
  not not_402 (not_402_out, OP4);
  not not_403 (not_403_out, OP3);
  not not_404 (not_404_out, OP2);
  not not_405 (not_405_out, OP1);
  not not_406 (not_406_out, OP0);
  not not_407 (not_407_out, F4);
  not not_408 (not_408_out, F3);
  not not_409 (not_409_out, F2);
  not not_410 (not_410_out, OP5);
  not not_411 (not_411_out, OP4);
  not not_412 (not_412_out, OP3);
  not not_413 (not_413_out, OP2);
  not not_414 (not_414_out, OP1);
  not not_415 (not_415_out, OP0);
  not not_416 (not_416_out, F4);
  not not_417 (not_417_out, F3);
  not not_418 (not_418_out, F0);
  not not_419 (not_419_out, OP5);
  not not_420 (not_420_out, OP4);
  not not_421 (not_421_out, OP3);
  not not_422 (not_422_out, OP2);
  not not_423 (not_423_out, OP1);
  not not_424 (not_424_out, OP0);
  not not_425 (not_425_out, F5);
  not not_426 (not_426_out, F2);
  not not_427 (not_427_out, F1);
  not not_428 (not_428_out, OP5);
  not not_429 (not_429_out, OP4);
  not not_430 (not_430_out, OP3);
  not not_431 (not_431_out, OP2);
  not not_432 (not_432_out, OP1);
  not not_433 (not_433_out, OP0);
  not not_434 (not_434_out, F5);
  not not_435 (not_435_out, F2);
  not not_436 (not_436_out, OP4);
  not not_437 (not_437_out, OP2);
  not not_438 (not_438_out, OP1);
  not not_439 (not_439_out, OP0);
  not not_440 (not_440_out, OP4);
  not not_441 (not_441_out, OP2);
  not not_442 (not_442_out, OP1);
  and and_1 (and_1_out, not_1_out, not_2_out, not_3_out, not_4_out, not_5_out, not_6_out, F5, not_7_out, not_8_out, not_9_out, not_10_out, not_11_out);
  and and_2 (and_2_out, not_12_out, not_13_out, not_14_out, not_15_out, not_16_out, not_17_out, F5, not_18_out, not_19_out, not_20_out, not_21_out, F0);
  and and_3 (and_3_out, not_22_out, not_23_out, not_24_out, not_25_out, not_26_out, not_27_out, F5, not_28_out, not_29_out, not_30_out, F1, not_31_out);
  and and_4 (and_4_out, not_32_out, not_33_out, not_34_out, not_35_out, not_36_out, not_37_out, F5, not_38_out, not_39_out, F2, not_40_out, not_41_out);
  and and_5 (and_5_out, not_42_out, not_43_out, not_44_out, not_45_out, not_46_out, not_47_out, F5, not_48_out, not_49_out, F2, not_50_out, F0);
  and and_6 (and_6_out, not_51_out, not_52_out, not_53_out, not_54_out, not_55_out, not_56_out, F5, not_57_out, not_58_out, F2, F1, F0);
  and and_7 (and_7_out, not_59_out, not_60_out, not_61_out, not_62_out, not_63_out, not_64_out, F5, not_65_out, F3, not_66_out, F1, not_67_out);
  and and_8 (and_8_out, not_68_out, not_69_out, not_70_out, not_71_out, not_72_out, not_73_out, F5, not_74_out, F3, not_75_out, F1, F0);
  and and_9 (and_9_out, not_76_out, not_77_out, not_78_out, not_79_out, not_80_out, not_81_out, not_82_out, not_83_out, F3, not_84_out, not_85_out, not_86_out);
  and and_10 (and_10_out, not_87_out, not_88_out, not_89_out, not_90_out, not_91_out, not_92_out, not_93_out, not_94_out, F3, F2, not_95_out, not_96_out);
  and and_11 (and_11_out, not_97_out, not_98_out, not_99_out, OP2, not_100_out, not_101_out);
  and and_12 (and_12_out, not_102_out, not_103_out, not_104_out, OP2, not_105_out, OP0);
  and and_13 (and_13_out, not_106_out, not_107_out, OP3, not_108_out, not_109_out, not_110_out);
  and and_14 (and_14_out, not_111_out, not_112_out, OP3, OP2, not_113_out, not_114_out);
  and and_15 (and_15_out, not_115_out, not_116_out, OP3, not_117_out, not_118_out, OP0);
  and and_16 (and_16_out, not_119_out, not_120_out, OP3, not_121_out, OP1, not_122_out);
  and and_17 (and_17_out, not_123_out, not_124_out, OP3, OP2, not_125_out, OP0);
  and and_18 (and_18_out, OP5, not_126_out, not_127_out, not_128_out, OP1, OP0);
  and and_19 (and_19_out, OP5, not_129_out, OP3, not_130_out, OP1, OP0);
  and and_20 (and_20_out, not_131_out, not_132_out, not_133_out, not_134_out, not_135_out, not_136_out, not_137_out, not_138_out, not_139_out, F2, not_140_out, not_141_out);
  and and_21 (and_21_out, not_142_out, not_143_out, not_144_out, not_145_out, not_146_out, not_147_out, not_148_out, not_149_out, not_150_out, F2, F1, not_151_out);
  and and_22 (and_22_out, not_152_out, not_153_out, not_154_out, not_155_out, not_156_out, not_157_out, not_158_out, not_159_out, not_160_out, F2, F1, F0);
  and and_23 (and_23_out, not_161_out, not_162_out, not_163_out, not_164_out, not_165_out, not_166_out, F5, not_167_out, not_168_out, not_169_out, F1, F0);
  and and_24 (and_24_out, not_170_out, not_171_out, not_172_out, not_173_out, not_174_out, not_175_out, F5, not_176_out, not_177_out, F2, F1, not_178_out);
  and and_25 (and_25_out, not_179_out, not_180_out, OP3, OP2, OP1, not_181_out);
  and and_26 (and_26_out, not_182_out, not_183_out, OP3, not_184_out, OP1, OP0);
  and and_27 (and_27_out, not_185_out, not_186_out, not_187_out, not_188_out, not_189_out, not_190_out, not_191_out, F4, F3, not_192_out, not_193_out, F0);
  and and_28 (and_28_out, not_194_out, not_195_out, not_196_out, not_197_out, not_198_out, not_199_out, not_200_out, F4, F3, not_201_out, F1, F0);
  and and_29 (and_29_out, OP5, not_202_out, not_203_out, not_204_out, not_205_out, not_206_out);
  and and_30 (and_30_out, OP5, not_207_out, not_208_out, OP2, not_209_out, not_210_out);
  and and_31 (and_31_out, OP5, not_211_out, not_212_out, not_213_out, not_214_out, OP0);
  and and_32 (and_32_out, OP5, not_215_out, not_216_out, OP2, not_217_out, OP0);
  and and_33 (and_33_out, OP5, not_218_out, OP3, not_219_out, not_220_out, not_221_out);
  and and_34 (and_34_out, OP5, not_222_out, OP3, not_223_out, not_224_out, OP0);
  and and_35 (and_35_out, not_225_out, not_226_out, not_227_out, OP2, OP1, not_228_out);
  and and_36 (and_36_out, not_229_out, not_230_out, not_231_out, OP2, OP1, OP0);
  and and_37 (and_37_out, not_232_out, not_233_out, not_234_out, not_235_out, not_236_out, OP0);
  and and_38 (and_38_out, not_237_out, not_238_out, not_239_out, not_240_out, not_241_out, OP0);
  and and_39 (and_39_out, not_242_out, not_243_out, not_244_out, not_245_out, not_246_out, not_247_out, not_248_out, not_249_out, not_250_out, not_251_out, not_252_out, not_253_out);
  and and_40 (and_40_out, not_254_out, not_255_out, not_256_out, not_257_out, not_258_out, not_259_out, not_260_out, not_261_out, not_262_out, not_263_out, F1, F0);
  and and_41 (and_41_out, not_264_out, not_265_out, not_266_out, not_267_out, not_268_out, not_269_out, not_270_out, not_271_out, not_272_out, not_273_out, F1, not_274_out);
  and and_42 (and_42_out, not_275_out, not_276_out, not_277_out, not_278_out, not_279_out, not_280_out, F5, not_281_out, not_282_out, not_283_out, not_284_out, not_285_out);
  and and_43 (and_43_out, not_286_out, not_287_out, not_288_out, not_289_out, not_290_out, not_291_out, F5, not_292_out, not_293_out, not_294_out, not_295_out, F0);
  and and_44 (and_44_out, not_296_out, not_297_out, not_298_out, not_299_out, not_300_out, not_301_out, F5, not_302_out, not_303_out, not_304_out, F1, not_305_out);
  and and_45 (and_45_out, not_306_out, not_307_out, not_308_out, not_309_out, not_310_out, not_311_out, F5, not_312_out, not_313_out, F2, not_314_out, not_315_out);
  and and_46 (and_46_out, not_316_out, not_317_out, not_318_out, not_319_out, not_320_out, not_321_out, F5, not_322_out, not_323_out, F2, not_324_out, F0);
  and and_47 (and_47_out, not_325_out, not_326_out, not_327_out, not_328_out, not_329_out, not_330_out, F5, not_331_out, not_332_out, F2, F1, F0);
  and and_48 (and_48_out, not_333_out, not_334_out, not_335_out, not_336_out, not_337_out, not_338_out, F5, not_339_out, F3, not_340_out, F1, not_341_out);
  and and_49 (and_49_out, not_342_out, not_343_out, not_344_out, not_345_out, not_346_out, not_347_out, F5, not_348_out, F3, not_349_out, F1, F0);
  and and_50 (and_50_out, not_350_out, not_351_out, not_352_out, not_353_out, not_354_out, not_355_out, not_356_out, not_357_out, F3, F2, not_358_out, not_359_out);
  and and_51 (and_51_out, not_360_out, not_361_out, not_362_out, OP2, not_363_out, not_364_out);
  and and_52 (and_52_out, not_365_out, not_366_out, not_367_out, OP2, not_368_out, OP0);
  and and_53 (and_53_out, OP5, not_369_out, OP3, not_370_out, OP1, OP0);
  and and_54 (and_54_out, not_371_out, not_372_out, not_373_out, not_374_out, not_375_out, not_376_out, not_377_out, not_378_out, not_379_out, F2, not_380_out, not_381_out);
  and and_55 (and_55_out, not_382_out, not_383_out, not_384_out, not_385_out, not_386_out, not_387_out, not_388_out, not_389_out, not_390_out, F2, F1, not_391_out);
  and and_56 (and_56_out, not_392_out, not_393_out, not_394_out, not_395_out, not_396_out, not_397_out, not_398_out, not_399_out, not_400_out, F2, F1, F0);
  and and_57 (and_57_out, not_401_out, not_402_out, not_403_out, not_404_out, not_405_out, not_406_out, F5, not_407_out, not_408_out, not_409_out, F1, F0);
  and and_58 (and_58_out, not_410_out, not_411_out, not_412_out, not_413_out, not_414_out, not_415_out, F5, not_416_out, not_417_out, F2, F1, not_418_out);
  and and_59 (and_59_out, not_419_out, not_420_out, not_421_out, not_422_out, not_423_out, not_424_out, not_425_out, F4, F3, not_426_out, not_427_out, F0);
  and and_60 (and_60_out, not_428_out, not_429_out, not_430_out, not_431_out, not_432_out, not_433_out, not_434_out, F4, F3, not_435_out, F1, F0);
  and and_61 (and_61_out, OP5, not_436_out, OP3, not_437_out, not_438_out, not_439_out);
  and and_62 (and_62_out, OP5, not_440_out, OP3, not_441_out, not_442_out, OP0);
  or or_1 (or_1_out, and_1_out, and_2_out, and_3_out, and_4_out, and_5_out, and_6_out, and_7_out, and_8_out, and_9_out, and_10_out, and_11_out, and_12_out, and_13_out, and_14_out, and_15_out, and_16_out, and_17_out, and_18_out, and_19_out);
  or or_2 (or_2_out, and_20_out, and_21_out, and_22_out, and_23_out, and_24_out, and_25_out, and_26_out, and_27_out, and_28_out, and_29_out, and_30_out, and_31_out, and_32_out, and_33_out, and_34_out, and_35_out, and_36_out, and_37_out, and_38_out);
  or or_3 (R2_Used, and_39_out, and_40_out, and_41_out, and_42_out, and_43_out, and_44_out, and_45_out, and_46_out, and_47_out, and_48_out, and_49_out, and_50_out, and_51_out, and_52_out, and_53_out, and_54_out, and_55_out, and_56_out, and_57_out, and_58_out, and_59_out, and_60_out, and_61_out, and_62_out);
  or or_4 (R1_Used, or_1_out, or_2_out);
endmodule

module \数据相关检测  (
  input  [5:0] OP,
  input  EX_RegWrite,
  input  [4:0] EX_W_num,
  input  MEM_RegWrite,
  input  [5:0] Func,
  input  [4:0] Mem_W_num,
  input  [4:0] ID_R1_num,
  input  [4:0] ID_R2_num,
  input  MEM_MemToReg,
  input  EX_MemToReg,
  output Load_Use,
  output [1:0] R2_forward,
  output [1:0] R1_forward
);

  wire and_1_out, and_2_out, and_3_out, and_4_out, and_9_out, and_10_out, and_11_out, comparator_1_eq,
       comparator_2_eq, comparator_3_eq, comparator_4_eq, comparator_5_eq, comparator_6_eq, not_1_out,
       not_2_out, or_2_out, or_3_out, or_5_out, R1_used, R2_used, \数据相关 ;

  \源寄存器使用情况  \u_源寄存器使用情况_1  (
    .OP0(OP[0]), .OP1(OP[1]), .OP2(OP[2]), .OP3(OP[3]), .OP4(OP[4]), .OP5(OP[5]), .F0(Func[0]), .F1(Func[1]),
    .F2(Func[2]), .F3(Func[3]), .F4(Func[4]), .F5(Func[5]), .R1_Used(R1_used), .R2_Used(R2_used));
  and and_1 (and_1_out, EX_RegWrite, R2_used);
  and and_2 (and_2_out, MEM_RegWrite, R2_used);
  and and_3 (and_3_out, EX_RegWrite, R1_used);
  and and_4 (and_4_out, MEM_RegWrite, R1_used);
  not not_1 (not_1_out, comparator_1_eq);
  Comparator #(.width(5)) comparator_1 (.a({5{1'b0}}), .b(ID_R1_num), .eq(comparator_1_eq));  // open: gt, lt
  Comparator #(.width(5)) comparator_2 (.a(Mem_W_num), .b(ID_R1_num), .eq(comparator_2_eq));  // open: gt, lt
  Comparator #(.width(5)) comparator_3 (.a(ID_R1_num), .b(EX_W_num), .eq(comparator_3_eq));  // open: gt, lt
  Comparator #(.width(5)) comparator_4 (.a(EX_W_num), .b(ID_R2_num), .eq(comparator_4_eq));  // open: gt, lt
  Comparator #(.width(5)) comparator_5 (.a(Mem_W_num), .b(ID_R2_num), .eq(comparator_5_eq));  // open: gt, lt
  not not_2 (not_2_out, comparator_6_eq);
  Comparator #(.width(5)) comparator_6 (.a(ID_R2_num), .b({5{1'b0}}), .eq(comparator_6_eq));  // open: gt, lt
  and and_5 (R1_forward[0], and_3_out, not_1_out, comparator_3_eq);
  and and_6 (R1_forward[1], and_4_out, not_1_out, comparator_2_eq);
  and and_7 (R2_forward[0], and_1_out, not_2_out, comparator_4_eq);
  and and_8 (R2_forward[1], and_2_out, not_2_out, comparator_5_eq);
  or or_1 (\数据相关 , R1_forward[0], R1_forward[1], R2_forward[0], R2_forward[1]);
  or or_2 (or_2_out, R2_forward[0], R1_forward[0]);
  or or_3 (or_3_out, R2_forward[1], R1_forward[1]);
  and and_9 (and_9_out, EX_MemToReg, or_2_out);
  or or_4 (Load_Use, and_9_out, and_10_out);
  and and_10 (and_10_out, or_3_out, MEM_MemToReg);
  or or_5 (or_5_out, MEM_MemToReg, EX_MemToReg);
  and and_11 (and_11_out, \数据相关 , or_5_out);

  // Other names for the same wires on the sheet: OP_CODE[5:0] = OP
endmodule

// IF/ID
module IF_ID (
  input  [31:0] PC_in,
  input  [31:0] IR_in,
  input  CLK,
  input  \同步清零_气泡_高电平有效 ,
  input  \使能端_低电平有效_stall_高电平有效 ,
  output [31:0] PC_out,
  output [31:0] IR_out
);

  wire not_1_out;
  wire [31:0] multiplexer_1_out, multiplexer_2_out;

  Multiplexer #(.width(32), .enable("false")) multiplexer_1 (
    .in0(PC_in), .in1({32{1'b0}}), .out(multiplexer_1_out), .sel(\同步清零_气泡_高电平有效 ));
  Multiplexer #(.width(32), .enable("false")) multiplexer_2 (
    .in0(IR_in), .in1({32{1'b0}}), .out(multiplexer_2_out), .sel(\同步清零_气泡_高电平有效 ));
  Register #(.width(32)) register_1 (.D(multiplexer_1_out), .en(not_1_out), .Q(PC_out), .clk(CLK));  // open: clr
  Register #(.width(32)) register_2 (.D(multiplexer_2_out), .en(not_1_out), .Q(IR_out), .clk(CLK));  // open: clr
  not not_1 (not_1_out, \使能端_低电平有效_stall_高电平有效 );
endmodule

// ID/EX
module ID_EX (
  input  RegWrite_in,
  input  jal_in,
  input  lui_in,
  input  mflo_in,
  input  MemToReg_in,
  input  syscall_in,
  input  mem_sign_ext_in,
  input  MemWrite_in,
  input  [1:0] MODE_in,
  input  shamt_src_in,
  input  HLEN_in,
  input  AluSrcB_in,
  input  [3:0] AluOP_in,
  input  [4:0] w__in,
  input  [31:0] imm_ext_sft_in,
  input  [31:0] imm_ext_in,
  input  [31:0] R2_v0_in,
  input  [31:0] R1_a0_in,
  input  [31:0] PC_in,
  input  [31:0] IR_in,
  input  CLK,
  input  \同步清零_气泡_高电平有效 ,
  input  \使能端_低电平有效_stall_高电平有效 ,
  output RegWrite_out,
  output jal_out,
  output lui_out,
  output mflo_out,
  output MemToReg_out,
  output syscall_out,
  output mem_sign_ext_out,
  output MemWrite_out,
  output [1:0] MODE_out,
  output shamt_src_out,
  output HLEN_out,
  output AluSrcB_out,
  output [3:0] AluOP_out,
  output [4:0] w__out,
  output [31:0] imm_ext_sft_out,
  output [31:0] imm_ext_out,
  output [31:0] R2_v0_out,
  output [31:0] R1_a0_out,
  output [31:0] PC_out,
  output [31:0] IR_out
);

  wire not_1_out;
  wire [1:0] multiplexer_2_out, multiplexer_3_out;
  wire [2:0] multiplexer_4_out;
  wire [3:0] multiplexer_5_out;
  wire [4:0] multiplexer_6_out;
  wire [5:0] multiplexer_1_out;
  wire [31:0] multiplexer_7_out, multiplexer_8_out, multiplexer_9_out, multiplexer_10_out,
       multiplexer_11_out, multiplexer_12_out;

  Multiplexer #(.width(6), .enable("false")) multiplexer_1 (
    .in0({syscall_in, MemToReg_in, mflo_in, lui_in, jal_in, RegWrite_in}), .in1({6{1'b0}}),
    .out(multiplexer_1_out), .sel(\同步清零_气泡_高电平有效 ));
  Multiplexer #(.width(2), .enable("false")) multiplexer_2 (
    .in0({MemWrite_in, mem_sign_ext_in}), .in1(2'b00), .out(multiplexer_2_out), .sel(\同步清零_气泡_高电平有效 ));
  Multiplexer #(.width(2), .enable("false")) multiplexer_3 (
    .in0(MODE_in), .in1(2'b00), .out(multiplexer_3_out), .sel(\同步清零_气泡_高电平有效 ));
  Multiplexer #(.width(3), .enable("false")) multiplexer_4 (
    .in0({AluSrcB_in, HLEN_in, shamt_src_in}), .in1(3'b000), .out(multiplexer_4_out), .sel(\同步清零_气泡_高电平有效 ));
  Multiplexer #(.width(4), .enable("false")) multiplexer_5 (
    .in0(AluOP_in), .in1(4'b0000), .out(multiplexer_5_out), .sel(\同步清零_气泡_高电平有效 ));
  Multiplexer #(.width(5), .enable("false")) multiplexer_6 (
    .in0(w__in), .in1({5{1'b0}}), .out(multiplexer_6_out), .sel(\同步清零_气泡_高电平有效 ));
  Multiplexer #(.width(32), .enable("false")) multiplexer_7 (
    .in0(imm_ext_sft_in), .in1({32{1'b0}}), .out(multiplexer_7_out), .sel(\同步清零_气泡_高电平有效 ));
  Multiplexer #(.width(32), .enable("false")) multiplexer_8 (
    .in0(imm_ext_in), .in1({32{1'b0}}), .out(multiplexer_8_out), .sel(\同步清零_气泡_高电平有效 ));
  Multiplexer #(.width(32), .enable("false")) multiplexer_9 (
    .in0(R2_v0_in), .in1({32{1'b0}}), .out(multiplexer_9_out), .sel(\同步清零_气泡_高电平有效 ));
  Multiplexer #(.width(32), .enable("false")) multiplexer_10 (
    .in0(R1_a0_in), .in1({32{1'b0}}), .out(multiplexer_10_out), .sel(\同步清零_气泡_高电平有效 ));
  Multiplexer #(.width(32), .enable("false")) multiplexer_11 (
    .in0(PC_in), .in1({32{1'b0}}), .out(multiplexer_11_out), .sel(\同步清零_气泡_高电平有效 ));
  Multiplexer #(.width(32), .enable("false")) multiplexer_12 (
    .in0(IR_in), .in1({32{1'b0}}), .out(multiplexer_12_out), .sel(\同步清零_气泡_高电平有效 ));
  not not_1 (not_1_out, \使能端_低电平有效_stall_高电平有效 );
  Register #(.width(6)) register_1 (
    .D(multiplexer_1_out), .en(not_1_out),
    .Q({syscall_out, MemToReg_out, mflo_out, lui_out, jal_out, RegWrite_out}), .clk(CLK));  // open: clr
  Register #(.width(2)) register_2 (
    .D(multiplexer_2_out), .en(not_1_out), .Q({MemWrite_out, mem_sign_ext_out}), .clk(CLK));  // open: clr
  Register #(.width(2)) register_3 (.D(multiplexer_3_out), .en(not_1_out), .Q(MODE_out), .clk(CLK));  // open: clr
  Register #(.width(3)) register_4 (
    .D(multiplexer_4_out), .en(not_1_out), .Q({AluSrcB_out, HLEN_out, shamt_src_out}), .clk(CLK));  // open: clr
  Register #(.width(4)) register_5 (.D(multiplexer_5_out), .en(not_1_out), .Q(AluOP_out), .clk(CLK));  // open: clr
  Register #(.width(5)) register_6 (.D(multiplexer_6_out), .en(not_1_out), .Q(w__out), .clk(CLK));  // open: clr
  Register #(.width(32)) register_7 (
    .D(multiplexer_7_out), .en(not_1_out), .Q(imm_ext_sft_out), .clk(CLK));  // open: clr
  Register #(.width(32)) register_8 (.D(multiplexer_8_out), .en(not_1_out), .Q(imm_ext_out), .clk(CLK));  // open: clr
  Register #(.width(32)) register_9 (.D(multiplexer_9_out), .en(not_1_out), .Q(R2_v0_out), .clk(CLK));  // open: clr
  Register #(.width(32)) register_10 (.D(multiplexer_10_out), .en(not_1_out), .Q(R1_a0_out), .clk(CLK));  // open: clr
  Register #(.width(32)) register_11 (.D(multiplexer_11_out), .en(not_1_out), .Q(PC_out), .clk(CLK));  // open: clr
  Register #(.width(32)) register_12 (.D(multiplexer_12_out), .en(not_1_out), .Q(IR_out), .clk(CLK));  // open: clr
endmodule

// EX/MEM
module EX_MEM (
  input  RegWrite_in,
  input  jal_in,
  input  lui_in,
  input  mflo_in,
  input  MemToReg_in,
  input  syscall_in,
  input  mem_sign_ext_in,
  input  MemWrite_in,
  input  [1:0] MODE_in,
  input  [4:0] w__in,
  input  [31:0] alu_r1_lo_in,
  input  [31:0] lo_out_in,
  input  [31:0] imm_ext_sft_in,
  input  [31:0] imm_ext_in,
  input  [31:0] R2_v0_in,
  input  [31:0] R1_a0_in,
  input  [31:0] PC_in,
  input  [31:0] IR_in,
  input  CLK,
  input  \同步清零_气泡_高电平有效 ,
  input  \使能端_低电平有效_stall_高电平有效 ,
  output RegWrite_out,
  output jal_out,
  output lui_out,
  output mflo_out,
  output MemToReg_out,
  output syscall_out,
  output mem_sign_ext_out,
  output MemWrite_out,
  output [1:0] MODE_out,
  output [4:0] w__out,
  output [31:0] alu_r1_lo_out,
  output [31:0] lo_out_out,
  output [31:0] imm_ext_sft_out,
  output [31:0] imm_ext_out,
  output [31:0] R2_v0_out,
  output [31:0] R1_a0_out,
  output [31:0] PC_out,
  output [31:0] IR_out
);

  wire not_1_out;
  wire [1:0] multiplexer_2_out, multiplexer_3_out;
  wire [4:0] multiplexer_4_out;
  wire [5:0] multiplexer_1_out;
  wire [31:0] multiplexer_5_out, multiplexer_6_out, multiplexer_7_out, multiplexer_8_out, multiplexer_9_out,
       multiplexer_10_out, multiplexer_11_out, multiplexer_12_out, undriven;

  Multiplexer #(.width(6), .enable("false")) multiplexer_1 (
    .in0({syscall_in, MemToReg_in, mflo_in, lui_in, jal_in, RegWrite_in}), .in1({6{1'b0}}),
    .out(multiplexer_1_out), .sel(\同步清零_气泡_高电平有效 ));
  Multiplexer #(.width(2), .enable("false")) multiplexer_2 (
    .in0({MemWrite_in, mem_sign_ext_in}), .in1(2'b00), .out(multiplexer_2_out), .sel(\同步清零_气泡_高电平有效 ));
  Multiplexer #(.width(2), .enable("false")) multiplexer_3 (
    .in0(MODE_in), .in1(2'b00), .out(multiplexer_3_out), .sel(\同步清零_气泡_高电平有效 ));
  Multiplexer #(.width(5), .enable("false")) multiplexer_4 (
    .in0(w__in), .in1({5{1'b0}}), .out(multiplexer_4_out), .sel(\同步清零_气泡_高电平有效 ));
  Multiplexer #(.width(32), .enable("false")) multiplexer_5 (
    .in0(alu_r1_lo_in), .in1(undriven), .out(multiplexer_5_out), .sel(\同步清零_气泡_高电平有效 ));
  Multiplexer #(.width(32), .enable("false")) multiplexer_6 (
    .in0(lo_out_in), .in1(undriven), .out(multiplexer_6_out), .sel(\同步清零_气泡_高电平有效 ));
  Multiplexer #(.width(32), .enable("false")) multiplexer_7 (
    .in0(imm_ext_sft_in), .in1({32{1'b0}}), .out(multiplexer_7_out), .sel(\同步清零_气泡_高电平有效 ));
  Multiplexer #(.width(32), .enable("false")) multiplexer_8 (
    .in0(imm_ext_in), .in1({32{1'b0}}), .out(multiplexer_8_out), .sel(\同步清零_气泡_高电平有效 ));
  Multiplexer #(.width(32), .enable("false")) multiplexer_9 (
    .in0(R2_v0_in), .in1({32{1'b0}}), .out(multiplexer_9_out), .sel(\同步清零_气泡_高电平有效 ));
  Multiplexer #(.width(32), .enable("false")) multiplexer_10 (
    .in0(R1_a0_in), .in1({32{1'b0}}), .out(multiplexer_10_out), .sel(\同步清零_气泡_高电平有效 ));
  Multiplexer #(.width(32), .enable("false")) multiplexer_11 (
    .in0(PC_in), .in1({32{1'b0}}), .out(multiplexer_11_out), .sel(\同步清零_气泡_高电平有效 ));
  Multiplexer #(.width(32), .enable("false")) multiplexer_12 (
    .in0(IR_in), .in1({32{1'b0}}), .out(multiplexer_12_out), .sel(\同步清零_气泡_高电平有效 ));
  not not_1 (not_1_out, \使能端_低电平有效_stall_高电平有效 );
  Register #(.width(6)) register_1 (
    .D(multiplexer_1_out), .en(not_1_out),
    .Q({syscall_out, MemToReg_out, mflo_out, lui_out, jal_out, RegWrite_out}), .clk(CLK));  // open: clr
  Register #(.width(2)) register_2 (
    .D(multiplexer_2_out), .en(not_1_out), .Q({MemWrite_out, mem_sign_ext_out}), .clk(CLK));  // open: clr
  Register #(.width(2)) register_3 (.D(multiplexer_3_out), .en(not_1_out), .Q(MODE_out), .clk(CLK));  // open: clr
  Register #(.width(5)) register_4 (.D(multiplexer_4_out), .en(not_1_out), .Q(w__out), .clk(CLK));  // open: clr
  Register #(.width(32)) register_5 (.D(multiplexer_5_out), .en(not_1_out), .Q(alu_r1_lo_out), .clk(CLK));  // open: clr
  Register #(.width(32)) register_6 (.D(multiplexer_6_out), .en(not_1_out), .Q(lo_out_out), .clk(CLK));  // open: clr
  Register #(.width(32)) register_7 (
    .D(multiplexer_7_out), .en(not_1_out), .Q(imm_ext_sft_out), .clk(CLK));  // open: clr
  Register #(.width(32)) register_8 (.D(multiplexer_8_out), .en(not_1_out), .Q(imm_ext_out), .clk(CLK));  // open: clr
  Register #(.width(32)) register_9 (.D(multiplexer_9_out), .en(not_1_out), .Q(R2_v0_out), .clk(CLK));  // open: clr
  Register #(.width(32)) register_10 (.D(multiplexer_10_out), .en(not_1_out), .Q(R1_a0_out), .clk(CLK));  // open: clr
  Register #(.width(32)) register_11 (.D(multiplexer_11_out), .en(not_1_out), .Q(PC_out), .clk(CLK));  // open: clr
  Register #(.width(32)) register_12 (.D(multiplexer_12_out), .en(not_1_out), .Q(IR_out), .clk(CLK));  // open: clr
endmodule

// MEM/WB
module MEM_WB (
  input  RegWrite_in,
  input  jal_in,
  input  lui_in,
  input  mflo_in,
  input  MemToReg_in,
  input  syscall_in,
  input  [4:0] w__in,
  input  [31:0] MemOut_in,
  input  [31:0] alu_r1_lo_in,
  input  [31:0] lo_out_in,
  input  [31:0] imm_ext_sft_in,
  input  [31:0] R2_v0_in,
  input  [31:0] R1_a0_in,
  input  [31:0] PC_in,
  input  [31:0] IR_in,
  input  CLK,
  input  \同步清零_气泡_高电平有效 ,
  input  \使能端_低电平有效_stall_高电平有效 ,
  output RegWrite_out,
  output jal_out,
  output lui_out,
  output mflo_out,
  output MemToReg_out,
  output syscall_out,
  output [4:0] w__out,
  output [31:0] MemOut_out,
  output [31:0] alu_r1_lo_out,
  output [31:0] lo_out_out,
  output [31:0] imm_ext_sft_out,
  output [31:0] R2_v0_out,
  output [31:0] R1_a0_out,
  output [31:0] PC_out,
  output [31:0] IR_out
);

  wire not_1_out;
  wire [4:0] multiplexer_2_out;
  wire [5:0] multiplexer_1_out;
  wire [31:0] multiplexer_3_out, multiplexer_4_out, multiplexer_5_out, multiplexer_6_out, multiplexer_7_out,
       multiplexer_8_out, multiplexer_9_out, multiplexer_10_out;

  Multiplexer #(.width(6), .enable("false")) multiplexer_1 (
    .in0({syscall_in, MemToReg_in, mflo_in, lui_in, jal_in, RegWrite_in}), .in1({6{1'b0}}),
    .out(multiplexer_1_out), .sel(\同步清零_气泡_高电平有效 ));
  Multiplexer #(.width(5), .enable("false")) multiplexer_2 (
    .in0(w__in), .in1({5{1'b0}}), .out(multiplexer_2_out), .sel(\同步清零_气泡_高电平有效 ));
  Multiplexer #(.width(32), .enable("false")) multiplexer_3 (
    .in0(MemOut_in), .in1({32{1'b0}}), .out(multiplexer_3_out), .sel(\同步清零_气泡_高电平有效 ));
  Multiplexer #(.width(32), .enable("false")) multiplexer_4 (
    .in0(alu_r1_lo_in), .in1({32{1'b0}}), .out(multiplexer_4_out), .sel(\同步清零_气泡_高电平有效 ));
  Multiplexer #(.width(32), .enable("false")) multiplexer_5 (
    .in0(lo_out_in), .in1({32{1'b0}}), .out(multiplexer_5_out), .sel(\同步清零_气泡_高电平有效 ));
  Multiplexer #(.width(32), .enable("false")) multiplexer_6 (
    .in0(imm_ext_sft_in), .in1({32{1'b0}}), .out(multiplexer_6_out), .sel(\同步清零_气泡_高电平有效 ));
  Multiplexer #(.width(32), .enable("false")) multiplexer_7 (
    .in0(R2_v0_in), .in1({32{1'b0}}), .out(multiplexer_7_out), .sel(\同步清零_气泡_高电平有效 ));
  Multiplexer #(.width(32), .enable("false")) multiplexer_8 (
    .in0(R1_a0_in), .in1({32{1'b0}}), .out(multiplexer_8_out), .sel(\同步清零_气泡_高电平有效 ));
  Multiplexer #(.width(32), .enable("false")) multiplexer_9 (
    .in0(PC_in), .in1({32{1'b0}}), .out(multiplexer_9_out), .sel(\同步清零_气泡_高电平有效 ));
  Multiplexer #(.width(32), .enable("false")) multiplexer_10 (
    .in0(IR_in), .in1({32{1'b0}}), .out(multiplexer_10_out), .sel(\同步清零_气泡_高电平有效 ));
  not not_1 (not_1_out, \使能端_低电平有效_stall_高电平有效 );
  Register #(.width(6)) register_1 (
    .D(multiplexer_1_out), .en(not_1_out),
    .Q({syscall_out, MemToReg_out, mflo_out, lui_out, jal_out, RegWrite_out}), .clk(CLK));  // open: clr
  Register #(.width(5)) register_2 (.D(multiplexer_2_out), .en(not_1_out), .Q(w__out), .clk(CLK));  // open: clr
  Register #(.width(32)) register_3 (.D(multiplexer_3_out), .en(not_1_out), .Q(MemOut_out), .clk(CLK));  // open: clr
  Register #(.width(32)) register_4 (.D(multiplexer_4_out), .en(not_1_out), .Q(alu_r1_lo_out), .clk(CLK));  // open: clr
  Register #(.width(32)) register_5 (.D(multiplexer_5_out), .en(not_1_out), .Q(lo_out_out), .clk(CLK));  // open: clr
  Register #(.width(32)) register_6 (
    .D(multiplexer_6_out), .en(not_1_out), .Q(imm_ext_sft_out), .clk(CLK));  // open: clr
  Register #(.width(32)) register_7 (.D(multiplexer_7_out), .en(not_1_out), .Q(R2_v0_out), .clk(CLK));  // open: clr
  Register #(.width(32)) register_8 (.D(multiplexer_8_out), .en(not_1_out), .Q(R1_a0_out), .clk(CLK));  // open: clr
  Register #(.width(32)) register_9 (.D(multiplexer_9_out), .en(not_1_out), .Q(PC_out), .clk(CLK));  // open: clr
  Register #(.width(32)) register_10 (.D(multiplexer_10_out), .en(not_1_out), .Q(IR_out), .clk(CLK));  // open: clr
endmodule

module \分支相关流水线  (
);

  wire CLK, Go, IR1, IR2, IR3, RST, W1, W2, W3;
  wire [11:0] EX_PC, ID_PC, IF_PC, MEM_PC, WB_PC;
  wire [15:0] \LoadUse次数 , \总周期数 , \插入气泡数 , \无条件分支数 , \条件分支成功数 ;
  wire [31:0] LedData;

  Button \u_总复位  (.out(RST));
  Button _1 (.out(IR1));
  Button _2 (.out(IR2));
  Button _3 (.out(IR3));
  Button \u_继续运行  (.out(Go));
  LED led_1 (.in(W1));
  LED led_2 (.in(W2));
  LED led_3 (.in(W3));
  Hex_Digit_Display hex_digit_display_1 (.value(LedData[31:28]));  // open: dp
  Hex_Digit_Display hex_digit_display_2 (.value(LedData[27:24]));  // open: dp
  Hex_Digit_Display hex_digit_display_3 (.value(LedData[23:20]));  // open: dp
  Hex_Digit_Display hex_digit_display_4 (.value(LedData[19:16]));  // open: dp
  Hex_Digit_Display hex_digit_display_5 (.value(LedData[15:12]));  // open: dp
  Hex_Digit_Display hex_digit_display_6 (.value(LedData[7:4]));  // open: dp
  Hex_Digit_Display hex_digit_display_7 (.value(LedData[11:8]));  // open: dp
  Clock clock_1 (.out(CLK));
  Hex_Digit_Display hex_digit_display_8 (.value(LedData[3:0]));  // open: dp
  // Probe on \总周期数 
  // Probe on \无条件分支数 
  // Probe on \条件分支成功数 
  // Probe on \插入气泡数 
  // Probe on \LoadUse次数 
  // Probe on IF_PC
  // Probe on ID_PC
  // Probe on EX_PC
  // Probe on MEM_PC
  // Probe on WB_PC

  // Notes on the sheet:
  //   中断源
  //   中断等待指示
  //   数码管输出
  //   流水调试日志用
endmodule

module \气泡流水线  (
);

  wire CLK, Go, IR1, IR2, IR3, RST, W1, W2, W3;
  wire [11:0] EX_PC, ID_PC, IF_PC, MEM_PC, WB_PC;
  wire [15:0] \LoadUse次数 , \总周期数 , \插入气泡数 , \无条件分支数 , \条件分支成功数 ;
  wire [31:0] LedData;

  Button \u_总复位  (.out(RST));
  Button _1 (.out(IR1));
  Button _2 (.out(IR2));
  Button _3 (.out(IR3));
  Button \u_继续运行  (.out(Go));
  LED led_1 (.in(W1));
  LED led_2 (.in(W2));
  LED led_3 (.in(W3));
  Hex_Digit_Display hex_digit_display_1 (.value(LedData[31:28]));  // open: dp
  Hex_Digit_Display hex_digit_display_2 (.value(LedData[27:24]));  // open: dp
  Hex_Digit_Display hex_digit_display_3 (.value(LedData[23:20]));  // open: dp
  Hex_Digit_Display hex_digit_display_4 (.value(LedData[19:16]));  // open: dp
  Hex_Digit_Display hex_digit_display_5 (.value(LedData[15:12]));  // open: dp
  Hex_Digit_Display hex_digit_display_6 (.value(LedData[7:4]));  // open: dp
  Hex_Digit_Display hex_digit_display_7 (.value(LedData[11:8]));  // open: dp
  Clock clock_1 (.out(CLK));
  Hex_Digit_Display hex_digit_display_8 (.value(LedData[3:0]));  // open: dp
  // Probe on \总周期数 
  // Probe on \无条件分支数 
  // Probe on \条件分支成功数 
  // Probe on \插入气泡数 
  // Probe on \LoadUse次数 
  // Probe on IF_PC
  // Probe on ID_PC
  // Probe on EX_PC
  // Probe on MEM_PC
  // Probe on WB_PC

  // Notes on the sheet:
  //   中断源
  //   中断等待指示
  //   数码管输出
  //   流水调试日志用
endmodule

module \重定向流水线  (
  output [31:0] out_1,
  output [4:0] out_2,
  output [4:0] out_3,
  output [4:0] out_4
);

  wire AluSrcB, AluSrcB_ex, and_1_out, BEQ, BNE, CLK, Go, HLEN, HLEN_ex, IR1, IR2, IR3, J, Jal, Jal_ex,
       Jal_mem, Jal_wb, jr, Load_Use, LUI, LUI_ex, LUI_mem, LUI_wb, MEM_SIGN_EXT, MEM_SIGN_EXT_ex,
       MEM_SIGN_EXT_mem, MemToReg, MemToReg_ex, MemToReg_mem, MemToReg_wb, MemWrite, MemWrite_ex,
       MemWrite_mem, MFLO, MFLO_ex, MFLO_mem, MFLO_wb, not_1_out, not_2_out, not_3_out, or_1_out, or_2_out,
       or_3_out, or_4_out, or_5_out, pcvalid, RegDst, RegWrite, RegWrite_ex, RegWrite_mem, RegWrite_wb, RST,
       SHAMT_SRC, SHAMT_SRC_ex, SignedExt, syscall, syscall_ex, syscall_mem, syscall_wb, tunnel, W1, W2, W3,
       \流水线跳转语句分支判断_1_发生跳转 ;
  wire [1:0] B_BRANCH, MODE, MODE_ex, MODE_mem, R1_forward, R2_forward;
  wire [3:0] AluOp, AluOp_ex;
  wire [4:0] multiplexer_2_out, multiplexer_4_out, multiplexer_17_out, W__ex, W__mem, W_num;
  wire [5:0] func;
  wire [15:0] \LoadUse次数 , \总周期数 , \插入气泡数 , \无条件分支数 , \条件分支成功数 ;
  wire [25:6] Imm26;
  wire [31:0] adder_2_out, adder_3_out, adder_4_out, bit_extender_1_out, bit_extender_2_out, HI, imm_ext,
       imm_ext_ex, imm_ext_mem, imm_ext_sft, imm_ext_sft_ex, imm_ext_sft_mem, imm_ext_sft_wb, IR_ex, IR_mem,
       IR_wb, LedData, LO_Out, LO_Out_mem, LO_Out_wb, LO_R, LO_R_mem, LO_R_wb, Mem_out, Mem_out_wb,
       multiplexer_1_out, multiplexer_8_out, multiplexer_9_out, multiplexer_10_out, multiplexer_11_out,
       multiplexer_12_out, multiplexer_13_out, multiplexer_16_out, multiplexer_18_out, multiplexer_19_out,
       multiplexer_20_out, PC, PC_4, PC_ex, PC_id, PC_mem, PC_out, PC_wb, R1_a0, R1_a0_ex, R1_a0_mem,
       R1_a0_wb, R2_v0, R2_v0_ex, R2_v0_mem, R2_v0_wb, registerfile_1_p7, registerfile_1_p8, rom_1_data,
       shifter_2_out;
  wire [31:26] IR;

  Button \u_总复位  (.out(RST));
  Button _1 (.out(IR1));
  Button _2 (.out(IR2));
  Button _3 (.out(IR3));
  // Probe on {IR, Imm26, func}
  // Probe on PC_id
  // Probe on R1_a0_wb
  // Probe on R2_v0_wb
  and and_1 (and_1_out, pcvalid, ~Load_Use);  // AND_Gate
  Button \u_继续运行  (.out(Go));
  LED led_1 (.in(W1));
  LED led_2 (.in(W2));
  LED led_3 (.in(W3));
  // Probe on R1_forward
  // Probe on R2_forward
  Multiplexer #(.width(32), .enable("false")) multiplexer_1 (
    .in0(PC_4), .in1(PC_out), .out(multiplexer_1_out), .sel(\流水线跳转语句分支判断_1_发生跳转 ));
  Register #(.width(32)) u_PC (.D(multiplexer_1_out), .en(and_1_out), .Q(PC), .clk(CLK), .clr(RST));
  Counter #(.width(16), .max('hffff)) counter_1 (
    .count(pcvalid), .Q(\总周期数 ), .clk(CLK), .clr(RST));  // open: load, D, carry
  Hex_Digit_Display hex_digit_display_1 (.value(LedData[31:28]));  // open: dp
  Hex_Digit_Display hex_digit_display_2 (.value(LedData[27:24]));  // open: dp
  Adder #(.width(32)) adder_1 (.a(PC), .b(32'h4), .out(PC_4));  // open: cin, cout
  Hex_Digit_Display hex_digit_display_3 (.value(LedData[19:16]));  // open: dp
  Hex_Digit_Display hex_digit_display_4 (.value(LedData[23:20]));  // open: dp
  Counter #(.width(16), .max('hffff)) counter_2 (
    .count(\流水线跳转语句分支判断_1_发生跳转 ), .Q(\条件分支成功数 ), .clk(CLK), .clr(RST));  // open: load, D, carry
  Hex_Digit_Display hex_digit_display_5 (.value(LedData[15:12]));  // open: dp
  Hex_Digit_Display hex_digit_display_6 (.value(LedData[11:8]));  // open: dp
  Clock clock_1 (.out(CLK));
  ROM #(.addrWidth(10), .dataWidth(32)) rom_1 (.addr(PC[11:2]), .data(rom_1_data));  // open: sel
  Hex_Digit_Display hex_digit_display_7 (.value(LedData[7:4]));  // open: dp
  Hex_Digit_Display hex_digit_display_8 (.value(LedData[3:0]));  // open: dp
  or or_1 (or_1_out, \流水线跳转语句分支判断_1_发生跳转 , RST);
  or or_2 (or_2_out, Load_Use, ~pcvalid);  // OR_Gate
  IF_ID if_id_1 (
    .PC_in(PC), .IR_in(rom_1_data), .CLK(CLK), .PC_out(PC_id), .IR_out({IR, Imm26, func}),
    .\同步清零_气泡_高电平有效 (or_1_out), .\使能端_低电平有效_stall_高电平有效 (or_2_out));
  Counter #(.width(16), .max('hffff)) counter_3 (
    .count(Load_Use), .Q(\LoadUse次数 ), .clk(CLK), .clr(RST));  // open: load, D, carry
  \流水线跳转语句分支判断  \u_流水线跳转语句分支判断_1  (
    .PC(PC_id), .\_32位指令 ({IR, Imm26, func}), .\跳转信号 ({B_BRANCH, SignedExt, jr, Jal, J, BNE, BEQ}),
    .rs(R1_a0), .rt(R2_v0), .Next_PC(PC_out), .\发生跳转 (\流水线跳转语句分支判断_1_发生跳转 ));
  Multiplexer #(.width(5), .enable("false")) multiplexer_2 (
    .in0(Imm26[20:16]), .in1(Imm26[15:11]), .out(multiplexer_2_out), .sel(RegDst));
  // Probe on \总周期数 
  // Probe on \无条件分支数 
  // Probe on \条件分支成功数 
  // Probe on \插入气泡数 
  // Probe on \LoadUse次数 
  // Probe on PC_id[11:0]
  Multiplexer #(.width(5), .enable("false")) multiplexer_3 (
    .in0(Imm26[25:21]), .in1(5'b00100), .out(out_3), .sel(syscall));
  Multiplexer #(.width(5), .enable("false")) multiplexer_4 (
    .in0(Imm26[20:16]), .in1(5'b00010), .out(multiplexer_4_out), .sel(syscall));
  Multiplexer #(.width(5), .enable("false")) multiplexer_5 (
    .in0(multiplexer_2_out), .in1({5{1'b1}}), .out(W_num), .sel(Jal));
  assign bit_extender_1_out = {{16{1'b0}}, {Imm26[15:6], func}};  // Bit_Extender bit_extender_1
  assign bit_extender_2_out = {{16{Imm26[15]}}, {Imm26[15:6], func}};  // Bit_Extender bit_extender_2
  // Probe on PC[11:0]
  // Probe on PC_ex[11:0]
  // Probe on PC_mem[11:0]
  or or_3 (or_3_out, J, jr);
  or or_4 (or_4_out, B_BRANCH[1], B_BRANCH[0]);
  Multiplexer #(.width(5), .enable("false")) multiplexer_6 (
    .in0(multiplexer_4_out), .in1({5{1'b0}}), .out(out_4), .sel(or_4_out));
  Multiplexer #(.width(32), .enable("false")) multiplexer_7 (
    .in0(bit_extender_1_out), .in1(bit_extender_2_out), .out(imm_ext), .sel(SignedExt));
  // Probe on PC_id[11:0]
  // Probe on PC_ex[11:0]
  // Probe on PC_wb[11:0]
  Counter #(.width(16), .max('hffff)) counter_4 (
    .count(or_3_out), .Q(\无条件分支数 ), .clk(CLK), .clr(RST));  // open: load, D, carry
  Shifter #(.width(32)) shifter_1 (.in(bit_extender_1_out), .\dist (5'b10000), .out(imm_ext_sft));
  // Probe on PC_wb[11:0]
  // Probe on PC_mem[11:0]
  Shifter #(.width(32)) shifter_2 (.in(imm_ext), .\dist (5'b00010), .out(shifter_2_out));
  \硬布线控制器  \u_硬布线控制器_1  (
    .Func(func), .OP(IR), .ALU_OP(AluOp), .MemToReg(MemToReg), .MemWrite(MemWrite), .ALU_SRC(AluSrcB),
    .RegWrite(RegWrite), .SysCALL(syscall), .SignedExt(SignedExt), .RegDst(RegDst), .JR(jr), .JMP(J),
    .Beq(BEQ), .JAL(Jal), .Bne(BNE), .SHAMT_SRC(SHAMT_SRC), .LUI(LUI), .HLEN(HLEN), .MFLO(MFLO),
    .MEM_SIGN_EXT(MEM_SIGN_EXT), .B_BRANCH(B_BRANCH), .MODE(MODE));
  // RegisterFile registerfile_1: pin names not known; wires that end beside it: out_1, CLK, RegWrite_wb, out_2, out_3, out_4, registerfile_1_p7, registerfile_1_p8
  Adder #(.width(32)) adder_2 (.a(PC_ex), .b(32'h4), .out(adder_2_out));  // open: cin, cout
  Adder #(.width(32)) adder_3 (.a(PC_mem), .b(32'h4), .out(adder_3_out));  // open: cin, cout
  Multiplexer #(.width(32), .enable("false")) multiplexer_8 (
    .in0(LO_R), .in1(adder_2_out), .out(multiplexer_8_out), .sel(Jal_ex));
  Multiplexer #(.width(32), .enable("false")) multiplexer_9 (
    .in0(LO_R_mem), .in1(adder_3_out), .out(multiplexer_9_out), .sel(Jal_mem));
  Multiplexer #(.width(32), .enable("false")) multiplexer_10 (
    .in0(multiplexer_8_out), .in1(imm_ext_sft_ex), .out(multiplexer_10_out), .sel(LUI_ex));
  Multiplexer #(.width(32), .enable("false")) multiplexer_11 (
    .in0(multiplexer_10_out), .in1(LO_Out), .out(multiplexer_11_out), .sel(MFLO_ex));
  Multiplexer #(.width(32), .enable("false")) multiplexer_12 (
    .in0(multiplexer_9_out), .in1(imm_ext_sft_mem), .out(multiplexer_12_out), .sel(LUI_mem));
  Multiplexer #(.width(32), .enable("false")) multiplexer_13 (
    .in0(multiplexer_12_out), .in1(LO_Out_mem), .out(multiplexer_13_out), .sel(MFLO_mem));
  \数据相关检测  \u_数据相关检测_1  (
    .Load_Use(Load_Use), .OP(IR), .EX_RegWrite(RegWrite_ex), .R2_forward(R2_forward), .EX_W_num(W__ex),
    .MEM_RegWrite(RegWrite_mem), .Func(func), .Mem_W_num(W__mem), .ID_R1_num(out_3), .ID_R2_num(out_4),
    .R1_forward(R1_forward), .MEM_MemToReg(MemToReg_mem), .EX_MemToReg(MemToReg_ex));
  Multiplexer #(.select(2), .width(32), .enable("false")) multiplexer_14 (
    .in0(registerfile_1_p7), .in1(multiplexer_11_out), .in2(multiplexer_13_out), .in3(multiplexer_11_out),
    .out(R1_a0), .sel(R1_forward));
  Multiplexer #(.select(2), .width(32), .enable("false")) multiplexer_15 (
    .in0(registerfile_1_p8), .in1(multiplexer_11_out), .in2(multiplexer_13_out), .in3(multiplexer_11_out),
    .out(R2_v0), .sel(R2_forward));
  not not_1 (not_1_out, pcvalid);
  or or_5 (or_5_out, Load_Use, RST);
  ID_EX id_ex_1 (
    .RegWrite_in(RegWrite), .jal_in(Jal), .lui_in(LUI), .mflo_in(MFLO), .MemToReg_in(MemToReg),
    .syscall_in(syscall), .mem_sign_ext_in(MEM_SIGN_EXT), .MemWrite_in(MemWrite), .MODE_in(MODE),
    .shamt_src_in(SHAMT_SRC), .HLEN_in(HLEN), .AluSrcB_in(AluSrcB), .AluOP_in(AluOp),
    .imm_ext_sft_in(imm_ext_sft), .imm_ext_in(imm_ext), .R2_v0_in(R2_v0), .R1_a0_in(R1_a0), .PC_in(PC_id),
    .IR_in({IR, Imm26, func}), .CLK(CLK), .RegWrite_out(RegWrite_ex), .jal_out(Jal_ex), .lui_out(LUI_ex),
    .mflo_out(MFLO_ex), .MemToReg_out(MemToReg_ex), .syscall_out(syscall_ex),
    .mem_sign_ext_out(MEM_SIGN_EXT_ex), .MemWrite_out(MemWrite_ex), .MODE_out(MODE_ex),
    .shamt_src_out(SHAMT_SRC_ex), .HLEN_out(HLEN_ex), .AluSrcB_out(AluSrcB_ex), .AluOP_out(AluOp_ex),
    .imm_ext_sft_out(imm_ext_sft_ex), .imm_ext_out(imm_ext_ex), .R2_v0_out(R2_v0_ex), .R1_a0_out(R1_a0_ex),
    .PC_out(PC_ex), .IR_out(IR_ex), .\同步清零_气泡_高电平有效 (or_5_out), .\使能端_低电平有效_stall_高电平有效 (not_1_out),
    .w__in(W_num), .w__out(W__ex));
  Multiplexer #(.width(32), .enable("false")) multiplexer_16 (
    .in0(R2_v0_ex), .in1(imm_ext_ex), .out(multiplexer_16_out), .sel(AluSrcB_ex));
  Multiplexer #(.width(5), .enable("false")) multiplexer_17 (
    .in0(IR_ex[10:6]), .in1(R1_a0_ex[4:0]), .out(multiplexer_17_out), .sel(SHAMT_SRC_ex));
  Register #(.width(32)) register_1 (.D(LO_R), .en(HLEN_ex), .Q(LO_Out), .clk(CLK), .clr(RST));
  Register #(.width(32)) register_2 (.D(HI), .en(HLEN_ex), .clk(CLK), .clr(RST));  // open: Q
  not not_2 (not_2_out, pcvalid);
  EX_MEM ex_mem_1 (
    .RegWrite_in(RegWrite_ex), .jal_in(Jal_ex), .lui_in(LUI_ex), .mflo_in(MFLO_ex),
    .MemToReg_in(MemToReg_ex), .syscall_in(syscall_ex), .mem_sign_ext_in(MEM_SIGN_EXT_ex),
    .MemWrite_in(MemWrite_ex), .MODE_in(MODE_ex), .alu_r1_lo_in(LO_R), .lo_out_in(LO_Out),
    .imm_ext_sft_in(imm_ext_sft_ex), .imm_ext_in(imm_ext_ex), .R2_v0_in(R2_v0_ex), .R1_a0_in(R1_a0_ex),
    .PC_in(PC_ex), .IR_in(IR_ex), .CLK(CLK), .RegWrite_out(RegWrite_mem), .jal_out(Jal_mem),
    .lui_out(LUI_mem), .mflo_out(MFLO_mem), .MemToReg_out(MemToReg_mem), .syscall_out(syscall_mem),
    .mem_sign_ext_out(MEM_SIGN_EXT_mem), .MemWrite_out(MemWrite_mem), .MODE_out(MODE_mem),
    .alu_r1_lo_out(LO_R_mem), .lo_out_out(LO_Out_mem), .imm_ext_sft_out(imm_ext_sft_mem),
    .imm_ext_out(imm_ext_mem), .R2_v0_out(R2_v0_mem), .R1_a0_out(R1_a0_mem), .PC_out(PC_mem),
    .IR_out(IR_mem), .\同步清零_气泡_高电平有效 (RST), .\使能端_低电平有效_stall_高电平有效 (not_2_out), .w__in(W__ex),
    .w__out(W__mem));
  MIPS_ALU mips_alu_1 (
    .X(R1_a0_ex), .Y(multiplexer_16_out), .AluOP(AluOp_ex), .Equal(tunnel), .Result(LO_R), .Result_2(HI),
    .shamt(multiplexer_17_out));
  Syscall syscall_1 (
    .CLK(CLK), .RST(RST), .syscall(syscall_wb), .go(Go), .a0(R1_a0_wb), .v0(R2_v0_wb), .LedData(LedData),
    .PcValid(pcvalid));
  not not_3 (not_3_out, pcvalid);
  MEM_WB mem_wb_1 (
    .RegWrite_in(RegWrite_mem), .jal_in(Jal_mem), .lui_in(LUI_mem), .mflo_in(MFLO_mem),
    .MemToReg_in(MemToReg_mem), .syscall_in(syscall_mem), .PC_in(PC_mem), .IR_in(IR_mem), .CLK(CLK),
    .RegWrite_out(RegWrite_wb), .jal_out(Jal_wb), .lui_out(LUI_wb), .mflo_out(MFLO_wb),
    .MemToReg_out(MemToReg_wb), .syscall_out(syscall_wb), .PC_out(PC_wb), .IR_out(IR_wb),
    .\同步清零_气泡_高电平有效 (RST), .\使能端_低电平有效_stall_高电平有效 (not_3_out), .R2_v0_in(R2_v0_mem), .R2_v0_out(R2_v0_wb),
    .R1_a0_in(R1_a0_mem), .R1_a0_out(R1_a0_wb), .alu_r1_lo_in(LO_R_mem), .alu_r1_lo_out(LO_R_wb),
    .lo_out_in(LO_Out_mem), .lo_out_out(LO_Out_wb), .imm_ext_sft_in(imm_ext_sft_mem),
    .imm_ext_sft_out(imm_ext_sft_wb), .MemOut_in(Mem_out), .MemOut_out(Mem_out_wb), .w__in(W__mem),
    .w__out(out_2));
  \数据存储器  \u_数据存储器_1  (
    .\字节地址 (LO_R_mem[11:0]), .Din(R2_v0_mem), .DataOut(Mem_out), .CLK(CLK), .WE(MemWrite_mem),
    .Mode(MODE_mem), .clr(RST), .in_3(MEM_SIGN_EXT_mem));
  Multiplexer #(.width(32), .enable("false")) multiplexer_18 (
    .in0(LO_R_wb), .in1(Mem_out_wb), .out(multiplexer_18_out), .sel(MemToReg_wb));
  Adder #(.width(32)) adder_4 (.a(PC_wb), .b(32'h4), .out(adder_4_out));  // open: cin, cout
  Multiplexer #(.width(32), .enable("false")) multiplexer_19 (
    .in0(multiplexer_18_out), .in1(adder_4_out), .out(multiplexer_19_out), .sel(Jal_wb));
  Multiplexer #(.width(32), .enable("false")) multiplexer_20 (
    .in0(multiplexer_19_out), .in1(imm_ext_sft_wb), .out(multiplexer_20_out), .sel(LUI_wb));
  Multiplexer #(.width(32), .enable("false")) multiplexer_21 (
    .in0(multiplexer_20_out), .in1(LO_Out_wb), .out(out_1), .sel(MFLO_wb));

  // Other names for the same wires on the sheet: Imm26[5:0] = func; IR[25:0] = {Imm26, func}; rt[4:0] = Imm26[20:16];
  //   OP[5:0] = IR; R1[4:0] = out_3; R2[4:0] = out_4; RegDin[31:0] = out_1; rs[31:0] = R1_a0_ex; W__wb[4:0] = out_2

  // Notes on the sheet:
  //   中断源
  //   中断等待指示
  //   数码管输出
  //   指令存储器
  //   指令字
  //   contents of rom_1 (hex, n*v repeats v):
  //   20110001 8000c05 20110001 20120002 20130003 8000c09 20110001 20120002 20130003 8000c0d 20110001
  //   20120002 20130003 8000c11 20110001 20120002 20130003 c000e00 20100001 20110001 118fc0 112020
  //   20020022 c 118882 12200001 8000c15 112020 20020022 c 20110001 118880 112020 20020022 c 12200001
  //   8000c1f 20110001 118fc0 112020 20020022 c 1188c3 112020 20020022 c 118903 112020 20020022 c 118903
  //   112020 20020022 c 118903 112020 20020022 c 118903 112020 20020022 c 118903 112020 20020022 c 118903
  //   112020 20020022 c 118903 112020 20020022 c 20100001 109fc0 139fc3 8021 2012000c 24160003 26100001
  //   3210000f 20080008 20090001 139900 2709825 132020 20020022 c 1094022 1500fff9 22100001 2018000f
  //   2188024 108700 20080008 20090001 139902 2709825 132021 20020022 c 1094022 1500fff9 108702 2c9b022
  //   12c00001 8000c50 4020 1084027 84400 3508ffff 82021 20020022 c 2010ffff 20110000 ae300000 22100001
  //   22310004 ae300000 22100001 22310004 ae300000 22100001 22310004 ae300000 22100001 22310004 ae300000
  //   22100001 22310004 ae300000 22100001 22310004 ae300000 22100001 22310004 ae300000 22100001 22310004
  //   ae300000 22100001 22310004 ae300000 22100001 22310004 ae300000 22100001 22310004 ae300000 22100001
  //   22310004 ae300000 22100001 22310004 ae300000 22100001 22310004 ae300000 22100001 22310004 ae300000
  //   22100001 22310004 22100001 8020 2011003c 8e130000 8e340000 274402a 11000002 ae330000 ae140000
  //   2231fffc 1611fff8 102020 20020022 c 22100004 2011003c 1611fff2 20020032 c 20080001 20090003 20110876
  //   112020 20020022 c 200b0008 1118804 1318804 112020 20020022 c 216bffff 1560fff9 20020032 c 20080001
  //   20090003 20110876 118d00 112020 20020022 c 200b0008 1118806 1318806 112020 20020022 c 216bffff
  //   1560fff9 20020032 c 20080001 20090003 20110876 118d00 112020 20020022 c 200b0008 1118807 1318807
  //   112020 20020022 c 216bffff 1560fff9 20020032 c 20080001 20110010 112020 20020022 c 200b0020 2288823
  //   112020 20020022 c 216bffff 1560fffa 20020032 c 2008ffff 20117777 112020 20020022 c 200b0010 2288826
  //   112020 20020022 c 216bffff 1560fffa 20020032 c 2008ffff 20117777 112020 20020022 c 200b0010 3a31ffff
  //   112020 20020022 c 216bffff 1560fffa 20020032 c 200b0008 3c11fedc 3631ffff 112020 20020022 c 3c11ba98
  //   112020 c 3c117654 112020 c 3c113210 112020 c 216bffff 1560fff0 20020032 c 2008ffff 20090000 20111997
  //   112020 20020022 c 2288820 2e291949 1120fffa 20020032 c 20080002 20111111 112020 20020022 c 200b0020
  //   2280019 8812 112020 20020022 c 216bffff 1560fff9 20020032 c 20080002 20111111 118c00 112020 20020022
  //   c 200b001c 228001b 8812 112020 20020022 c 216bffff 1560fff9 20020032 c 20090000 200b0010 34118483
  //   20120404 118c00 129400 36318281 22520404 ad310000 2328820 21290004 216bffff 1560fffb 200b0020
  //   20090000 81310000 112020 20020022 c 21290001 216bffff 1560fff9 20020032 c 20090000 200b0010 34118483
  //   20120404 118c00 129400 36318281 22520404 ad310000 2328820 21290004 216bffff 1560fffb 200b0020
  //   20090000 91310000 112020 20020022 c 21290001 216bffff 1560fff9 20020032 c 20090000 200b0010 34118483
  //   20120404 118c00 129400 36318281 22520404 ad310000 2328820 21290004 216bffff 1560fffb 200b0020
  //   20090000 85310000 112020 20020022 c 21290002 216bffff 1560fff9 20020032 c 20090000 200b0010 34118483
  //   20120404 118c00 129400 36318281 22520404 ad310000 2328820 21290004 216bffff 1560fffb 200b0020
  //   20090000 95310000 112020 20020022 c 21290002 216bffff 1560fff9 20020032 c 20090000 200b0020 20110000
  //   20120001 a1310000 112020 20020022 c 2328820 21290001 216bffff 1560fff8 200b0008 20090000 8d310000
  //   112020 20020022 c 21290004 216bffff 1560fff9 20020032 c 20090000 200b0020 20110001 20120001 a5310000
  //   112020 20020022 c 2328820 21290002 216bffff 1560fff8 200b0010 20090000 8d310000 112020 20020022 c
  //   21290004 216bffff 1560fff9 20020032 c 2011fff1 112020 20020022 c 22310001 1a20fffb 20020032 c
  //   2011000f 112020 20020022 c 2231ffff 1e20fffb 20020032 c 2011fff1 112020 20020022 c 22310001 620fffb
  //   20020032 c 2011000f 112020 20020022 c 2231ffff 621fffb 20020032 c c 20100000 22100001 102020
  //   20020022 c 22100002 102020 20020022 c 22100003 102020 20020022 c 22100004 10202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
  //   OP
  //   rs
  //   rt
  //   rd
  //   imm
  //   Func
  //   流水调试日志用
  //   JMP
  //   JR
  //   OP
  //   Func
  //   Syscall
  //   Beq
  //   Bne
  //   AluOP
  //   AluSrcB
  //   RegWrite
  //   JAL
  //   RegDst
  //   MemToReg
  //   MemWrite
endmodule

module \数据存储器  (
  input  [11:0] \字节地址 ,
  input  [31:0] Din,
  input  in_3,
  input  CLK,
  input  WE,
  input  [1:0] Mode,
  input  clr,
  output [31:0] DataOut
);

  wire and_1_out, and_2_out, and_3_out, and_4_out, and_5_out, and_6_out, buffer_1_out, buffer_2_out,
       buffer_3_out, buffer_4_out, buffer_5_out, buffer_6_out, buffer_13_out, CS0, CS1, CS2, CS3, not_2_out,
       not_3_out, nWE, xor_1_out, \半字访问 , \字节访问 , \字访问 ;
  wire [7:0] buffer_7_out, D0, D1, D2, D3, DIN0, DIN1, DIN2, DIN3;
  wire [15:0] buffer_11_out;
  wire [31:0] bit_extender_1_out, bit_extender_2_out, bit_extender_3_out, bit_extender_4_out, buffer_14_out,
       demultiplexer_1_out0, demultiplexer_1_out1, demultiplexer_1_out2, demultiplexer_1_out3,
       multiplexer_1_out, multiplexer_2_out;

  not not_1 (nWE, WE);
  Demultiplexer #(.select(2), .width(32), .enable("false")) demultiplexer_1 (
    .out0(demultiplexer_1_out0), .out1(demultiplexer_1_out1), .out2(demultiplexer_1_out2),
    .out3(demultiplexer_1_out3), .in(Din), .sel(Mode));
  // MIPS_RAM mips_ram_1: pin names not known; wires that end beside it: \字节地址 [11:2], {DIN3, DIN2, DIN1, DIN0}, WE, {CS3, CS2, CS1, CS0}, CLK, clr, {D3, D2, D1, D0}
  assign DIN0 = demultiplexer_1_out0[7:0] | demultiplexer_1_out1[7:0] | demultiplexer_1_out2[7:0];  // OR_Gate or_1, 8 bits wide
  assign DIN1 = demultiplexer_1_out0[15:8] | demultiplexer_1_out1[7:0] | demultiplexer_1_out2[15:8];  // OR_Gate or_2, 8 bits wide
  assign DIN2 = demultiplexer_1_out0[23:16] | demultiplexer_1_out1[7:0] | demultiplexer_1_out2[7:0];  // OR_Gate or_3, 8 bits wide
  assign DIN3 = demultiplexer_1_out0[31:24] | demultiplexer_1_out1[7:0] | demultiplexer_1_out2[15:8];  // OR_Gate or_4, 8 bits wide
  // Probe on DataOut
  buf buffer_1 (buffer_1_out, buffer_2_out);
  buf buffer_2 (buffer_2_out, \字访问 );
  and and_1 (and_1_out, \字节地址 [1], \半字访问 );
  buf buffer_3 (buffer_3_out, \半字访问 );
  xor xor_1 (xor_1_out, \半字访问 , \字节地址 [1]);
  buf buffer_4 (buffer_4_out, \字节访问 );
  not not_2 (not_2_out, \字节地址 [0]);
  buf buffer_5 (buffer_5_out, \字节地址 [0]);
  buf buffer_6 (buffer_6_out, \字节地址 [1]);
  not not_3 (not_3_out, \字节地址 [1]);
  assign buffer_7_out = D0;  // Buffer buffer_7, 8 bits wide
  assign buffer_7_out = D1;  // Buffer buffer_8, 8 bits wide
  assign buffer_7_out = D2;  // Buffer buffer_9, 8 bits wide
  assign buffer_7_out = D3;  // Buffer buffer_10, 8 bits wide
  assign buffer_11_out = {D1, D0};  // Buffer buffer_11, 16 bits wide
  assign buffer_11_out = {D3, D2};  // Buffer buffer_12, 16 bits wide
  Decoder #(.select(2), .enable("false")) decoder_1 (
    .out0(\字访问 ), .out1(\字节访问 ), .out2(\半字访问 ), .sel(Mode));  // open: out3
  buf buffer_13 (buffer_13_out, and_1_out);
  and and_2 (and_2_out, buffer_3_out, xor_1_out);
  assign buffer_14_out = {D3, D2, D1, D0};  // Buffer buffer_14, 32 bits wide
  assign bit_extender_1_out = {{24{1'b0}}, buffer_7_out};  // Bit_Extender bit_extender_1
  assign bit_extender_2_out = {{24{buffer_7_out[7]}}, buffer_7_out};  // Bit_Extender bit_extender_2
  assign bit_extender_3_out = {{16{1'b0}}, buffer_11_out};  // Bit_Extender bit_extender_3
  assign bit_extender_4_out = {{16{buffer_11_out[15]}}, buffer_11_out};  // Bit_Extender bit_extender_4
  Multiplexer #(.width(32), .enable("false")) multiplexer_1 (
    .in0(bit_extender_1_out), .in1(bit_extender_2_out), .out(multiplexer_1_out), .sel(in_3));
  Multiplexer #(.width(32), .enable("false")) multiplexer_2 (
    .in0(bit_extender_3_out), .in1(bit_extender_4_out), .out(multiplexer_2_out), .sel(in_3));
  and and_3 (and_3_out, buffer_4_out, buffer_5_out, buffer_6_out);
  and and_4 (and_4_out, buffer_4_out, not_2_out, buffer_6_out);
  and and_5 (and_5_out, buffer_4_out, buffer_5_out, not_3_out);
  and and_6 (and_6_out, not_2_out, not_3_out, buffer_4_out);
  Multiplexer #(.select(2), .width(32), .enable("false")) multiplexer_3 (
    .in0(buffer_14_out), .in1(multiplexer_1_out), .in2(multiplexer_2_out), .in3({32{1'b0}}), .out(DataOut),
    .sel(Mode));
  or or_5 (CS3, buffer_1_out, buffer_13_out, and_3_out);
  or or_6 (CS2, buffer_1_out, buffer_13_out, and_4_out);
  or or_7 (CS1, buffer_1_out, and_2_out, and_5_out);
  or or_8 (CS0, buffer_1_out, and_2_out, and_6_out);

  // Other names for the same wires on the sheet: Dout[31:0] = DataOut; Mem_SignExt = in_3; 字节选择[1:0] = \字节地址 [1:0];
  //   半字选择 = \字节地址 [1]; 字地址[9:0] = \字节地址 [11:2]

  // Notes on the sheet:
  //   输入引脚区
  //   请勿增改引脚，请勿修改子电路封装
  //   电路功能：利用下图中给定的RAM器件实现既既可以按照字节，也可以按照半字，也可以按照32位字访问的MIPS存储器
  //   请在下方利用上方输入输出引脚的隧道信号构建电路，ctrl+d复制选择部件
  //   输出引脚区
endmodule

module Syscall (
  input  CLK,
  input  RST,
  input  syscall,
  input  go,
  input  [31:0] a0,
  input  [31:0] v0,
  output [31:0] LedData,
  output PcValid
);

  wire and_3_out, comparator_3_eq, datain, exit, not_1_out, pause;
  wire [31:0] and_1_out, bit_extender_1_out;

  assign bit_extender_1_out = {{31{syscall}}, syscall};  // Bit_Extender bit_extender_1
  assign and_1_out = bit_extender_1_out & v0;  // AND_Gate and_1, 32 bits wide
  Comparator #(.width(32)) comparator_1 (.a(and_1_out), .b(32'ha), .eq(exit));  // open: gt, lt
  Comparator #(.width(32)) comparator_2 (.a(and_1_out), .b(32'h22), .eq(datain));  // open: gt, lt
  not not_1 (not_1_out, comparator_3_eq);
  Comparator #(.width(32)) comparator_3 (.a(and_1_out), .b(32'h22), .eq(comparator_3_eq));  // open: gt, lt
  and and_2 (pause, not_1_out, syscall, ~go);  // AND_Gate
  Register #(.width(32), .trigger("falling")) register_1 (.D(a0), .en(datain), .Q(LedData), .clk(CLK), .clr(RST));
  and and_3 (and_3_out, go, ~exit);  // AND_Gate
  J_K_Flip_Flop #(.trigger("falling")) j_k_ff_1 (
    .J(pause), .clk(CLK), .K(and_3_out), .Qn(PcValid), .reset(RST));  // open: Q, preset, en

  // Notes on the sheet:
  //   exit
  //   print hex
  //   pause
endmodule

module \PC转移逻辑  (
  input  [31:0] rs,
  input  [31:0] PC,
  input  [31:0] imm_ext,
  input  [25:0] imm26,
  input  JR,
  input  J,
  input  Branch,
  output [31:0] PC_Out
);

  wire and_1_out;
  wire [31:0] adder_1_out, adder_2_out, multiplexer_1_out, multiplexer_2_out, shifter_1_out;

  Adder #(.width(32)) adder_1 (.a(32'h4), .b(PC), .out(adder_1_out));  // open: cin, cout
  Shifter #(.width(32)) shifter_1 (.in(imm_ext), .\dist (5'b00010), .out(shifter_1_out));
  Adder #(.width(32)) adder_2 (.a(adder_1_out), .b(shifter_1_out), .out(adder_2_out));  // open: cin, cout
  Multiplexer #(.width(32), .enable("false")) multiplexer_1 (
    .in0(adder_1_out), .in1(adder_2_out), .out(multiplexer_1_out), .sel(Branch));
  and and_1 (and_1_out, J, ~JR);  // AND_Gate
  Multiplexer #(.width(32), .enable("false")) multiplexer_2 (
    .in0(multiplexer_1_out), .in1(rs), .out(multiplexer_2_out), .sel(JR));
  Multiplexer #(.width(32), .enable("false")) multiplexer_3 (
    .in0(multiplexer_2_out), .in1({adder_1_out[31:28], imm26, 2'b00}), .out(PC_Out), .sel(and_1_out));

  // Other names for the same wires on the sheet: Imm[31:0] = imm_ext

  // Notes on the sheet:
  //   输入引脚区
  //   输出引脚区
endmodule

module Branch (
  input  R,
  input  [1:0] B,
  input  in_3,
  input  [4:0] rt,
  input  Beq,
  input  Bne,
  output Branch
);

  wire and_1_out, and_2_out, and_3_out, and_4_out, and_5_out, and_6_out, and_7_out, and_8_out,
       comparator_1_eq, decoder_1_out1, decoder_1_out2, decoder_1_out3, nor_1_out, not_1_out, not_2_out,
       not_3_out, not_4_out;

  Decoder #(.select(2), .enable("false")) decoder_1 (
    .out1(decoder_1_out1), .out2(decoder_1_out2), .out3(decoder_1_out3), .sel(B));  // open: out0
  not not_1 (not_1_out, in_3);
  nor nor_1 (nor_1_out, in_3, R);
  and and_1 (and_1_out, Beq, in_3);
  and and_2 (and_2_out, Bne, not_1_out);
  and and_3 (and_3_out, decoder_1_out3, comparator_1_eq);
  Comparator #(.width(5)) comparator_1 (.a(rt), .b({5{1'b0}}), .eq(comparator_1_eq));  // open: gt, lt
  not not_2 (not_2_out, comparator_1_eq);
  not not_3 (not_3_out, nor_1_out);
  not not_4 (not_4_out, R);
  and and_4 (and_4_out, not_3_out, decoder_1_out1);
  and and_5 (and_5_out, nor_1_out, decoder_1_out2);
  and and_6 (and_6_out, R, and_3_out);
  and and_7 (and_7_out, not_4_out, and_8_out);
  and and_8 (and_8_out, decoder_1_out3, not_2_out);
  or or_1 (Branch, and_1_out, and_2_out, and_4_out, and_5_out, and_6_out, and_7_out);

  // Other names for the same wires on the sheet: tunnel = in_3

  // Notes on the sheet:
  //   输入引脚区
  //   BGTZ
  //   BLEZ
  //   BLTZ
  //   BGEZ
  //   输出引脚区
endmodule

module temp (
  input  RegWrite_in,
  input  jal_in,
  input  lui_in,
  input  mflo_in,
  input  MemToReg_in,
  input  syscall_in,
  output RegWrite_out,
  output jal_out,
  output lui_out,
  output mflo_out,
  output MemToReg_out,
  output syscall_out
);

  wire undriven, undriven_2, undriven_3;
  wire [5:0] multiplexer_1_out;

  Multiplexer #(.width(6), .enable("false")) multiplexer_1 (
    .in0({syscall_in, MemToReg_in, mflo_in, lui_in, jal_in, RegWrite_in}), .in1({6{1'b0}}),
    .out(multiplexer_1_out), .sel(undriven));
  Register #(.width(6)) register_1 (
    .D(multiplexer_1_out), .en(undriven_3),
    .Q({syscall_out, MemToReg_out, mflo_out, lui_out, jal_out, RegWrite_out}), .clk(undriven_2));  // open: clr
endmodule

module jump_test (
);

  wire AluSrcB, BEQ, BNE, CLK, Go, HLEN, J, Jal, jr, LUI, MEM_SIGN_EXT, MemToReg, MemWrite, MFLO, or_1_out,
       pcvalid, RegDst, RegWrite, RST, SHAMT_SRC, SignedExt, syscall, tunnel, \流水线跳转语句分支判断_1_发生跳转 ;
  wire [1:0] B_BRANCH, MODE;
  wire [3:0] AluOp;
  wire [4:0] multiplexer_1_out, multiplexer_2_out, multiplexer_3_out, multiplexer_4_out, multiplexer_5_out,
       multiplexer_8_out;
  wire [5:0] func;
  wire [15:0] \总周期数 , \无条件分支数 , \条件分支成功数 ;
  wire [25:6] Imm26;
  wire [31:0] a0, bit_extender_1_out, bit_extender_2_out, HI, Imm__2, imm_ext, LedData, LO_Out, LO_R,
       multiplexer_7_out, multiplexer_9_out, multiplexer_10_out, multiplexer_11_out, multiplexer_12_out, PC,
       PC_4, PC_out, shifter_1_out, v0, \数据存储器_1_dataout ;
  wire [31:26] IR;

  Button \u_总复位  (.out(RST));
  Button \u_继续运行  (.out(Go));
  Clock clock_1 (.out(CLK));
  Register #(.width(32)) u_PC (.D(PC_out), .en(pcvalid), .Q(PC), .clk(CLK), .clr(RST));
  Hex_Digit_Display hex_digit_display_1 (.value(LedData[31:28]));  // open: dp
  Adder #(.width(32)) adder_1 (.a(PC), .b(32'h4), .out(PC_4));  // open: cin, cout
  Counter #(.width(16), .max('hffff)) counter_1 (
    .count(pcvalid), .Q(\总周期数 ), .clk(CLK), .clr(RST));  // open: load, D, carry
  Hex_Digit_Display hex_digit_display_2 (.value(LedData[27:24]));  // open: dp
  Hex_Digit_Display hex_digit_display_3 (.value(LedData[23:20]));  // open: dp
  Hex_Digit_Display hex_digit_display_4 (.value(LedData[19:16]));  // open: dp
  Hex_Digit_Display hex_digit_display_5 (.value(LedData[15:12]));  // open: dp
  \流水线跳转语句分支判断  \u_流水线跳转语句分支判断_1  (
    .PC(PC), .\_32位指令 ({IR, Imm26, func}), .\跳转信号 ({B_BRANCH, SignedExt, jr, Jal, J, BNE, BEQ}), .rs(a0),
    .rt(v0), .Next_PC(PC_out), .\发生跳转 (\流水线跳转语句分支判断_1_发生跳转 ));
  ROM #(.addrWidth(10), .dataWidth(32)) rom_1 (.addr(PC[11:2]), .data({IR, Imm26, func}));  // open: sel
  Hex_Digit_Display hex_digit_display_6 (.value(LedData[7:4]));  // open: dp
  Hex_Digit_Display hex_digit_display_7 (.value(LedData[11:8]));  // open: dp
  Hex_Digit_Display hex_digit_display_8 (.value(LedData[3:0]));  // open: dp
  Multiplexer #(.width(5), .enable("false")) multiplexer_1 (
    .in0(Imm26[25:21]), .in1(5'b00100), .out(multiplexer_1_out), .sel(syscall));
  Multiplexer #(.width(5), .enable("false")) multiplexer_2 (
    .in0(Imm26[20:16]), .in1(Imm26[15:11]), .out(multiplexer_2_out), .sel(RegDst));
  Multiplexer #(.width(5), .enable("false")) multiplexer_3 (
    .in0(Imm26[20:16]), .in1(5'b00010), .out(multiplexer_3_out), .sel(syscall));
  Multiplexer #(.width(5), .enable("false")) multiplexer_4 (
    .in0(multiplexer_2_out), .in1({5{1'b1}}), .out(multiplexer_4_out), .sel(Jal));
  assign bit_extender_1_out = {{16{1'b0}}, {Imm26[15:6], func}};  // Bit_Extender bit_extender_1
  assign bit_extender_2_out = {{16{Imm26[15]}}, {Imm26[15:6], func}};  // Bit_Extender bit_extender_2
  // Probe on \总周期数 
  // Probe on \无条件分支数 
  // Probe on \条件分支成功数 
  \硬布线控制器  \u_硬布线控制器_1  (
    .Func(func), .OP(IR), .ALU_OP(AluOp), .MemToReg(MemToReg), .MemWrite(MemWrite), .ALU_SRC(AluSrcB),
    .RegWrite(RegWrite), .SysCALL(syscall), .SignedExt(SignedExt), .RegDst(RegDst), .JR(jr), .JMP(J),
    .Beq(BEQ), .JAL(Jal), .Bne(BNE), .SHAMT_SRC(SHAMT_SRC), .LUI(LUI), .HLEN(HLEN), .MFLO(MFLO),
    .MEM_SIGN_EXT(MEM_SIGN_EXT), .B_BRANCH(B_BRANCH), .MODE(MODE));
  or or_1 (or_1_out, B_BRANCH[1], B_BRANCH[0]);
  Multiplexer #(.width(5), .enable("false")) multiplexer_5 (
    .in0(multiplexer_3_out), .in1({5{1'b0}}), .out(multiplexer_5_out), .sel(or_1_out));
  Multiplexer #(.width(32), .enable("false")) multiplexer_6 (
    .in0(bit_extender_1_out), .in1(bit_extender_2_out), .out(imm_ext), .sel(SignedExt));
  Shifter #(.width(32)) shifter_1 (.in(bit_extender_1_out), .\dist (5'b10000), .out(shifter_1_out));
  MIPS_Regifile mips_regifile_1 (
    .Din(multiplexer_12_out), .Clk(CLK), .R1(a0), .R2(v0), .WE(RegWrite), .W_num(multiplexer_4_out),
    .R1_num(multiplexer_1_out), .R2_num(multiplexer_5_out));
  Multiplexer #(.width(32), .enable("false")) multiplexer_7 (
    .in0(v0), .in1(imm_ext), .out(multiplexer_7_out), .sel(AluSrcB));
  Multiplexer #(.width(5), .enable("false")) multiplexer_8 (
    .in0(Imm26[10:6]), .in1(a0[4:0]), .out(multiplexer_8_out), .sel(SHAMT_SRC));
  Shifter #(.width(32)) shifter_2 (.in(imm_ext), .\dist (5'b00010), .out(Imm__2));
  MIPS_ALU mips_alu_1 (
    .X(a0), .Y(multiplexer_7_out), .AluOP(AluOp), .Equal(tunnel), .Result(LO_R), .Result_2(HI),
    .shamt(multiplexer_8_out));
  \数据存储器  \u_数据存储器_1  (
    .\字节地址 (LO_R[11:0]), .Din(v0), .DataOut(\数据存储器_1_dataout ), .CLK(CLK), .WE(MemWrite), .Mode(MODE),
    .clr(RST), .in_3(MEM_SIGN_EXT));
  Multiplexer #(.width(32), .enable("false")) multiplexer_9 (
    .in0(LO_R), .in1(\数据存储器_1_dataout ), .out(multiplexer_9_out), .sel(MemToReg));
  Multiplexer #(.width(32), .enable("false")) multiplexer_10 (
    .in0(multiplexer_9_out), .in1(PC_4), .out(multiplexer_10_out), .sel(Jal));
  Multiplexer #(.width(32), .enable("false")) multiplexer_11 (
    .in0(multiplexer_10_out), .in1(shifter_1_out), .out(multiplexer_11_out), .sel(LUI));
  Multiplexer #(.width(32), .enable("false")) multiplexer_12 (
    .in0(multiplexer_11_out), .in1(LO_Out), .out(multiplexer_12_out), .sel(MFLO));
  Syscall syscall_1 (
    .CLK(CLK), .RST(RST), .syscall(syscall), .go(Go), .a0(a0), .v0(v0), .LedData(LedData), .PcValid(pcvalid));
  Register #(.width(32)) register_1 (.D(LO_R), .en(HLEN), .Q(LO_Out), .clk(CLK), .clr(RST));
  Register #(.width(32)) register_2 (.D(HI), .en(HLEN), .clk(CLK), .clr(RST));  // open: Q
  // AND_Gate and_1 is placed but not wired

  // Other names for the same wires on the sheet: Imm26[5:0] = func; IR[25:0] = {Imm26, func}; rt[4:0] = Imm26[20:16];
  //   OP[5:0] = IR; rs[31:0] = a0

  // Notes on the sheet:
  //   数码管输出应该用寄存器锁存，否则显示数据只能一闪而过
  //   可以通过项目增加Logisim库的方式将前几次实验完成的电路作为子电路引入到本电路中使用
  //   指令存储器
  //   指令字
  //   contents of rom_1 (hex, n*v repeats v):
  //   0 2010ffff 20110000 ae300000 22100001 22310004 ae300000 22100001 22310004 ae300000 22100001 22310004
  //   ae300000 22100001 22310004 ae300000 22100001 22310004 ae300000 22100001 22310004 ae300000 22100001
  //   22310004 ae300000 22100001 22310004 ae300000 22100001 22310004 ae300000 22100001 22310004 ae300000
  //   22100001 22310004 ae300000 22100001 22310004 ae300000 22100001 22310004 ae300000 22100001 22310004
  //   ae300000 22100001 22310004 ae300000 22100001 22310004 22100001 8020 2011003c 8e130000 8e340000
  //   274402a 11000002 ae330000 ae140000 2231fffc 1611fff8 102020 20020022 c 22100004 2011003c 1611fff2
  //   2002000a c
  //   数码管输出
  //   OP
  //   Func
  //   rs
  //   rt
  //   rd
  //   imm
  //   总复位信号应将除ROM以外所有存储组件全部清零
  //   Beq
  //   JMP
  //   JR
  //   Bne
  //   OP
  //   JAL
  //   Func
  //   Syscall
  //   MemToReg
  //   MemWrite
  //   AluOP
  //   AluSrcB
  //   RegWrite
  //   RegDst
endmodule
module \单周期单级中断  (
  input  \同步清零信号 ,
  input  \同步清零信号_2 ,
  output \与中断屏蔽位与 ,
  output \与中断屏蔽位与_2 
);

  wire \_1号中断 , \_1号中断等待指示 , \_2号中断 , \_2号中断等待指示 , \_3号中断 , \_3号中断等待指示 , AluSrcB, and_1_out, and_2_out, BEQ,
       BNE, CLK, clock_2_out, clock_3_out, d_ff_1_q, d_ff_2_q, Go, HLEN, J, Jal, jr, LUI, MEM_SIGN_EXT,
       MemToReg, MemWrite, MFLO, or_1_out, or_2_out, or_3_out, or_4_out, or_5_out, or_6_out, pcvalid, RegDst,
       RegWrite, RST, SHAMT_SRC, SignedExt, syscall, tunnel, \流水线跳转语句分支判断_1_发生跳转 ;
  wire [1:0] B_BRANCH, MODE;
  wire [3:0] AluOp;
  wire [4:0] multiplexer_1_out, multiplexer_2_out, multiplexer_3_out, multiplexer_4_out, multiplexer_5_out,
       multiplexer_8_out;
  wire [5:0] func;
  wire [15:0] \总周期数 , \无条件分支数 , \条件分支成功数 ;
  wire [25:6] Imm26;
  wire [31:0] a0, bit_extender_1_out, bit_extender_2_out, HI, Imm__2, imm_ext, LedData, LO_Out, LO_R,
       multiplexer_7_out, multiplexer_9_out, multiplexer_10_out, multiplexer_11_out, multiplexer_12_out, PC,
       PC_4, PC_out, shifter_1_out, v0, \数据存储器_1_dataout ;
  wire [31:26] IR;

  Button \u_总复位  (.out(RST));
  Button \u_继续运行  (.out(Go));
  Clock clock_1 (.out(CLK));
  Hex_Digit_Display hex_digit_display_1 (.value(LedData[31:28]));  // open: dp
  Button _1 (.out(\_1号中断 ));
  Button _2 (.out(\_2号中断 ));
  Button _3 (.out(\_3号中断 ));
  Counter #(.width(16), .max('hffff)) counter_1 (
    .count(\流水线跳转语句分支判断_1_发生跳转 ), .Q(\条件分支成功数 ), .clk(CLK), .clr(RST));  // open: load, D, carry
  Register #(.width(32)) u_PC (.D(PC_out), .en(pcvalid), .Q(PC), .clk(CLK), .clr(RST));
  Hex_Digit_Display hex_digit_display_2 (.value(LedData[27:24]));  // open: dp
  Hex_Digit_Display hex_digit_display_3 (.value(LedData[23:20]));  // open: dp
  LED _1_2 (.in(\_1号中断等待指示 ));
  LED _2_2 (.in(\_2号中断等待指示 ));
  LED _3_2 (.in(\_3号中断等待指示 ));
  Adder #(.width(32)) adder_1 (.a(PC), .b(32'h4), .out(PC_4));  // open: cin, cout
  Counter #(.width(16), .max('hffff)) counter_2 (
    .count(pcvalid), .Q(\总周期数 ), .clk(CLK), .clr(RST));  // open: load, D, carry
  Hex_Digit_Display hex_digit_display_4 (.value(LedData[19:16]));  // open: dp
  Hex_Digit_Display hex_digit_display_5 (.value(LedData[15:12]));  // open: dp
  Hex_Digit_Display hex_digit_display_6 (.value(LedData[7:4]));  // open: dp
  Hex_Digit_Display hex_digit_display_7 (.value(LedData[11:8]));  // open: dp
  \流水线跳转语句分支判断  \u_流水线跳转语句分支判断_1  (
    .PC(PC), .\_32位指令 ({IR, Imm26, func}), .\跳转信号 ({B_BRANCH, SignedExt, jr, Jal, J, BNE, BEQ}), .rs(a0),
    .rt(v0), .Next_PC(PC_out), .\发生跳转 (\流水线跳转语句分支判断_1_发生跳转 ));
  ROM #(.addrWidth(10), .dataWidth(32)) rom_1 (.addr(PC[11:2]), .data({IR, Imm26, func}));  // open: sel
  Hex_Digit_Display hex_digit_display_8 (.value(LedData[3:0]));  // open: dp
  // Probe on \_1号中断 
  // Probe on \_2号中断 
  // Probe on \_3号中断 
  Multiplexer #(.width(5), .enable("false")) multiplexer_1 (
    .in0(Imm26[25:21]), .in1(5'b00100), .out(multiplexer_1_out), .sel(syscall));
  Multiplexer #(.width(5), .enable("false")) multiplexer_2 (
    .in0(Imm26[20:16]), .in1(Imm26[15:11]), .out(multiplexer_2_out), .sel(RegDst));
  // Probe on \总周期数 
  // Probe on \无条件分支数 
  // Probe on \条件分支成功数 
  or or_1 (or_1_out, B_BRANCH[1], B_BRANCH[0]);
  Multiplexer #(.width(5), .enable("false")) multiplexer_3 (
    .in0(Imm26[20:16]), .in1(5'b00010), .out(multiplexer_3_out), .sel(syscall));
  Multiplexer #(.width(5), .enable("false")) multiplexer_4 (
    .in0(multiplexer_2_out), .in1({5{1'b1}}), .out(multiplexer_4_out), .sel(Jal));
  assign bit_extender_1_out = {{16{1'b0}}, {Imm26[15:6], func}};  // Bit_Extender bit_extender_1
  assign bit_extender_2_out = {{16{Imm26[15]}}, {Imm26[15:6], func}};  // Bit_Extender bit_extender_2
  Multiplexer #(.width(5), .enable("false")) multiplexer_5 (
    .in0(multiplexer_3_out), .in1({5{1'b0}}), .out(multiplexer_5_out), .sel(or_1_out));
  Multiplexer #(.width(32), .enable("false")) multiplexer_6 (
    .in0(bit_extender_1_out), .in1(bit_extender_2_out), .out(imm_ext), .sel(SignedExt));
  Shifter #(.width(32)) shifter_1 (.in(bit_extender_1_out), .\dist (5'b10000), .out(shifter_1_out));
  MIPS_Regifile mips_regifile_1 (
    .Din(multiplexer_12_out), .Clk(CLK), .R1(a0), .R2(v0), .WE(RegWrite), .W_num(multiplexer_4_out),
    .R1_num(multiplexer_1_out), .R2_num(multiplexer_5_out));
  Multiplexer #(.width(32), .enable("false")) multiplexer_7 (
    .in0(v0), .in1(imm_ext), .out(multiplexer_7_out), .sel(AluSrcB));
  Multiplexer #(.width(5), .enable("false")) multiplexer_8 (
    .in0(Imm26[10:6]), .in1(a0[4:0]), .out(multiplexer_8_out), .sel(SHAMT_SRC));
  Shifter #(.width(32)) shifter_2 (.in(imm_ext), .\dist (5'b00010), .out(Imm__2));
  Clock clock_2 (.out(clock_2_out));
  or or_2 (or_2_out, \与中断屏蔽位与 , d_ff_1_q);
  LED \_1号中断等待指示灯  (.in(or_2_out));
  Clock clock_3 (.out(clock_3_out));
  LED \_2号中断等待指示灯  (.in(or_3_out));
  \硬布线控制器  \u_硬布线控制器_1  (
    .Func(func), .OP(IR), .ALU_OP(AluOp), .MemToReg(MemToReg), .MemWrite(MemWrite), .ALU_SRC(AluSrcB),
    .RegWrite(RegWrite), .SysCALL(syscall), .SignedExt(SignedExt), .RegDst(RegDst), .JR(jr), .JMP(J),
    .Beq(BEQ), .JAL(Jal), .Bne(BNE), .SHAMT_SRC(SHAMT_SRC), .LUI(LUI), .HLEN(HLEN), .MFLO(MFLO),
    .MEM_SIGN_EXT(MEM_SIGN_EXT), .B_BRANCH(B_BRANCH), .MODE(MODE));
  MIPS_ALU mips_alu_1 (
    .X(a0), .Y(multiplexer_7_out), .AluOP(AluOp), .Equal(tunnel), .Result(LO_R), .Result_2(HI),
    .shamt(multiplexer_8_out));
  D_Flip_Flop d_ff_1 (.clk(\_1号中断 ), .D(1'b1), .Q(d_ff_1_q), .reset(\与中断屏蔽位与 ));  // open: Qn, preset, en
  D_Flip_Flop d_ff_2 (.clk(\_2号中断 ), .D(1'b1), .Q(d_ff_2_q), .reset(\与中断屏蔽位与_2 ));  // open: Qn, preset, en
  or or_3 (or_3_out, \与中断屏蔽位与_2 , d_ff_2_q);
  or or_4 (or_4_out, J, jr);
  \数据存储器  \u_数据存储器_1  (
    .\字节地址 (LO_R[11:0]), .Din(v0), .DataOut(\数据存储器_1_dataout ), .CLK(CLK), .WE(MemWrite), .Mode(MODE),
    .clr(RST), .in_3(MEM_SIGN_EXT));
  or or_5 (or_5_out, d_ff_1_q, \与中断屏蔽位与 );
  or or_6 (or_6_out, d_ff_2_q, \与中断屏蔽位与_2 );
  Counter #(.width(16), .max('hffff)) counter_3 (
    .count(or_4_out), .Q(\无条件分支数 ), .clk(CLK), .clr(RST));  // open: load, D, carry
  and and_1 (and_1_out, or_5_out, ~\同步清零信号 );  // AND_Gate
  and and_2 (and_2_out, or_6_out, ~\同步清零信号_2 );  // AND_Gate
  Multiplexer #(.width(32), .enable("false")) multiplexer_9 (
    .in0(LO_R), .in1(\数据存储器_1_dataout ), .out(multiplexer_9_out), .sel(MemToReg));
  Multiplexer #(.width(32), .enable("false")) multiplexer_10 (
    .in0(multiplexer_9_out), .in1(PC_4), .out(multiplexer_10_out), .sel(Jal));
  D_Flip_Flop IR1 (.clk(clock_2_out), .D(and_1_out), .Q(\与中断屏蔽位与 ));  // open: Qn, preset, en, reset
  D_Flip_Flop IR1_2 (.clk(clock_3_out), .D(and_2_out), .Q(\与中断屏蔽位与_2 ));  // open: Qn, preset, en, reset
  Multiplexer #(.width(32), .enable("false")) multiplexer_11 (
    .in0(multiplexer_10_out), .in1(shifter_1_out), .out(multiplexer_11_out), .sel(LUI));
  Multiplexer #(.width(32), .enable("false")) multiplexer_12 (
    .in0(multiplexer_11_out), .in1(LO_Out), .out(multiplexer_12_out), .sel(MFLO));
  Syscall syscall_1 (
    .CLK(CLK), .RST(RST), .syscall(syscall), .go(Go), .a0(a0), .v0(v0), .LedData(LedData), .PcValid(pcvalid));
  Register #(.width(32)) register_1 (.D(LO_R), .en(HLEN), .Q(LO_Out), .clk(CLK), .clr(RST));
  Register #(.width(32)) register_2 (.D(HI), .en(HLEN), .clk(CLK), .clr(RST));  // open: Q
  // AND_Gate and_3 is placed but not wired

  // Other names for the same wires on the sheet: Imm26[5:0] = func; IR[25:0] = {Imm26, func}; rt[4:0] = Imm26[20:16];
  //   OP[5:0] = IR; rs[31:0] = a0

  // Notes on the sheet:
  //   数码管输出应该用寄存器锁存，否则显示数据只能一闪而过
  //   可以通过项目增加Logisim库的方式将前几次实验完成的电路作为子电路引入到本电路中使用
  //   中断信号源及指示电路规范（优先级3>2>1>CPU(0）)
  //   指令存储器
  //   指令字
  //   contents of rom_1 (hex, n*v repeats v):
  //   0 2010ffff 20110000 ae300000 22100001 22310004 ae300000 22100001 22310004 ae300000 22100001 22310004
  //   ae300000 22100001 22310004 ae300000 22100001 22310004 ae300000 22100001 22310004 ae300000 22100001
  //   22310004 ae300000 22100001 22310004 ae300000 22100001 22310004 ae300000 22100001 22310004 ae300000
  //   22100001 22310004 ae300000 22100001 22310004 ae300000 22100001 22310004 ae300000 22100001 22310004
  //   ae300000 22100001 22310004 ae300000 22100001 22310004 22100001 8020 2011003c 8e130000 8e340000
  //   274402a 11000002 ae330000 ae140000 2231fffc 1611fff8 102020 20020022 c 22100004 2011003c 1611fff2
  //   2002000a c
  //   数码管输出
  //   OP
  //   Func
  //   rs
  //   rt
  //   rd
  //   imm
  //   总复位信号应将除ROM以外所有存储组件全部清零
  //   JMP
  //   JR
  //   OP
  //   Func
  //   Beq
  //   Bne
  //   MemToReg
  //   MemWrite
  //   AluOP
  //   AluSrcB
  //   RegWrite
  //   JAL
  //   RegDst
  //   Syscall
  //   Reset 
  //   Reset 
endmodule

module CP0 (
);

  Register #(.width(32)) EPC ();  // open: D, en, Q, clk, clr
  Register #(.width(1)) STATUS ();  // open: D, en, Q, clk, clr
  Register #(.width(32)) \u_中断屏蔽字  ();  // open: D, en, Q, clk, clr
endmodule
